// Digital circuit 4bit_counter_sync.dig as structural Verilog
module _4bit_counter_sync (
  input  [3:0] in,
  input  clk,
  input  nclr,
  input  en,
  input  nld,
  input  cin,
  output [3:0] out,
  output ovf
);

  _74163 _74163_1 (
    .pin1(nclr), .pin2(clk), .pin3(in[0]), .pin4(in[1]), .pin5(in[2]), .pin6(in[3]), .pin7(en), .pin8(1'b0),
    .pin9(nld), .pin10(cin), .pin11(out[3]), .pin12(out[2]), .pin13(out[1]), .pin14(out[0]), .pin15(ovf),
    .pin16(1'b1));
endmodule
