// Digital circuit 74138_modified.dig as structural Verilog
// 3-line to 8-line decoder/demultiplexer, inverted out
module _74138_modified (
  input  A,
  input  C,
  input  B,
  input  G,
  input  nGB,
  input  nGA,
  input  VCC,
  input  GND,
  output nY0,
  output nY1,
  output nY2,
  output nY3,
  output nY4,
  output nY5,
  output nY6,
  output nY7
);

  wire demultiplexer_1_out_0, demultiplexer_1_out_1, demultiplexer_1_out_2, demultiplexer_1_out_3,
       demultiplexer_1_out_4, demultiplexer_1_out_5, demultiplexer_1_out_6, demultiplexer_1_out_7,
       nand_1_out, not_1_out;

  PowerSupply powersupply_1 (.VDD(VCC), .GND(GND));
  nand nand_1 (nand_1_out, G, ~nGB, ~nGA);  // NAnd
  not not_1 (not_1_out, nand_1_out);
  Demultiplexer #(.Selector_Bits(3)) demultiplexer_1 (
    .sel({C, B, A}), .in(not_1_out), .out_0(demultiplexer_1_out_0), .out_1(demultiplexer_1_out_1),
    .out_2(demultiplexer_1_out_2), .out_3(demultiplexer_1_out_3), .out_4(demultiplexer_1_out_4),
    .out_5(demultiplexer_1_out_5), .out_6(demultiplexer_1_out_6), .out_7(demultiplexer_1_out_7));
  not not_2 (nY0, demultiplexer_1_out_0);
  not not_3 (nY1, demultiplexer_1_out_1);
  not not_4 (nY2, demultiplexer_1_out_2);
  not not_5 (nY3, demultiplexer_1_out_3);
  not not_6 (nY4, demultiplexer_1_out_4);
  not not_7 (nY5, demultiplexer_1_out_5);
  not not_8 (nY6, demultiplexer_1_out_6);
  not not_9 (nY7, demultiplexer_1_out_7);

  // Notes on the sheet:
  //   A: pin 1
  //   C: pin 3
  //   B: pin 2
  //   G: pin 6
  //   nGB: pin 5
  //   nGA: pin 4
  //   nY0: pin 15
  //   nY1: pin 14
  //   nY2: pin 13
  //   nY3: pin 12
  //   nY4: pin 11
  //   nY5: pin 10
  //   nY6: pin 9
  //   nY7: pin 7
  //   VCC: pin 16, default 1
  //   GND: pin 8
endmodule

/* Test case:
~GA ~GB G A B C ~Y0 ~Y1 ~Y2 ~Y3 ~Y4 ~Y5 ~Y6 ~Y7

 1   X  X X X X  1   1   1   1   1   1   1   1
 X   1  X X X X  1   1   1   1   1   1   1   1
 X   X  0 X X X  1   1   1   1   1   1   1   1

 0   0  1 0 0 0  0   1   1   1   1   1   1   1
 0   0  1 1 0 0  1   0   1   1   1   1   1   1
 0   0  1 0 1 0  1   1   0   1   1   1   1   1
 0   0  1 1 1 0  1   1   1   0   1   1   1   1
 0   0  1 0 0 1  1   1   1   1   0   1   1   1
 0   0  1 1 0 1  1   1   1   1   1   0   1   1
 0   0  1 0 1 1  1   1   1   1   1   1   0   1
 0   0  1 1 1 1  1   1   1   1   1   1   1   0
*/
