// Digital circuit 8bit_comparator.dig as structural Verilog
module _8bit_comparator (
  input  [7:0] a,
  input  [7:0] b,
  output gt,
  output eq,
  output lt
);

  wire _7485_1_pin5, _7485_1_pin6, _7485_1_pin7;

  _7485 _7485_1 (
    .pin1(b[3]), .pin2(1'b1), .pin3(1'b1), .pin4(1'b1), .pin5(_7485_1_pin5), .pin6(_7485_1_pin6),
    .pin7(_7485_1_pin7), .pin8(1'b0), .pin9(b[0]), .pin10(a[0]), .pin11(b[1]), .pin12(a[1]), .pin13(a[2]),
    .pin14(b[2]), .pin15(a[3]), .pin16(1'b1));
  _7485 _7485_2 (
    .pin1(b[7]), .pin2(_7485_1_pin7), .pin3(_7485_1_pin6), .pin4(_7485_1_pin5), .pin5(gt), .pin6(eq),
    .pin7(lt), .pin8(1'b0), .pin9(b[4]), .pin10(a[4]), .pin11(b[5]), .pin12(a[5]), .pin13(a[6]),
    .pin14(b[6]), .pin15(a[7]), .pin16(1'b1));
endmodule
