// Digital circuit 8bit_counter.dig as structural Verilog
module _8bit_counter (
  input  [7:0] in,
  input  en,
  input  nld,
  input  clk,
  output [7:0] out,
  output ovf
);

  wire _74163_1_pin15;

  _74163 _74163_1 (
    .pin1(1'b1), .pin2(clk), .pin3(in[0]), .pin4(in[1]), .pin5(in[2]), .pin6(in[3]), .pin7(en), .pin8(1'b0),
    .pin9(nld), .pin10(1'b1), .pin11(out[3]), .pin12(out[2]), .pin13(out[1]), .pin14(out[0]),
    .pin15(_74163_1_pin15), .pin16(1'b1));
  _74163 _74163_2 (
    .pin1(1'b1), .pin2(clk), .pin3(in[4]), .pin4(in[5]), .pin5(in[6]), .pin6(in[7]), .pin7(en), .pin8(1'b0),
    .pin9(nld), .pin10(_74163_1_pin15), .pin11(out[7]), .pin12(out[6]), .pin13(out[5]), .pin14(out[4]),
    .pin15(ovf), .pin16(1'b1));

  // Notes on the sheet:
  //   clk: Hz: 100
endmodule
