// Digital circuit 8bit_nand.dig as structural Verilog
module _8bit_nand (
  input  [7:0] D,
  output Q
);

  _7430 _7430_1 (
    .pin1(D[0]), .pin2(D[1]), .pin3(D[2]), .pin4(D[3]), .pin5(D[4]), .pin6(D[5]), .pin7(1'b0), .pin8(Q),
    .pin11(D[6]), .pin12(D[7]), .pin14(1'b1));  // open: pin9, pin10, pin13
endmodule
