// Digital circuit dual_JK.dig as structural Verilog
module dual_JK (
  input  J_0,
  input  K_0,
  input  J_1,
  input  K_1,
  input  nclr0,
  input  nclr1,
  input  clk,
  output nQ_0,
  output Q_0,
  output Q_1,
  output nQ_1
);

  wire _74107_1_pin9;

  _74107 _74107_1 (
    .pin1(J_0), .pin2(nQ_0), .pin3(Q_0), .pin4(K_0), .pin5(Q_1), .pin6(nQ_1), .pin7(1'b0), .pin8(J_1),
    .pin9(_74107_1_pin9), .pin10(nclr1), .pin11(K_1), .pin12(_74107_1_pin9), .pin13(nclr0), .pin14(1'b1));
  not not_1 (_74107_1_pin9, clk);
endmodule
