// Digital circuit gpu.dig as structural Verilog
module gpu (
  input  clk,
  input  [15:0] in_3,
  output [15:0] out_1,
  output [7:0] out_4,
  output [15:0] out_5
);

  wire _8bit_comparator_1_eq, _8bit_counter_1_ovf, _8bit_counter_2_ovf, _8bit_nand_1_q, _74138_1_pin7,
       _74138_1_pin13, _74138_1_pin14, and_1_out, and_2_out, and_3_out, and_4_out, and_5_out, and_6_out,
       button_1_out, jk_ff_2_nq, load_3, load_4, load_5, nor_1_out, nor_2_out, not_1_out, not_2_out,
       not_3_out, not_4_out, not_5_out, or_1_out, or_2_out, or_3_out, state_char_1_done;
  wire [1:0] jk_ff_1_q;
  wire [7:0] _8bit_register_1_q, _8bit_register_2_q;
  wire [15:0] memory_ptr_1_out, sprite_ptr_1_out;

  Button button_1 (.out(button_1_out));
  or or_1 (or_1_out, jk_ff_1_q[1], jk_ff_2_nq);
  not not_1 (not_1_out, or_1_out);
  not not_2 (not_2_out, jk_ff_1_q[1]);
  and and_1 (and_1_out, _8bit_nand_1_q, jk_ff_2_nq);
  JK_FF jk_ff_1 (.J(and_2_out), .C(clk), .K(button_1_out), .Q(jk_ff_1_q[1]));  // open: nQ
  sprite_ptr sprite_ptr_1 (
    .en0(jk_ff_1_q[0]), .clk(clk), .nclr0(not_1_out), .nclr1(not_2_out), .en1(1'b1), .out(sprite_ptr_1_out));
  nor nor_1 (nor_1_out, or_2_out, _74138_1_pin7);
  memory_ptr memory_ptr_1 (
    .in0(out_4), .en(and_1_out), .nld0(load_5), .in1(out_4), .clk(clk), .nld1(load_4), .out(memory_ptr_1_out));
  Multiplexer #(.Selector_Bits(2), .Bits(16)) multiplexer_1 (
    .sel(jk_ff_1_q), .in_0(memory_ptr_1_out), .in_1(sprite_ptr_1_out), .in_2(in_3), .in_3(in_3), .out(out_5));
  JK_FF jk_ff_2 (.J(or_2_out), .C(clk), .K(nor_1_out), .Q(jk_ff_1_q[0]), .nQ(jk_ff_2_nq));
  ROM #(.AddrBits(16), .Bits(8)) rom_1 (.A(out_5), .sel(1'b1), .D(out_4));
  _74138 _74138_1 (
    .pin1(sprite_ptr_1_out[0]), .pin2(sprite_ptr_1_out[1]), .pin3(sprite_ptr_1_out[2]), .pin4(1'b0),
    .pin5(1'b0), .pin6(jk_ff_1_q[0]), .pin7(_74138_1_pin7), .pin8(1'b0), .pin10(load_5), .pin11(load_4),
    .pin12(load_3), .pin13(_74138_1_pin13), .pin14(_74138_1_pin14), .pin16(1'b1));  // open: pin9, pin15
  not not_3 (not_3_out, _74138_1_pin14);
  not not_4 (not_4_out, _74138_1_pin13);
  _8bit_register _8bit_register_1 (.clk(clk), .D(out_4), .en(not_3_out), .Q(_8bit_register_1_q));
  _8bit_register _8bit_register_2 (.clk(clk), .D(out_4), .en(not_4_out), .Q(_8bit_register_2_q));
  nor nor_2 (nor_2_out, not_4_out, _8bit_comparator_1_eq);
  _8bit_counter _8bit_counter_1 (
    .in(_8bit_register_1_q), .en(jk_ff_2_nq), .nld(nor_2_out), .clk(clk), .out(out_1[7:0]),
    .ovf(_8bit_counter_1_ovf));
  and and_2 (and_2_out, _8bit_counter_2_ovf, and_3_out);
  _8bit_nand _8bit_nand_1 (.D(_8bit_register_1_q), .Q(_8bit_nand_1_q));
  state_char state_char_1 (.D(out_4), .done(state_char_1_done));  // open: next
  or or_2 (or_2_out, _8bit_counter_2_ovf, and_4_out);
  _8bit_comparator _8bit_comparator_1 (
    .a(_8bit_register_2_q), .b(out_1[7:0]), .eq(_8bit_comparator_1_eq));  // open: gt, lt
  and and_3 (and_3_out, state_char_1_done, jk_ff_2_nq);
  and and_4 (and_4_out, _8bit_nand_1_q, and_3_out);
  _8bit_counter _8bit_counter_2 (
    .in(out_4), .en(_8bit_comparator_1_eq), .nld(load_3), .clk(clk), .out(out_1[15:8]),
    .ovf(_8bit_counter_2_ovf));
  and and_5 (and_5_out, jk_ff_2_nq, or_3_out);
  not not_5 (not_5_out, _8bit_nand_1_q);
  or or_3 (or_3_out, 1'b0, out_4[0]);
  and and_6 (and_6_out, not_5_out, and_3_out);
  RAMSinglePort #(.AddrBits(16), .Bits(8)) ramsingleport_1 (.A(out_1), .str(and_5_out), .C(clk), .ld(1'b0), .D(out_4));

  // Other names for the same wires on the sheet: data[7:0] = out_4

  // Notes on the sheet:
  //   clk: Hz: 30000
  //   contents of rom_1 (hex, n*v repeats v):
  //   c,ff,fe,0,0,40,0,0,0,1e,3c,30,0,50,0,0,0,50,8b,2d,6,60,0,0,0,32
  //   ,50,14,0,50,0,0,0,ff,fe,0,0,41,26*0,27,c,24*0,4*49,16*0,2,6*0
  //   ,4*49,e1,f5,f5,e1,49,15*0,2,7*0,49,e1,9b,9b,e1,e1,9b,9b,49,49
  //   ,13*0,2,6*0,49,e1,e1,e1,4*9b,e1,9b,9b,49,12*0,2,5*0,49,f5,e1,e1
  //   ,4*9b,e1,e1,f5,9b,9b,49,11*0,2,4*0,49,9b,f5,f5,9b,f5,e1,f5,e1,e1
  //   ,f5,f5,f5,9b,49,11*0,2,4*0,49,e1,e1,e1,7*f5,e1,e1,9b,49,11*0,2
  //   ,5*0,49,9b,4*e1,49,e1,49,9b,9b,e1,9b,9b,49,10*0,2,4*0,9b,49,9b
  //   ,e1,e1,49,49,eb,49,eb,49,49,9b,e1,9b,49,10*0,2,4*0,49,0,49,1,49
  //   ,db,db,db,49,db,db,db,1,9b,9b,49,10*0,2,4*0,49,0,0,1,db,ff,1,eb
  //   ,db,1,ff,db,1,9b,49,11*0,2,7*0,1,db,ff,1,eb,eb,1,ff,db,1,9b,49
  //   ,11*0,2,7*0,1,db,6*eb,db,1,49,12*0,2,6*0,45,45,1,db,4*eb,db,1
  //   ,45,45,12*0,2,5*0,45,ff,ef,1,1,db,eb,eb,db,1,1,ff,ef,45,11*0,2
  //   ,5*0,45,ef,ef,9f,9f,4*1,9f,45,ef,ef,45,11*0,2,4*0,5*45,6*ef,9f
  //   ,4*45,10*0,2,4*0,45,db,db,45,9f,9f,ef,ff,ff,ff,ef,9f,45,81,db
  //   ,45,10*0,2,4*0,45,45,81,1,45,9f,9f,ef,ef,ef,9f,45,1,81,45,45,10*0
  //   ,2,4*0,45,9f,45,0,1,45,4*9f,45,1,0,45,9f,45,10*0,2,4*0,45,45,45
  //   ,1,1,9f,4*45,9f,1,1,45,45,45,10*0,2,4*0,1,eb,eb,1,45,45,9f,ff
  //   ,ef,9f,45,45,1,eb,eb,1,10*0,2,4*0,1,db,db,1,81,81,4*45,81,81,1
  //   ,db,db,1,10*0,2,5*0,1,1,1,4*81,1,81,81,81,1,1,1,11*0,2,7*0,1,81
  //   ,db,81,81,1,81,81,81,1,13*0,2,7*0,1,4*81,1,81,81,81,1,13*0,2,8*0
  //   ,1,81,81,81,1,81,81,1,14*0,2,8*0,1,81,81,81,1,81,81,1,14*0,2,8*0
  //   ,1,9f,81,81,1,81,81,1,14*0,2,8*0,1,ef,ef,9f,1,9f,9f,1,14*0,2,9*0
  //   ,7*1,14*0,2,30*0,2,30*0,2,30*0,2,30*0,2,30*0,2,30*0,2,30*0,2,30*0
  //   ,2,30*0,2,30*0,2,30*0,2,30*0,2,30*0,2,30*0,2,30*0,2,30*0,2,30*0
  //   ,2,30*0,2,30*0,2,c,31*0,f5,f5,4*a5,ad,ad,a5,ad,ad,18*0,2,22*0
  //   ,f5,ad,ad,ed,ed,ad,5*a5,9d,9b,7*a5,5b,53,15*0,2,18*0,ad,ad,f5,f5
  //   ,ed,4*a5,9d,9b,5b,9b,5b,5b,5b,9b,9d,9d,5*a5,5b,53,15*0,2,15*0
  //   ,a3,a5,a5,a5,ad,4*a5,9d,a5,9d,6*5b,5*53,5b,9d,a5,a5,5b,5b,53,14*0
  //   ,2,14*0,a3,a5,a3,4*9b,a5,a5,9d,9b,9d,4*5b,5*53,4b,4b,4*53,5b,9b
  //   ,5b,5b,14*0,2,13*0,a3,a3,9b,9b,5b,5b,9b,9b,a3,5*9b,5b,5b,53,53
  //   ,b,b,b,8*53,5b,5b,53,53,53,12*0,2,12*0,9b,9b,9b,5b,5b,53,5b,6*9b
  //   ,5b,53,5b,5b,15*53,4*5b,11*0,2,11*0,a3,a3,9b,5b,4*53,9b,4*53,5b
  //   ,9b,9b,18*53,4*5b,10*0,2,10*0,a5,a3,5b,5b,7*53,49,4b,13*53,4b
  //   ,4*b,4b,4b,4*53,5b,5b,10*0,2,10*0,a5,9b,6*53,49,5*9,49,49,49,8*53
  //   ,4b,53,7*b,4b,53,53,53,5b,5b,9*0,2,8*0,a5,a5,9b,5*53,49,49,9,1,1,1
  //   ,9,1,1,9,8*53,4b,4b,10*b,53,5b,5b,53,53,8*0,2,8*0,ad,9b,5b,4*53
  //   ,49,9,49,9,9,1,1,9,1,1,9,49,6*53,4b,5*9,6*b,53,4b,53,5b,5b,5b
  //   ,8*0,2,7*0,ad,a5,7*53,49,49,49,9,9,9,49,9,9,9,1,49,5b,9d,5b,53,53
  //   ,4b,4b,b,b,4*9,5*b,53,53,53,5b,5b,8*0,2,7*0,a5,17*53,4*49,53,53,53
  //   ,4b,4b,10*9,b,b,b,4b,53,53,5b,53,7*0,2,6*0,a5,5b,53,53,53,5b,5b
  //   ,8*53,5*5b,7*53,4b,49,10*9,b,b,4b,4b,53,53,53,7*0,2,5*0,ed,a5
  //   ,4*9b,5b,9*9b,6*a5,9b,9b,5b,5b,53,53,53,4b,49,49,8*9,4b,4b,49,49
  //   ,53,53,5b,53,6*0,2,4*0,f7,ad,4*9b,5b,9b,9b,9b,5b,9b,a3,a5,a5,ad
  //   ,4*ed,f7,f7,ed,ed,ad,a5,a3,9b,53,51,51,4b,49,49,49,4*9,4*49,9,9
  //   ,49,49,53,5b,6*0,2,4*0,f7,a5,9b,5b,9b,9b,9b,5b,5b,53,5b,a5,ad
  //   ,ed,13*f7,ed,a5,a3,5b,53,15*49,53,5b,5b,5*0,2,4*0,a5,9b,5b,9b,9b,9b
  //   ,53,5b,9b,53,a3,ed,17*f7,ed,ed,a5,9b,9b,6*53,51,5*49,51,53,5b,5b
  //   ,5*0,2,4*0,a5,5b,9b,9b,5b,53,53,9b,53,5b,ad,20*f7,ef,ed,ad,4*a5
  //   ,9d,9b,9b,53,49,49,49,9,53,53,53,a3,a3,4*0,2,0,0,0,f7,a5,53,9b,9b
  //   ,53,53,53,9b,53,9b,ed,22*f7,ef,ef,af,5*ad,a5,9b,49,9,9,9,53,53
  //   ,9b,a3,4*0,2,0,0,0,f7,9b,53,9b,9b,53,53,5b,5b,5b,ad,6*f7,ff,ff,ff
  //   ,18*f7,5*af,ad,a5,49,49,49,4b,53,5b,a3,4*0,2,0,0,0,ad,5b,5b,a3
  //   ,9b,53,9b,9b,5b,a5,ed,5*f7,5*ff,17*f7,ef,ef,5*af,9d,53,49,4b,53,53
  //   ,a3,a3,0,0,0,2,0,0,0,a5,53,5b,9b,9b,5b,9b,5b,5b,a5,ed,4*f7,5*ff
  //   ,17*f7,4*ef,af,ef,af,af,a5,5b,4*53,a3,a3,0,0,0,2,0,0,f7,9b,53
  //   ,5b,9b,5b,9b,a3,53,5b,a5,ed,f7,f7,f7,ff,ff,f7,ff,ff,17*f7,6*ef
  //   ,af,af,af,ad,5d,4*53,5b,ad,0,0,0,2,0,0,f7,5b,53,9b,9b,5b,9b,5b
  //   ,53,5b,ad,ed,23*f7,6*ef,af,af,af,ef,ef,ad,a5,53,4b,53,53,53,ad
  //   ,0,0,0,2,0,0,ed,5b,5b,9b,9b,4*53,9b,ad,ed,22*f7,6*ef,5*af,ef,ad
  //   ,a5,53,4b,53,53,53,ad,0,0,0,2,0,0,ad,5b,5b,9b,5*53,a5,ad,ed,22*f7
  //   ,6*ef,5*af,ef,ad,a5,5b,53,49,51,53,ad,ed,0,0,2,0,0,a5,53,53,5b
  //   ,53,53,53,4b,5b,a5,ad,ed,26*f7,ef,ef,af,ad,ad,ad,af,ef,ed,a5,5b
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endmodule
