// Digital circuit gpu_nomem.dig as structural Verilog
module gpu_nomem (
  input  clk,
  input  [15:0] addrin,
  input  draw,
  input  [7:0] din,
  output [15:0] ramaddr,
  output [15:0] addrout,
  output store
);

  wire _8bit_counter_1_ovf, _8bit_counter_2_ovf, _74138_modified_1_ny1, _74138_modified_1_ny2,
       _74138_modified_1_ny7, and_1_out, and_2_out, and_3_out, and_4_out, jk_ff_1_nq, jk_ff_2_nq, load_3,
       load_4, load_5, nor_1_out, nor_2_out, not_1_out, not_2_out, not_3_out, or_1_out, or_2_out, or_3_out,
       state_char_1_done, state_char_1_fill, state_char_1_next, state_char_1_send;
  wire [1:0] jk_ff_2_q;
  wire [7:0] _8bit_register_1_q;
  wire [15:0] memory_ptr_1_out, sprite_ptr_1_out;

  and and_1 (and_1_out, nor_2_out, jk_ff_2_nq);
  JK_FF jk_ff_1 (.J(and_2_out), .C(clk), .K(draw), .Q(jk_ff_2_q[1]), .nQ(jk_ff_1_nq));
  sprite_ptr sprite_ptr_1 (
    .en0(jk_ff_2_q[0]), .clk(clk), .nclr0(jk_ff_1_nq), .nclr1(jk_ff_1_nq), .en1(jk_ff_2_q[0]),
    .out(sprite_ptr_1_out));
  nor nor_1 (nor_1_out, or_2_out, _74138_modified_1_ny7);
  memory_ptr memory_ptr_1 (
    .in0(din), .en(and_1_out), .nld0(load_5), .in1(din), .clk(clk), .nld1(load_4), .out(memory_ptr_1_out));
  Multiplexer #(.Selector_Bits(2), .Bits(16)) multiplexer_1 (
    .sel(jk_ff_2_q), .in_0(memory_ptr_1_out), .in_1(sprite_ptr_1_out), .in_2(addrin), .in_3(addrin),
    .out(addrout));
  JK_FF jk_ff_2 (.J(or_2_out), .C(clk), .K(nor_1_out), .Q(jk_ff_2_q[0]), .nQ(jk_ff_2_nq));
  _74138_modified _74138_modified_1 (
    .A(sprite_ptr_1_out[0]), .C(sprite_ptr_1_out[2]), .B(sprite_ptr_1_out[1]), .G(jk_ff_2_q[0]), .nGB(1'b0),
    .nGA(1'b0), .nY1(_74138_modified_1_ny1), .nY2(_74138_modified_1_ny2), .nY3(load_3), .nY4(load_4),
    .nY5(load_5), .nY7(_74138_modified_1_ny7), .VCC(1'b1), .GND(1'b0));  // open: nY0, nY6
  not not_1 (not_1_out, _74138_modified_1_ny1);
  not not_2 (not_2_out, _74138_modified_1_ny2);
  _8bit_register _8bit_register_1 (.clk(clk), .D(din), .en(not_1_out), .Q(_8bit_register_1_q));
  not not_3 (not_3_out, or_1_out);
  _8bit_counter _8bit_counter_1 (
    .in(_8bit_register_1_q), .en(jk_ff_2_nq), .nld(not_3_out), .clk(clk), .out(ramaddr[7:0]),
    .ovf(_8bit_counter_1_ovf));
  and and_2 (and_2_out, _8bit_counter_2_ovf, and_3_out);
  nor nor_2 (nor_2_out, state_char_1_send, state_char_1_fill);
  state_char state_char_1 (
    .D(din), .next(state_char_1_next), .done(state_char_1_done), .send(state_char_1_send),
    .fill(state_char_1_fill));
  and and_3 (and_3_out, state_char_1_send, jk_ff_2_nq);
  or or_1 (or_1_out, state_char_1_next, not_2_out, _8bit_counter_1_ovf);
  and and_4 (and_4_out, state_char_1_done, jk_ff_2_nq);
  or or_2 (or_2_out, _8bit_counter_2_ovf, and_4_out);
  _8bit_counter _8bit_counter_2 (
    .in(din), .en(or_1_out), .nld(load_3), .clk(clk), .out(ramaddr[15:8]), .ovf(_8bit_counter_2_ovf));
  and and_5 (store, jk_ff_2_nq, or_3_out);
  or or_3 (or_3_out, state_char_1_fill, din[0]);

  // Other names for the same wires on the sheet: data[7:0] = din

  // Notes on the sheet:
  //   clk: Hz: 30000
endmodule
