// Digital circuit gpu_vga.dig as structural Verilog
module gpu_vga (
  input  [15:0] addr_in,
  input  start,
  input  clk,
  input  reset,
  output [15:0] addr_ram,
  output [7:0] data,
  output [15:0] addr_rom,
  output store_ram,
  output [7:0] data_ram,
  output load_rom,
  output [11:0] pixel,
  output [11:0] line,
  output hsync,
  output vsync,
  output [7:0] video
);

  wire _4bit_counter_1_ovf, _4bit_counter_2_ovf, _4bit_counter_4_ovf, _4bit_counter_5_ovf,
       _8bit_counter_1_ovf, _8bit_counter_2_ovf, _74138_modified_1_ny0, _74138_modified_1_ny1,
       _74138_modified_1_ny2, and_1_out, and_5_out, and_6_out, and_7_out, data_0, done, drawing, load_3,
       load_4, load_5, nidling, nor_1_out, not_1_out, not_3_out, not_4_out, not_5_out, not_6_out, not_7_out,
       or_1_out, or_2_out, or_4_out, reset_t, state_char_1_next, u_hsync_blank, u_hsync_pad, u_hsync_reset,
       u_vsync_blank, u_vsync_reset;
  wire [1:0] jk_ff_1_q;
  wire [7:0] _8bit_register_1_q, buffer_d;
  wire [15:0] memory_ptr_1_out, sprite_ptr_1_out;

  sprite_ptr sprite_ptr_1 (
    .en0(or_1_out), .clk(clk), .nclr0(nidling), .nclr1(nidling), .en1(or_1_out), .out(sprite_ptr_1_out));
  memory_ptr memory_ptr_1 (
    .in0(data), .en(not_1_out), .nld0(load_5), .in1(data), .clk(clk), .nld1(load_4), .out(memory_ptr_1_out));
  not not_1 (not_1_out, 1'b0);
  Multiplexer #(.Selector_Bits(2), .Bits(16)) multiplexer_1 (
    .sel(jk_ff_1_q), .in_0(memory_ptr_1_out), .in_1(sprite_ptr_1_out), .in_2(addr_in), .in_3(addr_in),
    .out(addr_rom));
  not not_2 (drawing, jk_ff_1_q[0]);
  JK_FF jk_ff_1 (.J(and_1_out), .C(clk), .K(start), .Q(jk_ff_1_q[1]), .nQ(nidling));
  or or_1 (or_1_out, reset_t, jk_ff_1_q[0]);
  ROM #(.AddrBits(16), .Bits(8)) sprite_memory (.A(addr_rom), .sel(load_rom), .D(data));
  _74138_modified _74138_modified_1 (
    .A(sprite_ptr_1_out[0]), .C(sprite_ptr_1_out[2]), .B(sprite_ptr_1_out[1]), .G(1'b1), .nGB(1'b0),
    .nGA(1'b0), .nY0(_74138_modified_1_ny0), .nY1(_74138_modified_1_ny1), .nY2(_74138_modified_1_ny2),
    .nY3(load_3), .nY4(load_4), .nY5(load_5), .nY7(jk_ff_1_q[0]), .VCC(1'b1), .GND(1'b0));  // open: nY6
  not not_3 (not_3_out, _74138_modified_1_ny1);
  not not_4 (not_4_out, _74138_modified_1_ny0);
  not not_5 (not_5_out, _74138_modified_1_ny2);
  _8bit_register _8bit_register_1 (.clk(clk), .D(data), .en(not_3_out), .Q(_8bit_register_1_q));
  and and_1 (and_1_out, data_0, not_4_out);
  and and_2 (data_0, data[0], load_rom);
  and and_3 (load_rom, not_7_out, nidling);
  _8bit_counter _8bit_counter_1 (
    .in(_8bit_register_1_q), .en(drawing), .nld(not_6_out), .clk(clk), .out(addr_ram[7:0]),
    .ovf(_8bit_counter_1_ovf));
  not not_6 (not_6_out, or_2_out);
  not not_7 (not_7_out, 1'b0);
  state_char state_char_1 (.D(data), .en(drawing), .next(state_char_1_next), .done(done));
  or or_2 (or_2_out, state_char_1_next, _8bit_counter_1_ovf, not_5_out);
  _8bit_counter _8bit_counter_2 (
    .in(data), .en(or_2_out), .nld(load_3), .clk(clk), .out(addr_ram[15:8]), .ovf(_8bit_counter_2_ovf));
  or or_3 (reset_t, and_5_out, done);
  and and_4 (store_ram, drawing, or_4_out);
  and and_5 (and_5_out, _8bit_counter_2_ovf, _8bit_counter_1_ovf);
  or or_4 (or_4_out, 1'b0, data_0);
  RAMDualPort #(.AddrBits(16), .Bits(8)) ramdualport_1 (
    .A(addr_ram), .Din(data), .str(store_ram), .C(clk), .ld(1'b1), .D(data_ram));
  _4bit_counter _4bit_counter_1 (
    .in(4'b0000), .clk(clk), .nclr(u_hsync_reset), .en(1'b1), .nld(1'b1), .cin(1'b1), .out(pixel[3:0]),
    .ovf(_4bit_counter_1_ovf));
  _4bit_counter _4bit_counter_2 (
    .in(4'b0000), .clk(clk), .nclr(u_hsync_reset), .en(1'b1), .nld(1'b1), .cin(_4bit_counter_1_ovf),
    .out(pixel[7:4]), .ovf(_4bit_counter_2_ovf));
  _4bit_counter _4bit_counter_3 (
    .in(4'b0000), .clk(clk), .nclr(u_hsync_reset), .en(1'b1), .nld(1'b1), .cin(_4bit_counter_2_ovf),
    .out(pixel[11:8]));  // open: ovf
  _4bit_counter _4bit_counter_4 (
    .in(4'b0000), .clk(u_hsync_reset), .nclr(and_6_out), .en(1'b1), .nld(1'b1), .cin(1'b1), .out(line[3:0]),
    .ovf(_4bit_counter_4_ovf));
  _4bit_counter _4bit_counter_5 (
    .in(4'b0000), .clk(u_hsync_reset), .nclr(and_6_out), .en(1'b1), .nld(1'b1), .cin(_4bit_counter_4_ovf),
    .out(line[7:4]), .ovf(_4bit_counter_5_ovf));
  _4bit_counter _4bit_counter_6 (
    .in(4'b0000), .clk(u_hsync_reset), .nclr(and_6_out), .en(1'b1), .nld(1'b1), .cin(_4bit_counter_5_ovf),
    .out(line[11:8]));  // open: ovf
  hsync #(.applicationType("IVERILOG")) u_hsync (
    .pos(pixel), .sync(hsync), .blank(u_hsync_blank), .pad(u_hsync_pad), .reset(u_hsync_reset));
  vsync #(.applicationType("IVERILOG")) u_vsync (
    .pos(line), .sync(vsync), .blank(u_vsync_blank), .reset(u_vsync_reset));
  and and_6 (and_6_out, u_vsync_reset, reset);
  nor nor_1 (nor_1_out, u_hsync_blank, u_vsync_blank);
  ROM #(.AddrBits(16), .Bits(8)) buffer (.A({line[8:1], pixel[8:1]}), .sel(nor_1_out), .D(buffer_d));
  and and_7 (and_7_out, u_hsync_pad, ~u_vsync_blank);  // And
  Multiplexer #(.Bits(8)) multiplexer_2 (.sel(and_7_out), .in_0(buffer_d), .in_1({8{1'b1}}), .out(video));

  // Notes on the sheet:
  //   clk: Hz: 100
  //   contents of sprite_memory (hex, n*v repeats v):
  //   0,50,8b,2d,6,4160,0,0,0,32,50,14,0,50,0,0,0,50,8b,2d,6,60,0,0,0
  //   ,32,50,14,0,50,0,0,0,1e,3c,30,0,50,0,0,1,23*0,74,18,14*0,10*8
  //   ,4*49,16*8,a,6*8,4*49,e1,f5,f5,e1,49,15*8,a,7*8,49,e1,9b,9b,e1,e1
  //   ,9b,9b,49,49,13*8,a,6*8,49,e1,e1,e1,4*9b,e1,9b,9b,49,12*8,a,5*8
  //   ,49,f5,e1,e1,4*9b,e1,e1,f5,9b,9b,49,11*8,a,4*8,49,9b,f5,f5,9b
  //   ,f5,e1,f5,e1,e1,f5,f5,f5,9b,49,11*8,a,4*8,49,e1,e1,e1,7*f5,e1,e1
  //   ,9b,49,11*8,a,5*8,49,9b,4*e1,49,e1,49,9b,9b,e1,9b,9b,49,10*8,a
  //   ,4*8,9b,49,9b,e1,e1,49,49,eb,49,eb,49,49,9b,e1,9b,49,10*8,a,4*8
  //   ,49,8,49,1,49,db,db,db,49,db,db,db,1,9b,9b,49,10*8,a,4*8,49,8,8
  //   ,1,db,ff,1,eb,db,1,ff,db,1,9b,49,11*8,a,7*8,1,db,ff,1,eb,eb,1
  //   ,ff,db,1,9b,49,11*8,a,7*8,1,db,6*eb,db,1,49,12*8,a,6*8,45,45,1
  //   ,db,4*eb,db,1,45,45,12*8,a,5*8,45,ff,ef,1,1,db,eb,eb,db,1,1,ff
  //   ,ef,45,11*8,a,5*8,45,ef,ef,9f,9f,4*1,9f,45,ef,ef,45,11*8,a,4*8
  //   ,5*45,6*ef,9f,4*45,10*8,a,4*8,45,db,db,45,9f,9f,ef,ff,ff,ff,ef
  //   ,9f,45,81,db,45,10*8,a,4*8,45,45,81,1,45,9f,9f,ef,ef,ef,9f,45
  //   ,1,81,45,45,10*8,a,4*8,45,9f,45,8,1,45,4*9f,45,1,8,45,9f,45,10*8
  //   ,a,4*8,45,45,45,1,1,9f,4*45,9f,1,1,45,45,45,10*8,a,4*8,1,eb,eb
  //   ,1,45,45,9f,ff,ef,9f,45,45,1,eb,eb,1,10*8,a,4*8,1,db,db,1,81,81
  //   ,4*45,81,81,1,db,db,1,10*8,a,5*8,1,1,1,4*81,1,81,81,81,1,1,1,11*8
  //   ,a,7*8,1,81,db,81,81,1,81,81,81,1,13*8,a,7*8,1,4*81,1,81,81,81
  //   ,1,13*8,a,8*8,1,81,81,81,1,81,81,1,14*8,a,8*8,1,81,81,81,1,81,81
  //   ,1,14*8,a,8*8,1,9f,81,81,1,81,81,1,14*8,a,8*8,1,ef,ef,9f,1,9f,9f
  //   ,1,14*8,a,9*8,7*1,14*8,a,30*8,a,30*8,a,30*8,a,30*8,a,30*8,a,30*8
  //   ,a,30*8,a,30*8,a,30*8,a,30*8,a,30*8,a,30*8,a,30*8,a,30*8,a,30*8
  //   ,a,30*8,a,30*8,a,30*8,a,30*8,a,c,0,30*8,f5,f5,4*a5,ad,ad,a5,ad,ad
  //   ,18*8,a,22*8,f5,ad,ad,ed,ed,ad,5*a5,9d,9b,7*a5,5b,53,15*8,a,18*8
  //   ,ad,ad,f5,f5,ed,4*a5,9d,9b,5b,9b,5b,5b,5b,9b,9d,9d,5*a5,5b,53
  //   ,15*8,a,15*8,a3,a5,a5,a5,ad,4*a5,9d,a5,9d,6*5b,5*53,5b,9d,a5,a5
  //   ,5b,5b,53,14*8,a,14*8,a3,a5,a3,4*9b,a5,a5,9d,9b,9d,4*5b,5*53,4b,4b
  //   ,4*53,5b,9b,5b,5b,14*8,a,13*8,a3,a3,9b,9b,5b,5b,9b,9b,a3,5*9b
  //   ,5b,5b,53,53,b,b,b,8*53,5b,5b,53,53,53,12*8,a,12*8,9b,9b,9b,5b,5b
  //   ,53,5b,6*9b,5b,53,5b,5b,15*53,4*5b,11*8,a,11*8,a3,a3,9b,5b,4*53
  //   ,9b,4*53,5b,9b,9b,18*53,4*5b,10*8,a,10*8,a5,a3,5b,5b,7*53,49,4b
  //   ,13*53,4b,4*b,4b,4b,4*53,5b,5b,10*8,a,10*8,a5,9b,6*53,49,5*9,49,49,49
  //   ,8*53,4b,53,7*b,4b,53,53,53,5b,5b,9*8,a,8*8,a5,a5,9b,5*53,49,49
  //   ,9,1,1,1,9,1,1,9,8*53,4b,4b,10*b,53,5b,5b,53,53,8*8,a,8*8,ad,9b
  //   ,5b,4*53,49,9,49,9,9,1,1,9,1,1,9,49,6*53,4b,5*9,6*b,53,4b,53,5b,5b,5b
  //   ,8*8,a,7*8,ad,a5,7*53,49,49,49,9,9,9,49,9,9,9,1,49,5b,9d,5b,53,53
  //   ,4b,4b,b,b,4*9,5*b,53,53,53,5b,5b,8*8,a,7*8,a5,17*53,4*49,53,53,53
  //   ,4b,4b,10*9,b,b,b,4b,53,53,5b,53,7*8,a,6*8,a5,5b,53,53,53,5b,5b
  //   ,8*53,5*5b,7*53,4b,49,10*9,b,b,4b,4b,53,53,53,7*8,a,5*8,ed,a5
  //   ,4*9b,5b,9*9b,6*a5,9b,9b,5b,5b,53,53,53,4b,49,49,8*9,4b,4b,49,49
  //   ,53,53,5b,53,6*8,a,4*8,f7,ad,4*9b,5b,9b,9b,9b,5b,9b,a3,a5,a5,ad
  //   ,4*ed,f7,f7,ed,ed,ad,a5,a3,9b,53,51,51,4b,49,49,49,4*9,4*49,9,9
  //   ,49,49,53,5b,6*8,a,4*8,f7,a5,9b,5b,9b,9b,9b,5b,5b,53,5b,a5,ad
  //   ,ed,13*f7,ed,a5,a3,5b,53,15*49,53,5b,5b,5*8,a,4*8,a5,9b,5b,9b,9b,9b
  //   ,53,5b,9b,53,a3,ed,17*f7,ed,ed,a5,9b,9b,6*53,51,5*49,51,53,5b,5b
  //   ,5*8,a,4*8,a5,5b,9b,9b,5b,53,53,9b,53,5b,ad,20*f7,ef,ed,ad,4*a5
  //   ,9d,9b,9b,53,49,49,49,9,53,53,53,a3,a3,4*8,a,8,8,8,f7,a5,53,9b,9b
  //   ,53,53,53,9b,53,9b,ed,22*f7,ef,ef,af,5*ad,a5,9b,49,9,9,9,53,53
  //   ,9b,a3,4*8,a,8,8,8,f7,9b,53,9b,9b,53,53,5b,5b,5b,ad,6*f7,ff,ff,ff
  //   ,18*f7,5*af,ad,a5,49,49,49,4b,53,5b,a3,4*8,a,8,8,8,ad,5b,5b,a3
  //   ,9b,53,9b,9b,5b,a5,ed,5*f7,5*ff,17*f7,ef,ef,5*af,9d,53,49,4b,53,53
  //   ,a3,a3,8,8,8,a,8,8,8,a5,53,5b,9b,9b,5b,9b,5b,5b,a5,ed,4*f7,5*ff
  //   ,17*f7,4*ef,af,ef,af,af,a5,5b,4*53,a3,a3,8,8,8,a,8,8,f7,9b,53
  //   ,5b,9b,5b,9b,a3,53,5b,a5,ed,f7,f7,f7,ff,ff,f7,ff,ff,17*f7,6*ef
  //   ,af,af,af,ad,5d,4*53,5b,ad,8,8,8,a,8,8,f7,5b,53,9b,9b,5b,9b,5b
  //   ,53,5b,ad,ed,23*f7,6*ef,af,af,af,ef,ef,ad,a5,53,4b,53,53,53,ad
  //   ,8,8,8,a,8,8,ed,5b,5b,9b,9b,4*53,9b,ad,ed,22*f7,6*ef,5*af,ef,ad
  //   ,a5,53,4b,53,53,53,ad,8,8,8,a,8,8,ad,5b,5b,9b,5*53,a5,ad,ed,22*f7
  //   ,6*ef,5*af,ef,ad,a5,5b,53,49,51,53,ad,ed,8,8,a,8,8,a5,53,53,5b
  //   ,53,53,53,4b,5b,a5,ad,ed,26*f7,ef,ef,af,ad,ad,ad,af,ef,ed,a5,5b
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  //   contents of buffer (hex, n*v repeats v):
  //   2f,4*4f,2f,4f,6*2f,53,73,73,53,4f,4f,53,53,53,5*4f,2f,4f,4f,4*53
  //   ,73,73,73,53,53,53,10*4f,10*53,73,4*53,10*73,97,97,bb,db,df,df
  //   ,6*db,df,df,ff,ff,df,df,b7,97,97,b7,4*bb,6*db,4*bb,b7,b7,97,b7,b7
  //   ,97,97,97,93,6*73,53,4*4f,53,53,53,7*73,93,93,73,73,93,93,97,93
  //   ,7*97,93,97,b7,bb,bb,b7,b7,97,97,73,4f,73,97,97,73,73,73,93,93
  //   ,73,73,b7,db,df,26*ff,df,db,db,df,42*ff,4*df,4f,4f,4f,53,4f,4f
  //   ,53,53,53,4f,2f,2f,2f,53,5*97,73,73,73,53,2f,4f,4f,4f,53,53,4f
  //   ,53,73,53,53,53,73,97,77,73,53,11*4f,14*53,73,73,73,53,53,53,6*73
  //   ,97,bb,db,df,df,db,db,bb,db,db,df,ff,ff,ff,df,db,5*97,b7,bb,bb
  //   ,7*db,4*bb,4*b7,4*97,7*73,7*4f,53,8*73,93,93,93,73,93,93,4*97
  //   ,93,5*97,b7,b7,b7,97,97,97,93,73,97,97,93,5*73,6f,73,97,bb,db
  //   ,28*ff,df,db,df,40*ff,5*df,97,53,53,77,97,4f,4f,4f,53,53,4f,73
  //   ,53,53,73,73,97,db,df,db,bb,bb,73,53,4f,2f,4f,53,53,4f,6*53,73,73
  //   ,97,73,53,53,11*4f,16*53,73,73,53,53,4*73,97,4*bb,4*db,df,df,4*ff
  //   ,bb,97,93,5*97,b7,bb,bb,bb,db,bb,db,db,4*bb,6*b7,97,97,97,93,4*73
  //   ,53,8*4f,53,53,7*73,97,97,93,93,4*97,93,93,4*97,93,97,b7,5*97
  //   ,93,97,97,73,5*4f,73,93,b7,db,df,28*ff,df,bb,df,df,37*ff,8*df
  //   ,bb,bb,db,db,97,4f,4f,53,73,73,97,77,53,53,73,77,b7,db,df,df,db
  //   ,97,73,73,4f,4f,4*53,73,73,73,53,53,5*73,53,4f,4f,4f,53,4f,53
  //   ,4*4f,53,53,53,4f,4f,13*53,73,53,53,5*73,97,97,b7,b7,bb,db,df,df,df
  //   ,5*ff,db,8*97,b7,b7,bb,bb,bb,db,db,db,6*bb,4*b7,97,97,97,5*73
  //   ,9*4f,53,53,6*73,93,6*97,93,73,73,73,93,73,73,73,93,97,93,93,97,97
  //   ,b7,b7,b7,73,4f,4f,4f,2f,2f,4f,4f,73,97,bb,df,28*ff,df,bb,db,df,df
  //   ,31*ff,df,ff,ff,9*df,5*ff,bb,97,73,53,53,53,77,73,53,53,53,73
  //   ,97,b7,db,ff,df,db,97,73,53,4f,4f,53,53,73,73,7*97,73,73,53,4f,4f
  //   ,53,53,4f,53,15*4f,53,4f,4f,7*53,73,53,53,73,73,73,4*97,bb,db
  //   ,df,df,5*ff,df,bb,5*97,4*b7,bb,db,bb,4*db,6*bb,5*b7,97,97,5*73
  //   ,53,8*4f,53,5*73,93,7*97,6*73,53,4*73,4f,73,97,b7,bb,97,73,4f,4f
  //   ,2f,2b,2f,4f,73,73,93,bb,db,df,27*ff,df,db,bb,db,df,df,df,28*ff
  //   ,13*df,6*ff,db,bb,73,4f,53,73,73,73,53,53,73,97,bb,bb,df,df,df
  //   ,bb,97,73,53,4f,53,73,73,73,b7,bb,db,db,bb,bb,db,bb,97,53,4f,4f,4f
  //   ,53,53,20*4f,9*53,4*73,97,73,73,97,bb,db,df,6*ff,db,b7,4*97,b7
  //   ,bb,b7,b7,bb,db,bb,db,db,db,bb,bb,db,bb,bb,db,bb,bb,b7,b7,b7,bb
  //   ,b7,97,97,6*73,8*4f,53,4*73,8*97,6*73,6*4f,73,73,97,97,73,4f,4f
  //   ,2f,2f,2b,2f,4f,73,73,73,b7,db,db,27*ff,df,db,bb,bb,db,db,df,df
  //   ,26*ff,15*df,6*ff,db,73,4f,4f,5*53,73,97,bb,bb,bb,df,df,bb,bb
  //   ,73,53,53,53,73,73,73,97,bb,df,df,df,db,df,ff,db,97,4f,4f,4f,53,53
  //   ,5*4f,53,53,12*4f,12*53,73,73,93,73,73,93,97,db,df,6*ff,df,bb
  //   ,4*97,b7,bb,b7,97,b7,bb,bb,bb,db,db,db,4*bb,db,db,bb,b7,97,97
  //   ,b7,bb,b7,97,93,6*73,53,53,5*4f,53,4*73,7*97,93,6*73,6*4f,53,73,73,73
  //   ,4f,4f,2f,2f,2b,2b,2f,4f,4f,4f,73,97,bb,db,df,26*ff,df,4*bb,db
  //   ,5*df,22*ff,15*df,db,6*ff,df,97,53,53,4*73,4f,53,77,bb,bb,bb,4*db
  //   ,97,73,53,73,4*97,bb,df,6*ff,db,73,4f,53,53,53,5*4f,73,73,8*4f
  //   ,53,53,73,53,4f,11*53,6*73,97,bb,db,df,5*ff,df,bb,9*97,4*bb,db,db,db
  //   ,bb,b7,b7,4*bb,b7,97,4*b7,97,93,8*73,53,4*4f,53,73,73,73,93,6*97
  //   ,6*73,53,10*4f,4*2f,2b,2b,2b,2f,2f,2f,4f,93,bb,db,df,19*ff,df,df,df
  //   ,4*ff,df,db,bb,bb,bb,db,db,6*df,20*ff,15*df,db,7*ff,db,bb,b7,bb,bb,bb
  //   ,b7,97,73,73,97,bb,db,db,bb,db,db,bb,97,73,97,97,97,b7,97,b7,db
  //   ,7*ff,bb,73,4*53,4f,53,4f,53,73,73,53,4*4f,4*53,73,73,73,11*53
  //   ,7*73,97,b7,bb,bb,df,df,ff,ff,df,db,bb,9*97,b7,bb,b7,b7,bb,bb
  //   ,db,bb,bb,b7,b7,bb,bb,bb,6*b7,97,97,97,93,8*73,53,53,4f,4f,53
  //   ,73,73,73,93,5*97,93,73,53,73,73,53,53,4*4f,8*2f,8*2b,2f,73,b7
  //   ,bb,db,df,9*ff,df,6*ff,df,df,db,db,df,ff,ff,ff,df,db,db,4*bb,db,db
  //   ,13*df,8*ff,14*df,5*db,9*ff,df,db,bb,db,df,ff,df,b7,73,73,97,bb
  //   ,db,bb,97,bb,db,bb,bb,bb,b7,bb,b7,b7,b7,bb,8*ff,97,53,53,53,4f
  //   ,53,6*73,4*4f,5*53,73,73,10*53,4*73,93,4*73,97,97,97,bb,4*db,bb,bb
  //   ,5*97,93,73,73,5*97,b7,bb,bb,db,bb,bb,b7,4*bb,b7,b7,b7,7*97,93
  //   ,8*73,4*53,73,73,73,93,5*97,73,53,53,53,5*4f,2f,2f,2f,2b,4*2f
  //   ,2b,2f,2f,7*2b,4f,93,b7,bb,db,df,df,df,ff,ff,df,db,db,db,8*df
  //   ,4*db,df,df,df,db,db,db,4*bb,db,db,db,15*df,ff,ff,17*df,5*db,9*ff
  //   ,df,bb,bb,df,4*ff,bb,97,97,bb,db,bb,97,97,bb,db,db,bb,db,db,4*bb
  //   ,8*ff,db,73,4f,4f,4f,53,73,73,73,97,97,73,53,4f,4f,4f,5*53,73,73
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endmodule

/* Code of hsync:
module hsync(
	input [11:0] pos,
	output sync,
	output blank,
	output pad,
	output reset
);

assign blank = pos >= 512;
assign pad = blank && (pos < 576 || pos > 736);
assign reset = !(pos == 800);
assign sync = !(pos >= 592 && pos < 688);
endmodule
*/

/* Code of vsync:
module vsync(
	input [11:0] pos,
	output sync,
	output blank,
	output reset
);

assign blank = pos >= 480;
assign reset = !(pos == 525);
assign sync = !(pos >= 490 && pos < 492);
endmodule
*/
