// Digital circuit horizontal.dig as structural Verilog
module horizontal (
  input  clk,
  output [7:0] char,
  output hsync
);

  wire nand_1_out, nand_2_out, nand_3_out;

  Counter #(.Bits(8)) counter_1 (.en(1'b1), .C(clk), .clr(~nand_3_out), .out(char));  // open: ovf
  nand nand_1 (nand_1_out, char[1], char[4], char[6]);
  nand nand_2 (nand_2_out, char[1], char[2], char[3], char[4]);
  nand nand_3 (nand_3_out, char[2], char[5], char[6]);
  RS_FF_AS rs_ff_as_1 (.S(~nand_2_out), .R(~nand_1_out), .Q(hsync));  // open: nQ

  // Notes on the sheet:
  //   clk: Hz: 20
endmodule
