// Digital circuit memory_ptr.dig as structural Verilog
module memory_ptr (
  input  [7:0] in0,
  input  en,
  input  nld0,
  input  [7:0] in1,
  input  clk,
  input  nld1,
  output [15:0] out
);

  wire _74163_1_pin15, _74163_2_pin15, _74163_3_pin15;

  _74163 _74163_1 (
    .pin1(1'b1), .pin2(clk), .pin3(in0[0]), .pin4(in0[1]), .pin5(in0[2]), .pin6(in0[3]), .pin7(en),
    .pin8(1'b0), .pin9(nld0), .pin10(1'b1), .pin11(out[3]), .pin12(out[2]), .pin13(out[1]), .pin14(out[0]),
    .pin15(_74163_1_pin15), .pin16(1'b1));
  _74163 _74163_2 (
    .pin1(1'b1), .pin2(clk), .pin3(in0[4]), .pin4(in0[5]), .pin5(in0[6]), .pin6(in0[7]), .pin7(en),
    .pin8(1'b0), .pin9(nld0), .pin10(_74163_1_pin15), .pin11(out[7]), .pin12(out[6]), .pin13(out[5]),
    .pin14(out[4]), .pin15(_74163_2_pin15), .pin16(1'b1));
  _74163 _74163_3 (
    .pin1(1'b1), .pin2(clk), .pin3(in1[0]), .pin4(in1[1]), .pin5(in1[2]), .pin6(in1[3]), .pin7(en),
    .pin8(1'b0), .pin9(nld1), .pin10(_74163_2_pin15), .pin11(out[11]), .pin12(out[10]), .pin13(out[9]),
    .pin14(out[8]), .pin15(_74163_3_pin15), .pin16(1'b1));
  _74163 _74163_4 (
    .pin1(1'b1), .pin2(clk), .pin3(in1[4]), .pin4(in1[5]), .pin5(in1[6]), .pin6(in1[7]), .pin7(en),
    .pin8(1'b0), .pin9(nld1), .pin10(_74163_3_pin15), .pin11(out[15]), .pin12(out[14]), .pin13(out[13]),
    .pin14(out[12]), .pin16(1'b1));  // open: pin15

  // Notes on the sheet:
  //   clk: Hz: 100
endmodule
