// Digital circuit new_gpu.dig as structural Verilog
module new_gpu (
  input  clk,
  output [15:0] sprite_addr,
  output [15:0] addr_out,
  output [7:0] data_out
);

  wire _4bit_counter_sync_1_ovf, _4bit_counter_sync_2_ovf, _4bit_counter_sync_3_ovf,
       _4bit_counter_sync_5_ovf, _4bit_counter_sync_7_ovf, and_2_out, and_4_out, and_7_out, comparator_1_eq,
       demultiplexer_1_out_0, demultiplexer_1_out_1, demultiplexer_1_out_2, demultiplexer_1_out_3,
       demultiplexer_1_out_4, demultiplexer_1_out_6, done, drawing, jk_ff_2_nq, jk_ff_2_q, ld, ld_h, next,
       not_1_out, or_1_out, or_2_out, store;
  wire [3:0] _4bit_counter_sync_4_out;
  wire [7:0] d_ff_1_q, d_ff_2_q, data;

  D_FF #(.Bits(8)) d_ff_1 (.D(sprite_addr[11:4]), .C(demultiplexer_1_out_4), .Q(d_ff_1_q));  // open: nQ
  assign data = not_1_out ? d_ff_1_q : 8'bz;  // Driver driver_1
  or or_1 (or_1_out, _4bit_counter_sync_1_ovf, ~demultiplexer_1_out_3);  // Or
  _4bit_counter_sync _4bit_counter_sync_1 (
    .in(4'b0000), .clk(clk), .nclr(1'b1), .en(1'b1), .nld(ld), .cin(1'b1), .out(sprite_addr[3:0]),
    .ovf(_4bit_counter_sync_1_ovf));
  _4bit_counter_sync _4bit_counter_sync_2 (
    .in(data[3:0]), .clk(clk), .nclr(1'b1), .en(1'b1), .nld(ld), .cin(or_1_out), .out(sprite_addr[7:4]),
    .ovf(_4bit_counter_sync_2_ovf));
  _4bit_counter_sync _4bit_counter_sync_3 (
    .in(data[7:4]), .clk(clk), .nclr(1'b1), .en(1'b1), .nld(ld), .cin(_4bit_counter_sync_2_ovf),
    .out(sprite_addr[11:8]), .ovf(_4bit_counter_sync_3_ovf));
  _4bit_counter_sync _4bit_counter_sync_4 (
    .in(data[3:0]), .clk(clk), .nclr(1'b1), .en(1'b1), .nld(ld_h), .cin(_4bit_counter_sync_3_ovf),
    .out(_4bit_counter_sync_4_out));  // open: ovf
  assign sprite_addr[15:12] = _4bit_counter_sync_4_out & {4{drawing}};  // And and_1, 4 bits wide
  EEPROMDualPort #(.AddrBits(16), .Bits(8)) eepromdualport_1 (
    .A(sprite_addr), .Din({8{1'b0}}), .str(1'b0), .C(1'b0), .ld(jk_ff_2_nq), .D(data));
  Demultiplexer #(.Selector_Bits(3), .Default(1)) demultiplexer_1 (
    .sel(sprite_addr[2:0]), .in(drawing), .out_0(demultiplexer_1_out_0), .out_1(demultiplexer_1_out_1),
    .out_2(demultiplexer_1_out_2), .out_3(demultiplexer_1_out_3), .out_4(demultiplexer_1_out_4),
    .out_5(ld_h), .out_6(demultiplexer_1_out_6));  // open: out_7
  not not_1 (not_1_out, jk_ff_2_nq);
  JK_FF jk_ff_1 (.J(~demultiplexer_1_out_6), .C(clk), .K(jk_ff_2_q), .Q(drawing));  // open: nQ
  JK_FF jk_ff_2 (.J(done), .C(clk), .K(jk_ff_2_q), .Q(jk_ff_2_q), .nQ(jk_ff_2_nq));
  Comparator #(.Bits(6)) comparator_1 (.a(data[5:0]), .b({6{1'b1}}), .eq(comparator_1_eq));  // open: gt, lt
  and and_2 (and_2_out, ~demultiplexer_1_out_0, ~clk);  // And
  and and_3 (ld, demultiplexer_1_out_6, jk_ff_2_nq);
  D_FF #(.Bits(8)) d_ff_2 (.D(data), .C(and_2_out), .Q(d_ff_2_q));  // open: nQ
  and and_4 (and_4_out, demultiplexer_1_out_1, ~next);  // And
  and and_5 (done, comparator_1_eq, ~data[6], data[7]);  // And
  and and_6 (next, comparator_1_eq, ~data[7], data[6]);  // And
  and and_7 (and_7_out, data[7], data[6]);
  or or_2 (or_2_out, and_7_out, ~comparator_1_eq);  // Or
  _4bit_counter_sync _4bit_counter_sync_5 (
    .in(d_ff_2_q[3:0]), .clk(clk), .nclr(1'b1), .en(drawing), .nld(and_4_out), .cin(1'b1),
    .out(addr_out[3:0]), .ovf(_4bit_counter_sync_5_ovf));
  _4bit_counter_sync _4bit_counter_sync_6 (
    .in(d_ff_2_q[7:4]), .clk(clk), .nclr(1'b1), .en(drawing), .nld(and_4_out),
    .cin(_4bit_counter_sync_5_ovf), .out(addr_out[7:4]));  // open: ovf
  _4bit_counter_sync _4bit_counter_sync_7 (
    .in(data[3:0]), .clk(clk), .nclr(1'b1), .en(next), .nld(demultiplexer_1_out_1), .cin(1'b1),
    .out(addr_out[11:8]), .ovf(_4bit_counter_sync_7_ovf));
  _4bit_counter_sync _4bit_counter_sync_8 (
    .in(data[7:4]), .clk(clk), .nclr(1'b1), .en(next), .nld(demultiplexer_1_out_1),
    .cin(_4bit_counter_sync_7_ovf), .out(addr_out[15:12]));  // open: ovf
  and and_8 (store, or_2_out, jk_ff_2_nq, drawing);
  RAMDualPort #(.AddrBits(16), .Bits(8)) ramdualport_1 (
    .A(addr_out), .Din(data), .str(store), .C(clk), .ld(1'b1), .D(data_out));

  // Notes on the sheet:
  //   clk: Hz: 3
  //   contents of eepromdualport_1 (hex, n*v repeats v):
  //   1,2,14*0,3,4,0,0,0,1,23,14*0,1,23,4619*0,7f,0,3f,0,ff,0,bf
endmodule
