// Digital circuit textgen.dig as structural Verilog
module textgen (
  input  clk,
  output [7:0] reg1,
  output [7:0] reg0_debug,
  output hsync,
  output [11:0] line,
  output vsync,
  output [6:0] char,
  output video_out
);

  wire counter_1_ovf, counter_3_ovf, counter_4_ovf, demultiplexer_1_out_0, demultiplexer_1_out_1,
       demultiplexer_1_out_2, demultiplexer_1_out_3, demultiplexer_1_out_4, demultiplexer_1_out_6, not_1_out,
       not_4_out, not_5_out, u_horizontal_clr, u_vertical_clr;
  wire [0:0] counter_6_out_2;
  wire [3:0] counter_6_out;
  wire [3:3] counter_2_out;
  wire [7:0] d_ff_1_q, d_ff_2_q, video_mem_d;

  Counter #(.Bits(4)) counter_1 (
    .en(1'b1), .C(counter_6_out_2[0]), .clr(u_horizontal_clr), .out(char[3:0]), .ovf(counter_1_ovf));
  Counter #(.Bits(4)) counter_2 (
    .en(counter_1_ovf), .C(counter_6_out_2[0]), .clr(u_horizontal_clr), .out({counter_2_out[3], char[6:4]}));  // open: ovf
  Counter #(.Bits(4)) counter_3 (
    .en(u_horizontal_clr), .C(counter_6_out_2[0]), .clr(1'b0), .out(line[3:0]), .ovf(counter_3_ovf));
  Counter #(.Bits(4)) counter_4 (
    .en(counter_3_ovf), .C(counter_6_out_2[0]), .clr(u_vertical_clr), .out(line[7:4]), .ovf(counter_4_ovf));
  Counter #(.Bits(4)) counter_5 (
    .en(counter_4_ovf), .C(counter_6_out_2[0]), .clr(u_vertical_clr), .out(line[11:8]));  // open: ovf
  Counter #(.Bits(4)) counter_6 (
    .en(1'b1), .C(clk), .clr(1'b0), .out({counter_6_out[3], counter_6_out_2[0], counter_6_out[1:0]}));  // open: ovf
  Demultiplexer #(.Selector_Bits(3)) demultiplexer_1 (
    .sel({counter_6_out_2[0], counter_6_out[1:0]}), .in(1'b1), .out_0(demultiplexer_1_out_0),
    .out_1(demultiplexer_1_out_1), .out_2(demultiplexer_1_out_2), .out_3(demultiplexer_1_out_3),
    .out_4(demultiplexer_1_out_4), .out_6(demultiplexer_1_out_6));  // open: out_5, out_7
  not not_1 (not_1_out, demultiplexer_1_out_0);
  // Not not_2 has open pins: in=demultiplexer_1_out_1, out=open
  // Not not_3 has open pins: in=demultiplexer_1_out_2, out=open
  not not_4 (not_4_out, demultiplexer_1_out_3);
  not not_5 (not_5_out, demultiplexer_1_out_4);
  // Not not_6 has open pins: in=demultiplexer_1_out_6, out=open
  horizontal #(.applicationType("IVERILOG")) u_horizontal (.char(char), .sync(hsync), .clr(u_horizontal_clr));
  ROM #(.AddrBits(12), .Bits(8)) char_data (.A({video_mem_d, line[3:0]}), .sel(1'b1), .D(reg0_debug));
  vertical #(.applicationType("IVERILOG")) u_vertical (.line(line), .sync(vsync), .clr(u_vertical_clr));
  D_FF #(.Bits(8)) d_ff_1 (.D(reg0_debug), .C(not_1_out), .Q(d_ff_1_q));  // open: nQ
  D_FF #(.Bits(8)) d_ff_2 (.D(video_mem_d), .C(not_5_out), .Q(d_ff_2_q));  // open: nQ
  ROM #(.AddrBits(13), .Bits(8)) video_mem (.A({line[8:4], char, counter_6_out_2[0]}), .sel(1'b1), .D(video_mem_d));
  D_FF #(.Bits(8)) d_ff_3 (.D(d_ff_2_q), .C(not_1_out), .Q(reg1));  // open: nQ
  Multiplexer #(.Selector_Bits(3)) multiplexer_1 (
    .sel({counter_6_out_2[0], counter_6_out[1:0]}), .in_0(d_ff_1_q[0]), .in_1(d_ff_1_q[7]),
    .in_2(d_ff_1_q[6]), .in_3(d_ff_1_q[5]), .in_4(d_ff_1_q[4]), .in_5(d_ff_1_q[3]), .in_6(d_ff_1_q[2]),
    .in_7(d_ff_1_q[1]), .out(video_out));

  // Notes on the sheet:
  //   clk: Hz: 1000
  //   contents of char_data (hex, n*v repeats v):
  //   18*0,7e,81,a5,81,81,bd,99,81,81,7e,6*0,7e,ff,db,ff,ff,c3,e7,ff,ff
  //   ,7e,8*0,6c,4*fe,7c,38,10,8*0,10,38,7c,fe,7c,38,10,8*0,18,3c,3c
  //   ,e7,e7,e7,18,18,3c,7*0,18,3c,7e,ff,ff,7e,18,18,3c,10*0,18,3c,3c
  //   ,18,6*0,6*ff,e7,c3,c3,e7,6*ff,5*0,3c,66,42,42,66,3c,5*0,5*ff,c3
  //   ,99,bd,bd,99,c3,5*ff,0,0,1e,e,1a,32,78,4*cc,78,6*0,3c,4*66,3c
  //   ,18,7e,18,18,6*0,3f,33,3f,4*30,70,f0,e0,6*0,7f,63,7f,4*63,67,e7
  //   ,e6,c0,6*0,18,18,db,3c,e7,3c,db,18,18,5*0,80,c0,e0,f0,f8,fe,f8
  //   ,f0,e0,c0,80,5*0,2,6,e,1e,3e,fe,3e,1e,e,6,2,6*0,18,3c,7e,18,18,18
  //   ,7e,3c,18,7*0,7*66,0,66,66,6*0,7f,db,db,db,7b,5*1b,5*0,7c,c6,60
  //   ,38,6c,c6,c6,6c,38,c,c6,7c,11*0,4*fe,6*0,18,3c,7e,18,18,18,7e
  //   ,3c,18,7e,6*0,18,3c,7e,7*18,6*0,7*18,7e,3c,18,9*0,18,c,fe,c,18
  //   ,11*0,30,60,fe,60,30,12*0,c0,c0,c0,fe,11*0,24,66,ff,66,24,10*0
  //   ,10,38,38,7c,7c,fe,fe,9*0,fe,fe,7c,7c,38,38,10,23*0,18,3c,3c,3c
  //   ,18,18,18,0,18,18,5*0,66,66,66,24,14*0,6c,6c,fe,6c,6c,6c,fe,6c,6c
  //   ,4*0,18,18,7c,c6,c2,c0,7c,6,6,86,c6,7c,18,18,6*0,c2,c6,c,18,30
  //   ,60,c6,86,6*0,38,6c,6c,38,76,dc,cc,cc,cc,76,5*0,30,30,30,60,13*0
  //   ,c,18,6*30,18,c,6*0,30,18,6*c,18,30,9*0,66,3c,ff,3c,66,11*0,18,18
  //   ,7e,18,18,15*0,18,18,18,30,10*0,fe,18*0,18,18,8*0,2,6,c,18,30
  //   ,60,c0,80,6*0,3c,66,c3,c3,db,db,c3,c3,66,3c,6*0,18,38,78,6*18
  //   ,7e,6*0,7c,c6,6,c,18,30,60,c0,c6,fe,6*0,7c,c6,6,6,3c,6,6,6,c6
  //   ,7c,6*0,c,1c,3c,6c,cc,fe,c,c,c,1e,6*0,fe,c0,c0,c0,fc,6,6,6,c6
  //   ,7c,6*0,38,60,c0,c0,fc,4*c6,7c,6*0,fe,c6,6,6,c,18,4*30,6*0,7c
  //   ,c6,c6,c6,7c,4*c6,7c,6*0,7c,c6,c6,c6,7e,6,6,6,c,78,8*0,18,18,0,0,0
  //   ,18,18,9*0,18,18,0,0,0,18,18,30,7*0,6,c,18,30,60,30,18,c,6,9*0
  //   ,7e,0,0,7e,10*0,60,30,18,c,6,c,18,30,60,6*0,7c,c6,c6,c,18,18,18
  //   ,0,18,18,7*0,7c,c6,c6,de,de,de,dc,c0,7c,6*0,10,38,6c,c6,c6,fe
  //   ,4*c6,6*0,fc,66,66,66,7c,4*66,fc,6*0,3c,66,c2,4*c0,c2,66,3c,6*0
  //   ,f8,6c,6*66,6c,f8,6*0,fe,66,62,68,78,68,60,62,66,fe,6*0,fe,66
  //   ,62,68,78,68,60,60,60,f0,6*0,3c,66,c2,c0,c0,de,c6,c6,66,3a,6*0
  //   ,4*c6,fe,5*c6,6*0,3c,8*18,3c,6*0,1e,5*c,cc,cc,cc,78,6*0,e6,66,66
  //   ,6c,78,78,6c,66,66,e6,6*0,f0,6*60,62,66,fe,6*0,c3,e7,ff,ff,db
  //   ,5*c3,6*0,c6,e6,f6,fe,de,ce,4*c6,6*0,7c,8*c6,7c,6*0,fc,66,66,66
  //   ,7c,4*60,f0,6*0,7c,6*c6,d6,de,7c,c,e,4*0,fc,66,66,66,7c,6c,66,66,66
  //   ,e6,6*0,7c,c6,c6,60,38,c,6,c6,c6,7c,6*0,ff,db,99,6*18,3c,6*0,9*c6
  //   ,7c,6*0,7*c3,66,3c,18,6*0,5*c3,db,db,ff,66,66,6*0,c3,c3,66,3c
  //   ,18,18,3c,66,c3,c3,6*0,c3,c3,c3,66,3c,4*18,3c,6*0,ff,c3,86,c,18
  //   ,30,60,c1,c3,ff,6*0,3c,8*30,3c,7*0,80,c0,e0,70,38,1c,e,6,2,6*0
  //   ,3c,8*c,3c,4*0,10,38,6c,c6,25*0,ff,0,0,30,30,18,18*0,78,c,7c,cc,cc,cc
  //   ,76,6*0,e0,60,60,78,6c,4*66,7c,9*0,7c,c6,c0,c0,c0,c6,7c,6*0,1c
  //   ,c,c,3c,6c,4*cc,76,9*0,7c,c6,fe,c0,c0,c6,7c,6*0,38,6c,64,60,f0
  //   ,4*60,f0,9*0,76,5*cc,7c,c,cc,78,0,0,0,e0,60,60,6c,76,4*66,e6,6*0
  //   ,18,18,0,38,5*18,3c,6*0,6,6,0,e,6*6,66,66,3c,0,0,0,e0,60,60,66
  //   ,6c,78,78,6c,66,e6,6*0,38,8*18,3c,9*0,e6,ff,5*db,9*0,dc,6*66,9*0
  //   ,7c,5*c6,7c,9*0,dc,5*66,7c,60,60,f0,6*0,76,5*cc,7c,c,c,1e,6*0
  //   ,dc,76,66,60,60,60,f0,9*0,7c,c6,60,38,c,c6,7c,6*0,10,30,30,fc
  //   ,4*30,36,1c,9*0,6*cc,76,9*0,4*c3,66,3c,18,9*0,c3,c3,c3,db,db,ff
  //   ,66,9*0,c3,66,3c,18,3c,66,c3,9*0,6*c6,7e,6,c,f8,6*0,fe,cc,18,30
  //   ,60,c6,fe,6*0,e,18,18,18,70,4*18,e,6*0,4*18,0,5*18,6*0,70,18,18,18
  //   ,e,4*18,70,6*0,76,dc,16*0,10,38,6c,c6,c6,c6,fe,7*0,3c,66,c2,c0,c0,c0
  //   ,c2,66,3c,c,6,7c,4*0,cc,0,0,6*cc,76,5*0,c,18,30,0,7c,c6,fe,c0,c0
  //   ,c6,7c,5*0,10,38,6c,0,78,c,7c,cc,cc,cc,76,6*0,cc,0,0,78,c,7c,cc,cc,cc
  //   ,76,5*0,60,30,18,0,78,c,7c,cc,cc,cc,76,5*0,38,6c,38,0,78,c,7c
  //   ,cc,cc,cc,76,8*0,3c,66,60,60,66,3c,c,6,3c,4*0,10,38,6c,0,7c,c6
  //   ,fe,c0,c0,c6,7c,6*0,c6,0,0,7c,c6,fe,c0,c0,c6,7c,5*0,60,30,18,0
  //   ,7c,c6,fe,c0,c0,c6,7c,6*0,66,0,0,38,5*18,3c,5*0,18,3c,66,0,38
  //   ,5*18,3c,5*0,60,30,18,0,38,5*18,3c,5*0,c6,0,10,38,6c,c6,c6,fe
  //   ,c6,c6,c6,4*0,38,6c,38,0,38,6c,c6,c6,fe,c6,c6,c6,4*0,18,30,60
  //   ,0,fe,66,60,7c,60,60,66,fe,9*0,6e,3b,1b,7e,d8,dc,77,6*0,3e,6c
  //   ,cc,cc,fe,4*cc,ce,5*0,10,38,6c,0,7c,5*c6,7c,6*0,c6,0,0,7c,5*c6
  //   ,7c,5*0,60,30,18,0,7c,5*c6,7c,5*0,30,78,cc,0,6*cc,76,5*0,60,30
  //   ,18,0,6*cc,76,6*0,c6,0,0,6*c6,7e,6,c,78,0,0,c6,0,7c,7*c6,7c,5*0
  //   ,c6,0,8*c6,7c,5*0,18,18,7e,c3,c0,c0,c0,c3,7e,18,18,5*0,38,6c,64
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  //   contents of video_mem (hex, n*v repeats v):
  //   c9,1,cd,3,cd,1,cd,3,cd,1,cd,3,cd,1,cd,3,cd,1,cd,3,cd,1,cd,3,cd
  //   ,1,cd,3,cd,1,cd,3,cd,1,cd,3,cd,1,cd,3,cd,1,cd,3,cd,1,cd,3,cd,1
  //   ,cd,3,cd,1,cd,3,cd,1,cd,3,cd,1,cd,3,cd,1,cd,3,cd,1,cd,3,cd,1,cd
  //   ,3,cd,1,cd,3,cd,1,cd,3,cd,1,cd,3,cd,1,cd,3,cd,1,cd,3,cd,1,cd,3
  //   ,cd,1,cd,3,cd,1,cd,3,cd,1,cd,3,cd,1,cd,3,cd,1,cd,3,cd,1,cd,3,cd
  //   ,1,cd,3,cd,1,cd,3,cd,1,cd,3,cd,1,cd,3,cd,1,cd,3,cd,1,cd,3,cd,1
  //   ,cd,3,cd,1,cd,3,cd,1,bb,3,96*0,ba,3,41,1,63,3,63,1,6f,3,72,1,64
  //   ,3,69,1,6e,3,67,1,20,3,74,1,6f,3,20,1,61,3,6c,1,6c,3,20,1,6b,3
  //   ,6e,1,6f,3,77,1,6e,3,20,1,6c,3,61,1,77,3,73,1,20,3,6f,1,66,3,20
  //   ,1,61,3,76,1,69,3,61,1,74,3,69,1,6f,3,6e,1,2c,3,20,1,74,3,68,1
  //   ,65,3,72,1,65,3,20,1,69,3,73,1,20,3,6e,1,6f,3,20,1,77,3,61,1,79
  //   ,3,20,1,61,3,20,1,62,3,65,1,65,3,20,1,73,3,68,1,6f,3,75,1,6c,3
  //   ,64,1,20,3,62,1,65,3,20,1,61,3,62,1,6c,3,65,1,20,3,ba,1,96*0,ba
  //   ,1,74,3,6f,1,20,3,66,1,6c,3,79,1,2e,3,20,1,49,3,74,1,73,3,20,1
  //   ,77,3,69,1,6e,3,67,1,73,3,20,1,61,3,72,1,65,3,20,1,74,3,6f,1,6f
  //   ,3,20,1,73,3,6d,1,61,3,6c,1,6c,3,20,1,74,3,6f,1,20,3,67,1,65,3
  //   ,74,1,20,3,69,1,74,3,73,1,20,3,66,1,61,3,74,1,20,3,6c,1,69,3,74
  //   ,1,74,3,6c,1,65,3,20,1,62,3,6f,1,64,3,79,1,20,3,6f,1,66,3,66,1
  //   ,20,3,74,1,68,3,65,1,20,3,67,1,72,3,6f,1,75,3,6e,1,64,3,2e,1,20
  //   ,3,54,1,68,3,65,1,ba,3,96*0,ba,3,20,1,62,3,65,1,65,3,2c,1,20,3
  //   ,6f,1,66,3,20,1,63,3,6f,1,75,3,72,1,73,3,65,1,2c,3,20,1,66,3,6c
  //   ,1,69,3,65,1,73,3,20,1,61,3,6e,1,79,3,77,1,61,3,79,1,20,3,62,1
  //   ,65,3,63,1,61,3,75,1,73,3,65,1,20,3,62,1,65,3,65,1,73,3,20,1,64
  //   ,3,6f,1,6e,3,27,1,74,3,20,1,63,3,61,1,72,3,65,1,20,3,77,1,68,3
  //   ,61,1,74,3,20,1,68,3,75,1,6d,3,61,1,6e,3,73,1,20,3,74,1,68,3,69
  //   ,1,6e,3,6b,1,20,3,69,1,73,3,20,1,69,3,6d,1,70,3,ba,1,96*0,ba,1
  //   ,6f,3,73,1,73,3,69,1,62,3,6c,1,65,3,2e,1,20,3,59,1,65,3,6c,1,6c
  //   ,3,6f,1,77,3,2c,1,20,3,62,1,6c,3,61,1,63,3,6b,1,2e,3,20,1,59,3
  //   ,65,1,6c,3,6c,1,6f,3,77,1,2c,3,20,1,62,3,6c,1,61,3,63,1,6b,3,2e
  //   ,1,20,3,59,1,65,3,6c,1,6c,3,6f,1,77,3,2c,1,20,3,62,1,6c,3,61,1
  //   ,63,3,6b,1,2e,3,20,1,59,3,65,1,6c,3,6c,1,6f,3,77,1,2c,3,20,1,62
  //   ,3,6c,1,61,3,63,1,6b,3,2e,1,20,3,4f,1,6f,3,68,1,2c,3,20,1,62,3
  //   ,6c,1,61,3,63,1,ba,3,96*0,ba,3,6b,1,20,3,61,1,6e,3,64,1,20,3,79
  //   ,1,65,3,6c,1,6c,3,6f,1,77,3,21,1,20,3,4c,1,65,3,74,1,27,3,73,1
  //   ,20,3,73,1,68,3,61,1,6b,3,65,1,20,3,69,1,74,3,20,1,75,3,70,1,20
  //   ,3,61,1,20,3,6c,1,69,3,74,1,74,3,6c,1,65,3,2e,1,20,3,42,1,61,3
  //   ,72,1,72,3,79,1,21,3,20,1,42,3,72,1,65,3,61,1,6b,3,66,1,61,3,73
  //   ,1,74,3,20,1,69,3,73,1,20,3,72,1,65,3,61,1,64,3,79,1,21,3,20,1
  //   ,4f,3,6f,1,6d,3,69,1,6e,3,67,1,21,3,20,1,48,3,ba,1,96*0,ba,1,61
  //   ,3,6e,1,67,3,20,1,6f,3,6e,1,20,3,61,1,20,3,73,1,65,3,63,1,6f,3
  //   ,6e,1,64,3,2e,1,20,3,48,1,65,3,6c,1,6c,3,6f,1,3f,3,20,1,2d,3,20
  //   ,1,42,3,61,1,72,3,72,1,79,3,3f,1,20,3,2d,1,20,3,41,1,64,3,61,1
  //   ,6d,3,3f,1,20,3,2d,1,20,3,4f,1,61,3,6e,1,20,3,79,1,6f,3,75,1,20
  //   ,3,62,1,65,3,6c,1,69,3,65,1,76,3,65,1,20,3,74,1,68,3,69,1,73,3
  //   ,20,1,69,3,73,1,20,3,68,1,61,3,70,1,70,3,65,1,6e,3,69,1,6e,3,67
  //   ,1,3f,3,20,1,ba,3,96*0,ba,3,2d,1,20,3,49,1,20,3,63,1,61,3,6e,1
  //   ,27,3,74,1,2e,3,20,1,49,3,27,1,6c,3,6c,1,20,3,70,1,69,3,63,1,6b
  //   ,3,20,1,79,3,6f,1,75,3,20,1,75,3,70,1,2e,3,20,1,4c,3,6f,1,6f,3
  //   ,6b,1,69,3,6e,1,67,3,20,1,73,3,68,1,61,3,72,1,70,3,2e,1,20,3,55
  //   ,1,73,3,65,1,20,3,74,1,68,3,65,1,20,3,73,1,74,3,61,1,69,3,72,1
  //   ,73,3,2e,1,20,3,59,1,6f,3,75,1,72,3,20,1,66,3,61,1,74,3,68,1,65
  //   ,3,72,1,20,3,70,1,61,3,69,1,64,3,20,1,67,3,ba,1,96*0,ba,1,6f,3
  //   ,6f,1,64,3,20,1,6d,3,6f,1,6e,3,65,1,79,3,20,1,66,3,6f,1,72,3,20
  //   ,1,74,3,68,1,6f,3,73,1,65,3,2e,1,20,3,53,1,6f,3,72,1,72,3,79,1
  //   ,2e,3,20,1,49,3,27,1,6d,3,20,1,65,3,78,1,63,3,69,1,74,3,65,1,64
  //   ,3,2e,1,20,3,48,1,65,3,72,1,65,3,27,1,73,3,20,1,74,3,68,1,65,3
  //   ,20,1,67,3,72,1,61,3,64,1,75,3,61,1,74,3,65,1,2e,3,20,1,57,3,65
  //   ,1,27,3,72,1,65,3,20,1,76,3,65,1,72,3,79,1,20,3,70,1,72,3,6f,1
  //   ,75,3,64,1,ba,3,96*0,ba,3,20,1,6f,3,66,1,20,3,79,1,6f,3,75,1,2c
  //   ,3,20,1,73,3,6f,1,6e,3,2e,1,20,3,41,1,20,3,70,1,65,3,72,1,66,3
  //   ,65,1,63,3,74,1,20,3,72,1,65,3,70,1,6f,3,72,1,74,3,20,1,63,3,61
  //   ,1,72,3,64,1,2c,3,20,1,61,3,6c,1,6c,3,20,1,42,3,27,1,73,3,2e,1
  //   ,20,3,56,1,65,3,72,1,79,3,20,1,70,3,72,1,6f,3,75,1,64,3,2e,1,20
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endmodule

/* Code of horizontal:
module horizontal(
	input [6:0] char,
	output sync,
	output clr
);
	assign clr = char == 8'd99;
	assign sync = !(char >= 8'd82 && char < 8'd94);
endmodule
*/

/* Code of vertical:
module vertical(
	input [11:0] line,
	output sync,
	output clr
);
	assign clr = line == 524;
	assign sync = !(line >= 490 && line < 492);
endmodule
*/
