// Digital circuit textgen_simple.dig as structural Verilog
module textgen_simple (
  input  clk,
  output hsync,
  output [11:0] line,
  output vsync,
  output [6:0] char,
  output pixel,
  output [2:0] \bit ,
  output [3:0] color
);

  wire counter_1_ovf, counter_3_ovf, counter_4_ovf, u_horizontal_clr, u_vertical_clr;
  wire [3:3] counter_2_out, counter_6_out;
  wire [7:0] char_data_d, color_mem_d, d_ff_1_q, d_ff_2_q;
  wire [11:4] text_mem_d;

  Counter #(.Bits(4)) counter_1 (.en(1'b1), .C(\bit [2]), .clr(u_horizontal_clr), .out(char[3:0]), .ovf(counter_1_ovf));
  Counter #(.Bits(4)) counter_2 (
    .en(counter_1_ovf), .C(\bit [2]), .clr(u_horizontal_clr), .out({counter_2_out[3], char[6:4]}));  // open: ovf
  Counter #(.Bits(4)) counter_3 (.en(u_horizontal_clr), .C(\bit [2]), .clr(1'b0), .out(line[3:0]), .ovf(counter_3_ovf));
  Counter #(.Bits(4)) counter_4 (
    .en(counter_3_ovf), .C(\bit [2]), .clr(u_vertical_clr), .out(line[7:4]), .ovf(counter_4_ovf));
  Counter #(.Bits(4)) counter_5 (
    .en(counter_4_ovf), .C(\bit [2]), .clr(u_vertical_clr), .out(line[11:8]));  // open: ovf
  Counter #(.Bits(4)) counter_6 (.en(1'b1), .C(clk), .clr(1'b0), .out({counter_6_out[3], \bit }));  // open: ovf
  horizontal #(.applicationType("IVERILOG")) u_horizontal (.char(char), .sync(hsync), .clr(u_horizontal_clr));
  vertical #(.applicationType("IVERILOG")) u_vertical (.line(line), .sync(vsync), .clr(u_vertical_clr));
  ROM #(.AddrBits(12), .Bits(8)) char_data (.A({text_mem_d, line[3:0]}), .sel(1'b1), .D(char_data_d));
  D_FF #(.Bits(8)) d_ff_1 (.D(char_data_d), .C(\bit [2]), .Q(d_ff_1_q));  // open: nQ
  ROM #(.AddrBits(12), .Bits(8)) text_mem (.A({line[8:4], char}), .sel(1'b1), .D(text_mem_d));
  ROM #(.AddrBits(12), .Bits(8)) color_mem (.A({line[8:4], char}), .sel(1'b1), .D(color_mem_d));
  D_FF #(.Bits(8)) d_ff_2 (.D(color_mem_d), .C(\bit [2]), .Q(d_ff_2_q));  // open: nQ
  Multiplexer #(.Selector_Bits(3)) multiplexer_1 (
    .sel(\bit ), .in_0(d_ff_1_q[3]), .in_1(d_ff_1_q[2]), .in_2(d_ff_1_q[1]), .in_3(d_ff_1_q[0]),
    .in_4(d_ff_1_q[7]), .in_5(d_ff_1_q[6]), .in_6(d_ff_1_q[5]), .in_7(d_ff_1_q[4]), .out(pixel));
  Multiplexer #(.Bits(4)) multiplexer_2 (.sel(pixel), .in_0(d_ff_2_q[3:0]), .in_1(d_ff_2_q[7:4]), .out(color));

  // Notes on the sheet:
  //   clk: Hz: 1000
  //   contents of char_data (hex, n*v repeats v):
  //   18*0,7e,81,a5,81,81,bd,99,81,81,7e,6*0,7e,ff,db,ff,ff,c3,e7,ff,ff
  //   ,7e,8*0,6c,4*fe,7c,38,10,8*0,10,38,7c,fe,7c,38,10,8*0,18,3c,3c
  //   ,e7,e7,e7,18,18,3c,7*0,18,3c,7e,ff,ff,7e,18,18,3c,10*0,18,3c,3c
  //   ,18,6*0,6*ff,e7,c3,c3,e7,6*ff,5*0,3c,66,42,42,66,3c,5*0,5*ff,c3
  //   ,99,bd,bd,99,c3,5*ff,0,0,1e,e,1a,32,78,4*cc,78,6*0,3c,4*66,3c
  //   ,18,7e,18,18,6*0,3f,33,3f,4*30,70,f0,e0,6*0,7f,63,7f,4*63,67,e7
  //   ,e6,c0,6*0,18,18,db,3c,e7,3c,db,18,18,5*0,80,c0,e0,f0,f8,fe,f8
  //   ,f0,e0,c0,80,5*0,2,6,e,1e,3e,fe,3e,1e,e,6,2,6*0,18,3c,7e,18,18,18
  //   ,7e,3c,18,7*0,7*66,0,66,66,6*0,7f,db,db,db,7b,5*1b,5*0,7c,c6,60
  //   ,38,6c,c6,c6,6c,38,c,c6,7c,11*0,4*fe,6*0,18,3c,7e,18,18,18,7e
  //   ,3c,18,7e,6*0,18,3c,7e,7*18,6*0,7*18,7e,3c,18,9*0,18,c,fe,c,18
  //   ,11*0,30,60,fe,60,30,12*0,c0,c0,c0,fe,11*0,24,66,ff,66,24,10*0
  //   ,10,38,38,7c,7c,fe,fe,9*0,fe,fe,7c,7c,38,38,10,23*0,18,3c,3c,3c
  //   ,18,18,18,0,18,18,5*0,66,66,66,24,14*0,6c,6c,fe,6c,6c,6c,fe,6c,6c
  //   ,4*0,18,18,7c,c6,c2,c0,7c,6,6,86,c6,7c,18,18,6*0,c2,c6,c,18,30
  //   ,60,c6,86,6*0,38,6c,6c,38,76,dc,cc,cc,cc,76,5*0,30,30,30,60,13*0
  //   ,c,18,6*30,18,c,6*0,30,18,6*c,18,30,9*0,66,3c,ff,3c,66,11*0,18,18
  //   ,7e,18,18,15*0,18,18,18,30,10*0,fe,18*0,18,18,8*0,2,6,c,18,30
  //   ,60,c0,80,6*0,3c,66,c3,c3,db,db,c3,c3,66,3c,6*0,18,38,78,6*18
  //   ,7e,6*0,7c,c6,6,c,18,30,60,c0,c6,fe,6*0,7c,c6,6,6,3c,6,6,6,c6
  //   ,7c,6*0,c,1c,3c,6c,cc,fe,c,c,c,1e,6*0,fe,c0,c0,c0,fc,6,6,6,c6
  //   ,7c,6*0,38,60,c0,c0,fc,4*c6,7c,6*0,fe,c6,6,6,c,18,4*30,6*0,7c
  //   ,c6,c6,c6,7c,4*c6,7c,6*0,7c,c6,c6,c6,7e,6,6,6,c,78,8*0,18,18,0,0,0
  //   ,18,18,9*0,18,18,0,0,0,18,18,30,7*0,6,c,18,30,60,30,18,c,6,9*0
  //   ,7e,0,0,7e,10*0,60,30,18,c,6,c,18,30,60,6*0,7c,c6,c6,c,18,18,18
  //   ,0,18,18,7*0,7c,c6,c6,de,de,de,dc,c0,7c,6*0,10,38,6c,c6,c6,fe
  //   ,4*c6,6*0,fc,66,66,66,7c,4*66,fc,6*0,3c,66,c2,4*c0,c2,66,3c,6*0
  //   ,f8,6c,6*66,6c,f8,6*0,fe,66,62,68,78,68,60,62,66,fe,6*0,fe,66
  //   ,62,68,78,68,60,60,60,f0,6*0,3c,66,c2,c0,c0,de,c6,c6,66,3a,6*0
  //   ,4*c6,fe,5*c6,6*0,3c,8*18,3c,6*0,1e,5*c,cc,cc,cc,78,6*0,e6,66,66
  //   ,6c,78,78,6c,66,66,e6,6*0,f0,6*60,62,66,fe,6*0,c3,e7,ff,ff,db
  //   ,5*c3,6*0,c6,e6,f6,fe,de,ce,4*c6,6*0,7c,8*c6,7c,6*0,fc,66,66,66
  //   ,7c,4*60,f0,6*0,7c,6*c6,d6,de,7c,c,e,4*0,fc,66,66,66,7c,6c,66,66,66
  //   ,e6,6*0,7c,c6,c6,60,38,c,6,c6,c6,7c,6*0,ff,db,99,6*18,3c,6*0,9*c6
  //   ,7c,6*0,7*c3,66,3c,18,6*0,5*c3,db,db,ff,66,66,6*0,c3,c3,66,3c
  //   ,18,18,3c,66,c3,c3,6*0,c3,c3,c3,66,3c,4*18,3c,6*0,ff,c3,86,c,18
  //   ,30,60,c1,c3,ff,6*0,3c,8*30,3c,7*0,80,c0,e0,70,38,1c,e,6,2,6*0
  //   ,3c,8*c,3c,4*0,10,38,6c,c6,25*0,ff,0,0,30,30,18,18*0,78,c,7c,cc,cc,cc
  //   ,76,6*0,e0,60,60,78,6c,4*66,7c,9*0,7c,c6,c0,c0,c0,c6,7c,6*0,1c
  //   ,c,c,3c,6c,4*cc,76,9*0,7c,c6,fe,c0,c0,c6,7c,6*0,38,6c,64,60,f0
  //   ,4*60,f0,9*0,76,5*cc,7c,c,cc,78,0,0,0,e0,60,60,6c,76,4*66,e6,6*0
  //   ,18,18,0,38,5*18,3c,6*0,6,6,0,e,6*6,66,66,3c,0,0,0,e0,60,60,66
  //   ,6c,78,78,6c,66,e6,6*0,38,8*18,3c,9*0,e6,ff,5*db,9*0,dc,6*66,9*0
  //   ,7c,5*c6,7c,9*0,dc,5*66,7c,60,60,f0,6*0,76,5*cc,7c,c,c,1e,6*0
  //   ,dc,76,66,60,60,60,f0,9*0,7c,c6,60,38,c,c6,7c,6*0,10,30,30,fc
  //   ,4*30,36,1c,9*0,6*cc,76,9*0,4*c3,66,3c,18,9*0,c3,c3,c3,db,db,ff
  //   ,66,9*0,c3,66,3c,18,3c,66,c3,9*0,6*c6,7e,6,c,f8,6*0,fe,cc,18,30
  //   ,60,c6,fe,6*0,e,18,18,18,70,4*18,e,6*0,4*18,0,5*18,6*0,70,18,18,18
  //   ,e,4*18,70,6*0,76,dc,16*0,10,38,6c,c6,c6,c6,fe,7*0,3c,66,c2,c0,c0,c0
  //   ,c2,66,3c,c,6,7c,4*0,cc,0,0,6*cc,76,5*0,c,18,30,0,7c,c6,fe,c0,c0
  //   ,c6,7c,5*0,10,38,6c,0,78,c,7c,cc,cc,cc,76,6*0,cc,0,0,78,c,7c,cc,cc,cc
  //   ,76,5*0,60,30,18,0,78,c,7c,cc,cc,cc,76,5*0,38,6c,38,0,78,c,7c
  //   ,cc,cc,cc,76,8*0,3c,66,60,60,66,3c,c,6,3c,4*0,10,38,6c,0,7c,c6
  //   ,fe,c0,c0,c6,7c,6*0,c6,0,0,7c,c6,fe,c0,c0,c6,7c,5*0,60,30,18,0
  //   ,7c,c6,fe,c0,c0,c6,7c,6*0,66,0,0,38,5*18,3c,5*0,18,3c,66,0,38
  //   ,5*18,3c,5*0,60,30,18,0,38,5*18,3c,5*0,c6,0,10,38,6c,c6,c6,fe
  //   ,c6,c6,c6,4*0,38,6c,38,0,38,6c,c6,c6,fe,c6,c6,c6,4*0,18,30,60
  //   ,0,fe,66,60,7c,60,60,66,fe,9*0,6e,3b,1b,7e,d8,dc,77,6*0,3e,6c
  //   ,cc,cc,fe,4*cc,ce,5*0,10,38,6c,0,7c,5*c6,7c,6*0,c6,0,0,7c,5*c6
  //   ,7c,5*0,60,30,18,0,7c,5*c6,7c,5*0,30,78,cc,0,6*cc,76,5*0,60,30
  //   ,18,0,6*cc,76,6*0,c6,0,0,6*c6,7e,6,c,78,0,0,c6,0,7c,7*c6,7c,5*0
  //   ,c6,0,8*c6,7c,5*0,18,18,7e,c3,c0,c0,c0,c3,7e,18,18,5*0,38,6c,64
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  //   contents of text_mem (hex, n*v repeats v):
  //   c9,78*cd,bb,48*0,ba,41,63,63,6f,72,64,69,6e,67,20,74,6f,20,61
  //   ,6c,6c,20,6b,6e,6f,77,6e,20,6c,61,77,73,20,6f,66,20,61,76,69,61
  //   ,74,69,6f,6e,2c,20,74,68,65,72,65,20,69,73,20,6e,6f,20,77,61,79
  //   ,20,61,20,62,65,65,20,73,68,6f,75,6c,64,20,62,65,20,61,62,6c,65
  //   ,20,ba,48*0,ba,74,6f,20,66,6c,79,2e,20,49,74,73,20,77,69,6e,67
  //   ,73,20,61,72,65,20,74,6f,6f,20,73,6d,61,6c,6c,20,74,6f,20,67,65
  //   ,74,20,69,74,73,20,66,61,74,20,6c,69,74,74,6c,65,20,62,6f,64,79
  //   ,20,6f,66,66,20,74,68,65,20,67,72,6f,75,6e,64,2e,20,54,68,65,ba
  //   ,48*0,ba,20,62,65,65,2c,20,6f,66,20,63,6f,75,72,73,65,2c,20,66
  //   ,6c,69,65,73,20,61,6e,79,77,61,79,20,62,65,63,61,75,73,65,20,62
  //   ,65,65,73,20,64,6f,6e,27,74,20,63,61,72,65,20,77,68,61,74,20,68
  //   ,75,6d,61,6e,73,20,74,68,69,6e,6b,20,69,73,20,69,6d,70,ba,48*0
  //   ,ba,6f,73,73,69,62,6c,65,2e,20,59,65,6c,6c,6f,77,2c,20,62,6c,61
  //   ,63,6b,2e,20,59,65,6c,6c,6f,77,2c,20,62,6c,61,63,6b,2e,20,59,65
  //   ,6c,6c,6f,77,2c,20,62,6c,61,63,6b,2e,20,59,65,6c,6c,6f,77,2c,20
  //   ,62,6c,61,63,6b,2e,20,4f,6f,68,2c,20,62,6c,61,63,ba,48*0,ba,6b
  //   ,20,61,6e,64,20,79,65,6c,6c,6f,77,21,20,4c,65,74,27,73,20,73,68
  //   ,61,6b,65,20,69,74,20,75,70,20,61,20,6c,69,74,74,6c,65,2e,20,42
  //   ,61,72,72,79,21,20,42,72,65,61,6b,66,61,73,74,20,69,73,20,72,65
  //   ,61,64,79,21,20,4f,6f,6d,69,6e,67,21,20,48,ba,48*0,ba,61,6e,67
  //   ,20,6f,6e,20,61,20,73,65,63,6f,6e,64,2e,20,48,65,6c,6c,6f,3f,20
  //   ,2d,20,42,61,72,72,79,3f,20,2d,20,41,64,61,6d,3f,20,2d,20,4f,61
  //   ,6e,20,79,6f,75,20,62,65,6c,69,65,76,65,20,74,68,69,73,20,69,73
  //   ,20,68,61,70,70,65,6e,69,6e,67,3f,20,ba,48*0,ba,2d,20,49,20,63
  //   ,61,6e,27,74,2e,20,49,27,6c,6c,20,70,69,63,6b,20,79,6f,75,20,75
  //   ,70,2e,20,4c,6f,6f,6b,69,6e,67,20,73,68,61,72,70,2e,20,55,73,65
  //   ,20,74,68,65,20,73,74,61,69,72,73,2e,20,59,6f,75,72,20,66,61,74
  //   ,68,65,72,20,70,61,69,64,20,67,ba,48*0,ba,6f,6f,64,20,6d,6f,6e
  //   ,65,79,20,66,6f,72,20,74,68,6f,73,65,2e,20,53,6f,72,72,79,2e,20
  //   ,49,27,6d,20,65,78,63,69,74,65,64,2e,20,48,65,72,65,27,73,20,74
  //   ,68,65,20,67,72,61,64,75,61,74,65,2e,20,57,65,27,72,65,20,76,65
  //   ,72,79,20,70,72,6f,75,64,ba,48*0,ba,20,6f,66,20,79,6f,75,2c,20
  //   ,73,6f,6e,2e,20,41,20,70,65,72,66,65,63,74,20,72,65,70,6f,72,74
  //   ,20,63,61,72,64,2c,20,61,6c,6c,20,42,27,73,2e,20,56,65,72,79,20
  //   ,70,72,6f,75,64,2e,20,4d,61,21,20,49,20,67,6f,74,20,61,20,74,68
  //   ,69,6e,67,20,67,6f,ba,48*0,ba,69,6e,67,20,68,65,72,65,2e,20,2d
  //   ,20,59,6f,75,20,67,6f,74,20,6c,69,6e,74,20,6f,6e,20,79,6f,75,72
  //   ,20,66,75,7a,7a,2e,20,2d,20,4f,77,21,20,54,68,61,74,27,73,20,6d
  //   ,65,21,20,2d,20,57,61,76,65,20,74,6f,20,75,73,21,20,57,65,27,6c,6c
  //   ,20,62,65,ba,48*0,ba,20,69,6e,20,72,6f,77,20,31,31,38,2c,30,30,30
  //   ,2e,20,2d,20,42,79,65,21,20,42,61,72,72,79,2c,20,49,20,74,6f,6c
  //   ,64,20,79,6f,75,2c,20,73,74,6f,70,20,66,6c,79,69,6e,67,20,69,6e
  //   ,20,74,68,65,20,68,6f,75,73,65,21,20,2d,20,48,65,79,2c,20,41,64
  //   ,ba,48*0,ba,61,6d,2e,20,2d,20,48,65,79,2c,20,42,61,72,72,79,2e
  //   ,20,2d,20,49,73,20,74,68,61,74,20,66,75,7a,7a,20,67,65,6c,3f,20
  //   ,2d,20,41,20,6c,69,74,74,6c,65,2e,20,53,70,65,63,69,61,6c,20,64
  //   ,61,79,2c,20,67,72,61,64,75,61,74,69,6f,6e,2e,20,4e,65,76,ba,48*0
  //   ,ba,65,72,20,74,68,6f,75,67,68,74,20,49,27,64,20,6d,61,6b,65,20
  //   ,69,74,2e,20,54,68,72,65,65,20,64,61,79,73,20,67,72,61,64,65,20
  //   ,73,63,68,6f,6f,6c,2c,20,74,68,72,65,65,20,64,61,79,73,20,68,69
  //   ,67,68,20,73,63,68,6f,6f,6c,2e,20,54,68,6f,73,65,ba,48*0,ba,20
  //   ,77,65,72,65,20,61,77,6b,77,61,72,64,2e,20,54,68,72,65,65,20,64
  //   ,61,79,73,20,63,6f,6c,6c,65,67,65,2e,20,49,27,6d,20,67,6c,61,64
  //   ,20,49,20,74,6f,6f,6b,20,61,20,64,61,79,20,61,6e,64,20,68,69,74
  //   ,63,68,68,69,6b,65,64,20,61,72,6f,75,6e,64,ba,48*0,ba,20,74,68
  //   ,65,20,68,69,76,65,2e,20,59,6f,75,20,64,69,64,20,63,6f,6d,65,20
  //   ,62,61,63,6b,20,64,69,66,66,65,72,65,6e,74,2e,20,2d,20,48,69,2c
  //   ,20,42,61,72,72,79,2e,20,2d,20,41,72,74,69,65,2c,20,67,72,6f,77
  //   ,69,6e,67,20,61,20,6d,75,73,74,61,63,ba,48*0,ba,68,65,3f,20,4c
  //   ,6f,6f,6b,73,20,67,6f,6f,64,2e,20,2d,20,48,65,61,72,20,61,62,6f
  //   ,75,74,20,46,72,61,6e,6b,69,65,3f,20,2d,20,59,65,61,68,2e,20,2d
  //   ,20,59,6f,75,20,67,6f,69,6e,67,20,74,6f,20,74,68,65,20,66,75,6e
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  //   contents of color_mem (hex, n*v repeats v):
  //   80*f8,48*0,80*f8,48*0,80*f8,48*0,80*f8,48*0,80*f8,48*0,80*f8,48*0
  //   ,80*f8,48*0,80*f8,48*0,80*f8,48*0,80*f8,48*0,80*f8,48*0,80*f8
  //   ,48*0,80*f8,48*0,80*f8,48*0,80*f8,48*0,80*f8,48*0,80*f8,48*0,80*f8
  //   ,48*0,80*f8,48*0,80*f8,48*0,80*f8,48*0,80*f8,48*0,80*f8,48*0,80*f8
  //   ,48*0,80*f8,48*0,80*f8,48*0,80*f8,48*0,80*f8,48*0,80*f8,48*0,80*f8
endmodule

/* Code of horizontal:
module horizontal(
	input [6:0] char,
	output sync,
	output clr
);
	assign clr = char == 8'd99;
	assign sync = !(char >= 8'd82 && char < 8'd94);
endmodule
*/

/* Code of vertical:
module vertical(
	input [11:0] line,
	output sync,
	output clr
);
	assign clr = line == 524;
	assign sync = !(line >= 490 && line < 492);
endmodule
*/
