// Digital circuit new_gpu.dig as structural Verilog
module new_gpu (
  input  clk,
  input  rst,
  output [15:0] sprite_addr,
  output [15:0] addr_out,
  output [7:0] data_out
);

  wire _4bit_counter_sync_1_ovf, _4bit_counter_sync_2_ovf, _4bit_counter_sync_3_ovf,
       _4bit_counter_sync_5_ovf, _4bit_counter_sync_7_ovf, and_2_out, and_3_out, and_5_out, and_8_out,
       demultiplexer_1_out_0, demultiplexer_1_out_1, demultiplexer_1_out_2, demultiplexer_1_out_3,
       demultiplexer_1_out_4, demultiplexer_1_out_6, done, drawing, idle, jk_ff_1_nq, jk_ff_1_q, ld, ld_h,
       nand_1_out, nclk, next, nidle, not_3_out, not_4_out, not_5_out, nrst, or_1_out, or_2_out, store;
  wire [3:0] _4bit_counter_sync_4_out;
  wire [7:0] d_ff_1_q, d_ff_2_q, data;

  D_FF #(.Bits(8)) d_ff_1 (.D(sprite_addr[11:4]), .C(demultiplexer_1_out_4), .Q(d_ff_1_q));  // open: nQ
  assign data = not_3_out ? d_ff_1_q : 8'bz;  // Driver driver_1
  or or_1 (or_1_out, _4bit_counter_sync_1_ovf, ~demultiplexer_1_out_3);  // Or
  not not_1 (nrst, rst);
  not not_2 (nclk, clk);
  _4bit_counter_sync _4bit_counter_sync_1 (
    .in(4'b0000), .clk(clk), .nclr(nrst), .en(1'b1), .nld(ld), .cin(1'b1), .out(sprite_addr[3:0]),
    .ovf(_4bit_counter_sync_1_ovf));
  _4bit_counter_sync _4bit_counter_sync_2 (
    .in(data[3:0]), .clk(clk), .nclr(nrst), .en(1'b1), .nld(ld), .cin(or_1_out), .out(sprite_addr[7:4]),
    .ovf(_4bit_counter_sync_2_ovf));
  _4bit_counter_sync _4bit_counter_sync_3 (
    .in(data[7:4]), .clk(clk), .nclr(nrst), .en(1'b1), .nld(ld), .cin(_4bit_counter_sync_2_ovf),
    .out(sprite_addr[11:8]), .ovf(_4bit_counter_sync_3_ovf));
  _4bit_counter_sync _4bit_counter_sync_4 (
    .in(data[3:0]), .clk(clk), .nclr(nrst), .en(1'b1), .nld(ld_h), .cin(_4bit_counter_sync_3_ovf),
    .out(_4bit_counter_sync_4_out));  // open: ovf
  assign sprite_addr[15:12] = _4bit_counter_sync_4_out & {4{drawing}};  // And and_1, 4 bits wide
  EEPROMDualPort #(.AddrBits(16), .Bits(8)) eepromdualport_1 (
    .A(sprite_addr), .Din({8{1'b0}}), .str(1'b0), .C(1'b0), .ld(jk_ff_1_nq), .D(data));
  Demultiplexer #(.Selector_Bits(3), .Default(1)) demultiplexer_1 (
    .sel(sprite_addr[2:0]), .in(drawing), .out_0(demultiplexer_1_out_0), .out_1(demultiplexer_1_out_1),
    .out_2(demultiplexer_1_out_2), .out_3(demultiplexer_1_out_3), .out_4(demultiplexer_1_out_4),
    .out_5(ld_h), .out_6(demultiplexer_1_out_6));  // open: out_7
  not not_3 (not_3_out, jk_ff_1_nq);
  JK_FF_AS jk_ff_as_1 (
    .Set(1'b0), .J(~demultiplexer_1_out_6), .C(clk), .K(jk_ff_1_q), .Clr(rst), .Q(drawing));  // open: nQ
  JK_FF jk_ff_1 (.J(done), .C(clk), .K(jk_ff_1_q), .Q(jk_ff_1_q), .nQ(jk_ff_1_nq));
  nand nand_1 (nand_1_out, data[0], data[1], data[2], data[3], data[4], data[5], nidle, 1'b1);
  not not_4 (not_4_out, demultiplexer_1_out_2);
  and and_2 (and_2_out, data[0], not_4_out);
  and and_3 (and_3_out, ~demultiplexer_1_out_0, nclk);  // And
  and and_4 (ld, demultiplexer_1_out_6, jk_ff_1_nq);
  not not_5 (not_5_out, nand_1_out);
  JK_FF jk_ff_2 (.J(and_2_out), .C(clk), .K(rst), .Q(idle), .nQ(nidle));
  D_FF #(.Bits(8)) d_ff_2 (.D(data), .C(and_3_out), .Q(d_ff_2_q));  // open: nQ
  and and_5 (and_5_out, demultiplexer_1_out_1, ~next);  // And
  and and_6 (done, not_5_out, ~data[6], data[7]);  // And
  and and_7 (next, not_5_out, ~data[7], data[6]);  // And
  and and_8 (and_8_out, data[7], data[6]);
  or or_2 (or_2_out, and_8_out, nand_1_out);
  _4bit_counter_sync _4bit_counter_sync_5 (
    .in(d_ff_2_q[3:0]), .clk(clk), .nclr(1'b1), .en(drawing), .nld(and_5_out), .cin(1'b1),
    .out(addr_out[3:0]), .ovf(_4bit_counter_sync_5_ovf));
  _4bit_counter_sync _4bit_counter_sync_6 (
    .in(d_ff_2_q[7:4]), .clk(clk), .nclr(1'b1), .en(drawing), .nld(and_5_out),
    .cin(_4bit_counter_sync_5_ovf), .out(addr_out[7:4]));  // open: ovf
  _4bit_counter_sync _4bit_counter_sync_7 (
    .in(data[3:0]), .clk(clk), .nclr(1'b1), .en(next), .nld(demultiplexer_1_out_1), .cin(1'b1),
    .out(addr_out[11:8]), .ovf(_4bit_counter_sync_7_ovf));
  _4bit_counter_sync _4bit_counter_sync_8 (
    .in(data[7:4]), .clk(clk), .nclr(1'b1), .en(next), .nld(demultiplexer_1_out_1),
    .cin(_4bit_counter_sync_7_ovf), .out(addr_out[15:12]));  // open: ovf
  and and_9 (store, or_2_out, drawing, nidle, jk_ff_1_nq);
  RAMDualPort #(.AddrBits(16), .Bits(8)) ramdualport_1 (
    .A(addr_out), .Din(data), .str(store), .C(clk), .ld(1'b1), .D(data_out));

  // Notes on the sheet:
  //   clk: Hz: 3
  //   contents of eepromdualport_1 (hex, n*v repeats v):
  //   1,2,14*0,3,4,1,0,0,1,23,14*0,1,23,4619*0,7f,0,3f,0,ff,0,bf
endmodule
