// Digital circuit gpu.dig as structural Verilog
module gpu (
  input  clk,
  output [15:0] out_2
);

  wire _74138_1_pin11, _74138_1_pin12, _74138_1_pin13, _74138_1_pin14, Address_Offset_ovf, counter_2_ovf,
       nand_1_out, not_1_out, not_2_out, not_3_out, not_4_out, not_5_out, or_1_out, or_2_out, rs_ff_as_1_nq,
       rs_ff_as_1_q;
  wire [2:0] counter_2_out;
  wire [4:0] counter_1_out;
  wire [7:0] Address_Offset_out, and_1_out, multiplexer_1_out, Opcode_q, or_3_out, ramdualport_1_d, rom_1_d,
       Sprite_Width_q, X_endpoint_q;

  ROM #(.AddrBits(5), .Bits(8)) rom_1 (.A(counter_1_out), .sel(1'b1), .D(rom_1_d));
  Counter #(.Bits(5)) counter_1 (.en(1'b1), .C(clk), .clr(1'b0), .out(counter_1_out));  // open: ovf
  Counter #(.Bits(3)) counter_2 (.en(1'b1), .C(clk), .clr(not_5_out), .out(counter_2_out), .ovf(counter_2_ovf));
  RS_FF_AS rs_ff_as_1 (.S(not_5_out), .R(counter_2_ovf), .Q(rs_ff_as_1_q), .nQ(rs_ff_as_1_nq));
  _74138 _74138_1 (
    .pin1(counter_2_out[0]), .pin2(counter_2_out[1]), .pin3(counter_2_out[2]), .pin4(1'b0), .pin5(1'b0),
    .pin6(rs_ff_as_1_q), .pin8(1'b0), .pin11(_74138_1_pin11), .pin12(_74138_1_pin12), .pin13(_74138_1_pin13),
    .pin14(_74138_1_pin14), .pin16(1'b1));  // open: pin7, pin9, pin10, pin15
  not not_1 (not_1_out, _74138_1_pin14);
  not not_2 (not_2_out, _74138_1_pin13);
  D_FF #(.Bits(8)) Sprite_Width (.D(rom_1_d), .C(not_1_out), .Q(Sprite_Width_q));  // open: nQ
  D_FF #(.Bits(8)) X_endpoint (.D(rom_1_d), .C(not_2_out), .Q(X_endpoint_q));  // open: nQ
  not not_3 (not_3_out, _74138_1_pin12);
  D_FF #(.Bits(8)) Opcode (.D(rom_1_d), .C(not_4_out), .Q(Opcode_q));  // open: nQ
  not not_4 (not_4_out, _74138_1_pin11);
  or or_1 (or_1_out, not_2_out, Address_Offset_ovf);
  CounterPreset #(.Bits(8)) Address_Offset (
    .en(rs_ff_as_1_nq), .C(clk), .dir(1'b1), .in(Sprite_Width_q), .ld(or_1_out), .clr(1'b0),
    .out(Address_Offset_out), .ovf(Address_Offset_ovf));
  nand nand_1 (nand_1_out, rom_1_d[0], rom_1_d[1], rom_1_d[2], rom_1_d[3], rom_1_d[4], rom_1_d[5], rom_1_d[6], rom_1_d[7]);
  or or_2 (or_2_out, Address_Offset_ovf, not_3_out);
  not not_5 (not_5_out, nand_1_out);
  Add #(.Bits(8)) Address_7_0 (.a(X_endpoint_q), .b(Address_Offset_out), .c_i(1'b0), .s(out_2[7:0]));  // open: c_o
  assign or_3_out = rom_1_d | ramdualport_1_d;  // Or or_3, 8 bits wide
  assign and_1_out = rom_1_d & ramdualport_1_d;  // And and_1, 8 bits wide
  CounterPreset #(.Bits(8)) Address_15_8 (
    .en(or_2_out), .C(clk), .dir(1'b0), .in(rom_1_d), .ld(not_3_out), .clr(1'b0), .out(out_2[15:8]));  // open: ovf
  Multiplexer #(.Bits(8)) multiplexer_1 (.sel(Opcode_q[0]), .in_0(or_3_out), .in_1(and_1_out), .out(multiplexer_1_out));
  RAMDualPort #(.AddrBits(16), .Bits(8)) ramdualport_1 (
    .A(out_2), .Din(multiplexer_1_out), .str(rs_ff_as_1_nq), .C(clk), .ld(1'b1), .D(ramdualport_1_d));

  // Notes on the sheet:
  //   clk: Hz: 5
  //   contents of rom_1 (hex, n*v repeats v):
  //   ff,0,4,f0,a,0,0,0,ee,dd,cc,bb,aa,ee,dd,cc,bb,aa,10*ee,4*ff
endmodule
