// Digital circuit gpu74_old.dig as structural Verilog
module gpu74_old (
  input  clk,
  input  [15:0] in_3,
  output [15:0] out_1,
  output [7:0] out_4,
  output [15:0] out_5
);

  wire _74138_1_pin7, _74138_1_pin13, _74138_1_pin14, Address_15_8_ovf, Address_Offset_ovf, and_1_out,
       and_2_out, and_3_out, and_4_out, and_5_out, button_1_out, jk_ff_2_nq, load_3, load_4, load_5,
       nand_1_out, nand_2_out, nor_1_out, not_1_out, not_2_out, not_3_out, not_4_out, not_5_out, not_6_out,
       not_7_out, not_8_out, or_1_out, or_2_out, or_3_out;
  wire [1:0] jk_ff_1_q;
  wire [7:0] _8bit_register_1_q, _8bit_register_2_q, Address_Offset_out;
  wire [15:0] memory_ptr_1_out, sprite_ptr_1_out;

  Button button_1 (.out(button_1_out));
  or or_1 (or_1_out, jk_ff_1_q[1], jk_ff_2_nq);
  not not_1 (not_1_out, or_1_out);
  not not_2 (not_2_out, jk_ff_1_q[1]);
  and and_1 (and_1_out, nand_2_out, jk_ff_2_nq);
  JK_FF jk_ff_1 (.J(and_2_out), .C(clk), .K(button_1_out), .Q(jk_ff_1_q[1]));  // open: nQ
  sprite_ptr sprite_ptr_1 (
    .en0(jk_ff_1_q[0]), .clk(clk), .nclr0(not_1_out), .nclr1(not_2_out), .en1(1'b1), .out(sprite_ptr_1_out));
  nor nor_1 (nor_1_out, or_3_out, _74138_1_pin7);
  memory_ptr memory_ptr_1 (
    .in0(out_4), .en(and_1_out), .nld0(load_5), .in1(out_4), .clk(clk), .nld1(load_4), .out(memory_ptr_1_out));
  Multiplexer #(.Selector_Bits(2), .Bits(16)) multiplexer_1 (
    .sel(jk_ff_1_q), .in_0(memory_ptr_1_out), .in_1(sprite_ptr_1_out), .in_2(in_3), .in_3(in_3), .out(out_5));
  JK_FF jk_ff_2 (.J(or_3_out), .C(clk), .K(nor_1_out), .Q(jk_ff_1_q[0]), .nQ(jk_ff_2_nq));
  ROM #(.AddrBits(16), .Bits(8)) rom_1 (.A(out_5), .sel(1'b1), .D(out_4));
  _74138 _74138_1 (
    .pin1(sprite_ptr_1_out[0]), .pin2(sprite_ptr_1_out[1]), .pin3(sprite_ptr_1_out[2]), .pin4(1'b0),
    .pin5(1'b0), .pin6(jk_ff_1_q[0]), .pin7(_74138_1_pin7), .pin8(1'b0), .pin10(load_5), .pin11(load_4),
    .pin12(load_3), .pin13(_74138_1_pin13), .pin14(_74138_1_pin14), .pin16(1'b1));  // open: pin9, pin15
  not not_3 (not_3_out, _74138_1_pin14);
  not not_4 (not_4_out, _74138_1_pin13);
  _8bit_register _8bit_register_1 (.clk(clk), .D(out_4), .en(not_3_out), .Q(_8bit_register_1_q));
  _8bit_register _8bit_register_2 (.clk(clk), .D(out_4), .en(not_4_out), .Q(_8bit_register_2_q));
  or or_2 (or_2_out, not_4_out, Address_Offset_ovf);
  CounterPreset #(.Bits(8)) Address_Offset (
    .en(jk_ff_2_nq), .C(clk), .dir(1'b1), .in(_8bit_register_1_q), .ld(or_2_out), .clr(1'b0),
    .out(Address_Offset_out), .ovf(Address_Offset_ovf));
  and and_2 (and_2_out, Address_15_8_ovf, not_7_out);
  nand nand_1 (nand_1_out, not_5_out, out_4[1], out_4[2], out_4[3], out_4[4], out_4[5], out_4[6], out_4[7]);
  not not_5 (not_5_out, out_4[0]);
  not not_6 (not_6_out, load_3);
  nand nand_2 (nand_2_out, _8bit_register_1_q[0], _8bit_register_1_q[1], _8bit_register_1_q[2], _8bit_register_1_q[3], _8bit_register_1_q[4], _8bit_register_1_q[5], _8bit_register_1_q[6], _8bit_register_1_q[7]);
  or or_3 (or_3_out, Address_15_8_ovf, and_3_out);
  not not_7 (not_7_out, nand_1_out);
  Add #(.Bits(8)) Address_7_0 (
    .a(_8bit_register_2_q), .b(Address_Offset_out), .c_i(1'b0), .s(out_1[7:0]));  // open: c_o
  and and_3 (and_3_out, nand_2_out, not_7_out);
  CounterPreset #(.Bits(8)) Address_15_8 (
    .en(Address_Offset_ovf), .C(clk), .dir(1'b0), .in(out_4), .ld(not_6_out), .clr(1'b0), .out(out_1[15:8]),
    .ovf(Address_15_8_ovf));
  and and_4 (and_4_out, jk_ff_2_nq, out_4[0]);
  not not_8 (not_8_out, nand_2_out);
  and and_5 (and_5_out, not_8_out, not_7_out);
  RAMSinglePort #(.AddrBits(16), .Bits(8)) ramsingleport_1 (.A(out_1), .str(and_4_out), .C(clk), .ld(1'b0), .D(out_4));

  // Other names for the same wires on the sheet: data[7:0] = out_4

  // Notes on the sheet:
  //   clk: Hz: 30000
  //   contents of rom_1 (hex, n*v repeats v):
  //   fe,ff,0,0,0,40,0,0,0,1d,64,28,0,50,0,0,0,1d,32,3c,0,50,0,0,0,1d
  //   ,96,14,0,50,0,0,0,ff,0,0,0,41,26*0,27,fe,24*0,4*49,22*0,4*49,e1
  //   ,f5,f5,e1,49,22*0,49,e1,9b,9b,e1,e1,9b,9b,49,49,19*0,49,e1,e1,e1
  //   ,4*9b,e1,9b,9b,49,17*0,49,f5,e1,e1,4*9b,e1,e1,f5,9b,9b,49,15*0
  //   ,49,9b,f5,f5,9b,f5,e1,f5,e1,e1,f5,f5,f5,9b,49,15*0,49,e1,e1,e1
  //   ,7*f5,e1,e1,9b,49,16*0,49,9b,4*e1,49,e1,49,9b,9b,e1,9b,9b,49,14*0
  //   ,9b,49,9b,e1,e1,49,49,eb,49,eb,49,49,9b,e1,9b,49,14*0,49,0,49
  //   ,1,49,db,db,db,49,db,db,db,1,9b,9b,49,14*0,49,0,0,1,db,ff,1,eb
  //   ,db,1,ff,db,1,9b,49,18*0,1,db,ff,1,eb,eb,1,ff,db,1,9b,49,18*0
  //   ,1,db,6*eb,db,1,49,18*0,45,45,1,db,4*eb,db,1,45,45,17*0,45,ff
  //   ,ef,1,1,db,eb,eb,db,1,1,ff,ef,45,16*0,45,ef,ef,9f,9f,4*1,9f,45
  //   ,ef,ef,45,15*0,5*45,6*ef,9f,4*45,14*0,45,db,db,45,9f,9f,ef,ff,ff,ff
  //   ,ef,9f,45,81,db,45,14*0,45,45,81,1,45,9f,9f,ef,ef,ef,9f,45,1,81
  //   ,45,45,14*0,45,9f,45,0,1,45,4*9f,45,1,0,45,9f,45,14*0,45,45,45
  //   ,1,1,9f,4*45,9f,1,1,45,45,45,14*0,1,eb,eb,1,45,45,9f,ff,ef,9f
  //   ,45,45,1,eb,eb,1,14*0,1,db,db,1,81,81,4*45,81,81,1,db,db,1,15*0
  //   ,1,1,1,4*81,1,81,81,81,1,1,1,18*0,1,81,db,81,81,1,81,81,81,1,20*0
  //   ,1,4*81,1,81,81,81,1,21*0,1,81,81,81,1,81,81,1,22*0,1,81,81,81
  //   ,1,81,81,1,22*0,1,9f,81,81,1,81,81,1,22*0,1,ef,ef,9f,1,9f,9f,1
  //   ,23*0,7*1,584*0,fe
endmodule
