// Digital circuit gpu_v2.dig as structural Verilog
module gpu_v2 (
  input  clk,
  input  [15:0] in_3,
  output [15:0] out_1,
  output [6:0] out_4
);

  wire _74138_1_pin7, _74138_1_pin10, _74138_1_pin11, _74138_1_pin12, _74138_1_pin13, _74138_1_pin14,
       Address_15_8_ovf, Address_Offset_ovf, and_1_out, and_2_out, and_3_out, and_4_out, button_1_out,
       counter_1_ovf, counterpreset_1_ovf, nand_1_out, nand_2_out, nor_1_out, not_1_out, not_2_out,
       not_3_out, not_4_out, not_5_out, not_6_out, not_7_out, not_8_out, or_1_out, or_2_out, or_3_out,
       or_4_out, or_5_out, or_6_out, rs_ff_as_2_nq;
  wire [1:0] rs_ff_as_1_q;
  wire [2:0] counter_1_out;
  wire [7:0] Address_Offset_out, counterpreset_1_out, counterpreset_2_out, rom_1_d, Sprite_Width_q,
       X_endpoint_q;
  wire [11:0] counter_2_out;
  wire [15:0] multiplexer_1_out;

  Button button_1 (.out(button_1_out));
  or or_1 (or_1_out, rs_ff_as_1_q[1], rs_ff_as_2_nq);
  or or_2 (or_2_out, counter_1_ovf, rs_ff_as_1_q[1]);
  or or_3 (or_3_out, counterpreset_1_ovf, not_3_out);
  RS_FF_AS rs_ff_as_1 (.S(and_1_out), .R(button_1_out), .Q(rs_ff_as_1_q[1]));  // open: nQ
  CounterPreset #(.Bits(8)) counterpreset_1 (
    .en(nand_2_out), .C(clk), .dir(1'b0), .in(rom_1_d), .ld(not_4_out), .clr(1'b0),
    .out(counterpreset_1_out), .ovf(counterpreset_1_ovf));
  CounterPreset #(.Bits(8)) counterpreset_2 (
    .en(1'b1), .C(or_3_out), .dir(1'b0), .in(rom_1_d), .ld(not_3_out), .clr(1'b0), .out(counterpreset_2_out));  // open: ovf
  Counter #(.Bits(3)) counter_1 (
    .en(rs_ff_as_1_q[0]), .C(clk), .clr(or_1_out), .out(counter_1_out), .ovf(counter_1_ovf));
  Counter #(.Bits(12)) counter_2 (.en(1'b1), .C(or_2_out), .clr(rs_ff_as_1_q[1]), .out(counter_2_out));  // open: ovf
  nor nor_1 (nor_1_out, or_6_out, _74138_1_pin7);
  Multiplexer #(.Selector_Bits(2), .Bits(16)) multiplexer_1 (
    .sel(rs_ff_as_1_q), .in_0({counterpreset_2_out, counterpreset_1_out}),
    .in_1({1'b0, counter_2_out, counter_1_out}), .in_2(in_3), .in_3(in_3), .out(multiplexer_1_out));
  RS_FF_AS rs_ff_as_2 (.S(or_6_out), .R(nor_1_out), .Q(rs_ff_as_1_q[0]), .nQ(rs_ff_as_2_nq));
  ROM #(.AddrBits(16), .Bits(8)) rom_1 (.A(multiplexer_1_out), .sel(1'b1), .D(rom_1_d));
  _74138 _74138_1 (
    .pin1(counter_1_out[0]), .pin2(counter_1_out[1]), .pin3(counter_1_out[2]), .pin4(1'b0), .pin5(1'b0),
    .pin6(rs_ff_as_1_q[0]), .pin7(_74138_1_pin7), .pin8(1'b0), .pin10(_74138_1_pin10),
    .pin11(_74138_1_pin11), .pin12(_74138_1_pin12), .pin13(_74138_1_pin13), .pin14(_74138_1_pin14),
    .pin16(1'b1));  // open: pin9, pin15
  EEPROM eeprom_1 ();  // open: A, CS, WE, OE, D
  not not_1 (not_1_out, _74138_1_pin14);
  not not_2 (not_2_out, _74138_1_pin13);
  not not_3 (not_3_out, _74138_1_pin11);
  not not_4 (not_4_out, _74138_1_pin10);
  D_FF #(.Bits(8)) Sprite_Width (.D(rom_1_d), .C(not_1_out), .Q(Sprite_Width_q));  // open: nQ
  D_FF #(.Bits(8)) X_endpoint (.D(rom_1_d), .C(not_2_out), .Q(X_endpoint_q));  // open: nQ
  not not_5 (not_5_out, _74138_1_pin12);
  or or_4 (or_4_out, not_2_out, Address_Offset_ovf);
  CounterPreset #(.Bits(8)) Address_Offset (
    .en(rs_ff_as_2_nq), .C(clk), .dir(1'b1), .in(Sprite_Width_q), .ld(or_4_out), .clr(1'b0),
    .out(Address_Offset_out), .ovf(Address_Offset_ovf));
  and and_1 (and_1_out, Address_15_8_ovf, not_7_out);
  nand nand_1 (nand_1_out, not_6_out, rom_1_d[1], rom_1_d[2], rom_1_d[3], rom_1_d[4], rom_1_d[5], rom_1_d[6], rom_1_d[7]);
  not not_6 (not_6_out, rom_1_d[0]);
  nand nand_2 (nand_2_out, Sprite_Width_q[0], Sprite_Width_q[1], Sprite_Width_q[2], Sprite_Width_q[3], Sprite_Width_q[4], Sprite_Width_q[5], Sprite_Width_q[6], Sprite_Width_q[7]);
  or or_5 (or_5_out, Address_Offset_ovf, not_5_out);
  or or_6 (or_6_out, Address_15_8_ovf, and_2_out);
  not not_7 (not_7_out, nand_1_out);
  Add #(.Bits(8)) Address_7_0 (.a(X_endpoint_q), .b(Address_Offset_out), .c_i(1'b0), .s(out_1[7:0]));  // open: c_o
  and and_2 (and_2_out, nand_2_out, not_7_out);
  CounterPreset #(.Bits(8)) Address_15_8 (
    .en(or_5_out), .C(clk), .dir(1'b0), .in(rom_1_d), .ld(not_5_out), .clr(1'b0), .out(out_1[15:8]),
    .ovf(Address_15_8_ovf));
  Counter #(.Bits(7)) counter_3 (.en(1'b1), .C(not_7_out), .clr(1'b0), .out(out_4));  // open: ovf
  and and_3 (and_3_out, rs_ff_as_2_nq, rom_1_d[0]);
  not not_8 (not_8_out, nand_2_out);
  and and_4 (and_4_out, not_8_out, not_7_out);
  RAMSinglePort #(.AddrBits(16), .Bits(8)) ramsingleport_1 (
    .A(out_1), .str(and_3_out), .C(clk), .ld(1'b0), .D(rom_1_d));

  // Notes on the sheet:
  //   clk: Hz: 30000
  //   contents of rom_1 (hex, n*v repeats v):
  //   fe,ff,0,0,0,b0,0,0,0,2,10,4,0,ef,0,0,0,f,d0,a0,1,f,0,0,0,f,d5
  //   ,a5,1,f,0,0,0,f,78,1e,1,f,0,0,0,f,96,28,1,f,0,0,0,f,14,1e,1,f
  //   ,0,0,0,f,14,28,1,f,0,0,0,2,32,32,0,ef,0,0,0,ff,4*0,c0,97*0,51
  //   ,15*0,fe,48*0,ef,0,ef,ef,ef,0,ef,0,ff,12*0,4*af,11*0,6*af,10*0
  //   ,6*af,9*0,af,af,af,ef,ef,af,af,af,8*0,af,af,4*ef,af,af,8*0,af,af
  //   ,4*ef,af,af,8*0,af,af,af,ef,ef,af,af,af,9*0,6*af,10*0,6*af,11*0
  //   ,4*af,6*0,ff
endmodule
