// Digital circuit shift_reg.dig as structural Verilog
module shift_reg (
  input  sh_nld,
  input  clk,
  input  [7:0] in,
  output out
);

  _74166 _74166_1 (
    .pin1(1'b0), .pin2(in[0]), .pin3(in[1]), .pin4(in[2]), .pin5(in[3]), .pin6(1'b0), .pin7(clk),
    .pin8(1'b0), .pin9(1'b1), .pin10(in[4]), .pin11(in[5]), .pin12(in[6]), .pin13(out), .pin14(in[7]),
    .pin15(sh_nld), .pin16(1'b1));
endmodule
