// Digital circuit sprite_2024_realctr.dig as structural Verilog
module sprite_2024_realctr (
  input  clk,
  output hsync,
  output vsync,
  output [1:0] video_out,
  output [9:0] hpos,
  output [11:0] vpos,
  output [7:0] char_id,
  output [7:0] char_data,
  output vblank,
  output [1:0] debug_we
);

  wire _4bit_counter_1_ovf, _4bit_counter_3_ovf, _4bit_counter_4_ovf, not_2_out, not_3_out,
       u_horizontal_clr_n, u_vertical_clr_n;
  wire [3:0] _4bit_counter_6_out, ramasync_1_q, ramasync_2_q;

  _4bit_counter _4bit_counter_1 (
    .in(4'b0000), .clk(_4bit_counter_6_out[1]), .nclr(u_horizontal_clr_n), .en(1'b1), .nld(1'b1), .cin(1'b1),
    .out(hpos[5:2]), .ovf(_4bit_counter_1_ovf));
  _4bit_counter _4bit_counter_2 (
    .in(4'b0000), .clk(_4bit_counter_6_out[1]), .nclr(u_horizontal_clr_n), .en(1'b1), .nld(1'b1),
    .cin(_4bit_counter_1_ovf), .out(hpos[9:6]));  // open: ovf
  _4bit_counter _4bit_counter_3 (
    .in(4'b0000), .clk(u_horizontal_clr_n), .nclr(1'b1), .en(1'b1), .nld(u_vertical_clr_n), .cin(1'b1),
    .out(vpos[3:0]), .ovf(_4bit_counter_3_ovf));
  _4bit_counter _4bit_counter_4 (
    .in(4'b0000), .clk(u_horizontal_clr_n), .nclr(1'b1), .en(1'b1), .nld(u_vertical_clr_n),
    .cin(_4bit_counter_3_ovf), .out(vpos[7:4]), .ovf(_4bit_counter_4_ovf));
  _4bit_counter _4bit_counter_5 (
    .in(4'b0000), .clk(u_horizontal_clr_n), .nclr(1'b1), .en(1'b1), .nld(u_vertical_clr_n),
    .cin(_4bit_counter_4_ovf), .out(vpos[11:8]));  // open: ovf
  _4bit_counter _4bit_counter_6 (
    .in(4'b0000), .clk(clk), .nclr(1'b1), .en(1'b1), .nld(1'b1), .cin(1'b1), .out(_4bit_counter_6_out));  // open: ovf
  horizontal #(.applicationType("IVERILOG")) u_horizontal (
    .char(hpos[9:2]), .sync_n(hsync), .clr_n(u_horizontal_clr_n));
  vertical #(.applicationType("IVERILOG")) u_vertical (.line(vpos), .sync_n(vsync), .clr_n(u_vertical_clr_n));
  // Not not_1 has open pins: in=vsync, out=open
  ROM #(.AddrBits(13), .Bits(8)) u_char_data (.A({char_id, vpos[3:0], hpos[2]}), .sel(vsync), .D(char_data));
  ROM #(.AddrBits(12), .Bits(8)) video_mem (.A({vpos[8:4], hpos[9:3]}), .sel(1'b1), .D(char_id));
  Multiplexer #(.Selector_Bits(2), .Bits(2)) multiplexer_1 (
    .sel(_4bit_counter_6_out[1:0]), .in_0(char_data[3:2]), .in_1(char_data[1:0]), .in_2(char_data[7:6]),
    .in_3(char_data[5:4]), .out(video_out));
  not not_2 (not_2_out, vsync);
  not not_3 (not_3_out, vpos[9]);
  nand nand_1 (debug_we[0], char_id[0], not_2_out);
  nand nand_2 (debug_we[1], char_id[1], not_2_out);
  RAMAsync #(.AddrBits(4), .Bits(4)) ramasync_1 (
    .A({char_id[3:2], video_out}), .D(char_id[7:4]), .we(~debug_we[0]), .Q(ramasync_1_q));
  RAMAsync #(.AddrBits(4), .Bits(4)) ramasync_2 (
    .A({char_id[3:2], video_out}), .D(char_id[7:4]), .we(~debug_we[1]), .Q(ramasync_2_q));
  nand nand_3 (vblank, not_3_out, vsync);

  assign hpos[1:0] = 2'b00;

  // Notes on the sheet:
  //   clk: Hz: 100000
  //   contents of char_data (hex, n*v repeats v):
  //   36*0,26,64,80,1,44,22,80,1,40,2,89,91,42,42,80,1,40,2,19,98,12*0
  //   ,26,64,99,99,62,46,99,99,66,66,90,9,64,26,99,99,66,66,19,98,16*0
  //   ,24,60,99,98,66,64,99,98,66,64,19,90,6,40,1,17*0,2,0,9,80,26,60
  //   ,99,98,26,60,9,80,2,17*0,1,80,6,60,9,90,64,26,98,19,64,26,1,80
  //   ,2,40,9,90,14*0,1,80,6,60,19,98,66,66,99,99,26,64,1,80,2,40,9
  //   ,90,20*0,2,40,9,90,6,60,1,80,12*0,66,66,99,99,66,66,99,99,66,66
  //   ,99,99,64,26,90,9,60,6,98,19,66,66,99,99,66,66,99,99,66,66,99,99
  //   ,10*0,9,90,24,24,10,8,20,4,18,18,6,60,10*0,66,66,99,99,66,66,99,99
  //   ,66,66,90,9,42,42,89,91,46,62,81,81,60,6,99,99,66,66,99,99,66,66
  //   ,99,99,4*0,2,64,0,98,2,44,9,8,26,40,90,90,60,60,90,90,60,60,19
  //   ,80,12*0,6,60,18,18,24,24,18,18,24,24,9,90,2,40,19,98,2,40,1,80
  //   ,12*0,6,66,9,9,6,66,9,0,6,0,9,0,6,0,19,0,66,0,98,13*0,26,66,18
  //   ,9,26,66,18,9,24,6,18,9,24,6,18,19,64,26,98,18,60,13*0,1,80,2
  //   ,40,91,89,6,60,98,19,6,60,91,89,2,40,1,80,10*0,80,0,60,0,98,0
  //   ,66,0,99,80,66,64,99,80,66,0,98,0,60,0,80,12*0,8,0,24,0,98,2,64
  //   ,9,98,66,64,9,98,2,64,0,98,0,24,0,8,12*0,2,40,9,90,26,64,1,80
  //   ,2,40,1,80,26,64,9,90,2,40,14*0,24,24,18,18,24,24,18,18,24,24
  //   ,18,18,24,24,0,0,24,24,18,18,12*0,26,66,91,89,62,46,91,89,26,46
  //   ,1,89,2,46,1,89,2,46,1,89,10*0,19,90,60,24,18,0,6,40,18,90,60
  //   ,24,90,18,24,60,9,80,0,60,90,18,26,60,22*0,66,64,99,98,66,64,99
  //   ,98,12*0,2,40,9,90,26,64,1,80,2,40,1,80,26,64,9,90,2,40,19,98
  //   ,12*0,2,40,9,90,26,64,1,80,2,40,1,80,2,40,1,80,2,40,1,80,12*0
  //   ,2,40,1,80,2,40,1,80,2,40,1,80,2,40,19,98,6,60,1,80,18*0,1,80
  //   ,0,60,99,98,0,60,1,80,22*0,9,0,24,0,99,98,24,0,9,25*0,60,0,90
  //   ,0,60,0,99,98,22*0,8,10,24,24,99,99,24,24,8,10,20*0,2,0,9,80,6
  //   ,40,19,90,26,60,99,98,66,64,18*0,66,64,99,98,26,60,19,90,6,40
  //   ,9,80,2,47*0,2,40,9,90,6,60,9,90,2,40,1,80,2,40,0,0,2,40,1,80
  //   ,10*0,18,18,24,24,18,18,4,20,28*0,18,90,24,60,99,98,24,60,18,90
  //   ,24,60,99,98,24,60,18,90,8*0,2,40,1,80,26,60,90,18,60,4,90,0,26
  //   ,60,0,18,0,24,80,18,60,24,19,90,2,40,1,80,12*0,60,4,90,18,0,60
  //   ,1,80,6,0,18,0,60,24,80,18,12*0,6,40,18,90,24,60,9,80,26,24,91
  //   ,90,60,60,90,90,60,60,19,18,10*0,9,0,6,0,9,0,24,28*0,60,1,80,6
  //   ,0,9,0,6,0,9,0,6,0,9,0,2,40,0,90,12*0,6,0,1,80,0,60,0,90,0,60
  //   ,0,90,0,60,0,90,2,40,9,19*0,18,18,6,60,99,99,6,60,18,18,22*0,1
  //   ,80,2,40,19,98,2,40,1,80,30*0,1,80,2,40,1,80,6,21*0,99,98,36*0
  //   ,2,40,1,80,17*0,4,0,18,0,60,1,80,6,0,18,0,60,0,80,13*0,6,60,18,18
  //   ,60,6,90,9,62,46,91,89,60,6,90,9,24,24,9,90,12*0,2,40,9,80,26
  //   ,40,1,80,2,40,1,80,2,40,1,80,2,40,19,98,12*0,26,60,90,18,0,24
  //   ,0,90,2,40,9,0,24,0,90,0,60,24,99,98,12*0,26,60,90,18,0,24,0,18
  //   ,6,60,0,18,0,24,0,18,60,24,19,90,13*0,60,1,90,6,60,18,90,60,60
  //   ,99,98,0,60,0,90,0,60,1,98,12*0,66,64,90,0,60,0,90,0,66,60,0,18
  //   ,0,24,0,18,60,24,19,90,12*0,6,40,18,0,60,0,90,0,66,60,90,18,60
  //   ,24,90,18,60,24,19,90,12*0,66,64,90,18,0,24,0,18,0,60,1,80,6,0
  //   ,9,0,6,0,9,13*0,26,60,90,18,60,24,90,18,26,60,90,18,60,24,90,18
  //   ,60,24,19,90,12*0,26,60,90,18,60,24,90,18,26,64,0,18,0,24,0,18
  //   ,0,60,19,80,16*0,2,40,1,80,6*0,1,80,2,40,18*0,2,40,1,80,6*0,1
  //   ,80,2,40,9,16*0,18,0,60,1,80,6,0,18,0,6,0,1,80,0,60,0,18,18*0
  //   ,19,98,4*0,26,64,20*0,18,0,6,0,1,80,0,60,0,18,0,60,1,80,6,0,18
  //   ,13*0,26,60,90,18,60,24,0,90,2,40,1,80,2,40,0,0,2,40,1,80,14*0
  //   ,19,90,60,24,90,18,62,64,91,98,62,64,91,90,60,0,19,90,12*0,2,0
  //   ,9,80,24,60,90,18,60,24,99,98,60,24,90,18,60,24,90,18,12*0,66
  //   ,60,18,18,24,24,18,18,26,60,18,18,24,24,18,18,24,24,99,90,12*0
  //   ,6,60,18,18,60,4,90,0,60,0,90,0,60,0,90,8,24,24,9,90,12*0,66,40
  //   ,18,90,24,24,18,18,24,24,18,18,24,24,18,18,24,60,99,80,12*0,66
  //   ,64,18,18,24,4,18,80,26,40,18,80,24,0,18,8,24,24,99,98,12*0,66
  //   ,64,18,18,24,4,18,80,26,40,18,80,24,0,18,0,24,0,99,13*0,6,60,18,18
  //   ,60,4,90,0,60,0,91,98,60,24,90,18,24,24,9,88,12*0,60,24,90,18
  //   ,60,24,90,18,66,64,90,18,60,24,90,18,60,24,90,18,12*0,6,60,1,80
  //   ,2,40,1,80,2,40,1,80,2,40,1,80,2,40,9,90,12*0,2,64,0,90,0,60,0
  //   ,90,0,60,0,90,60,60,90,90,60,60,19,80,12*0,64,24,18,18,24,24,18
  //   ,90,26,40,19,80,24,60,18,18,24,24,98,18,12*0,66,0,18,0,24,0,18
  //   ,0,24,0,18,0,24,0,18,8,24,24,99,98,12*0,60,6,98,19,66,66,99,99
  //   ,62,46,90,9,60,6,90,9,60,6,90,9,12*0,60,24,98,18,66,24,99,98,62
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  //   contents of video_mem (hex, n*v repeats v):
  //   c9,78*cd,bb,48*0,ba,41,63,63,6f,72,64,69,6e,67,20,74,6f,20,61
  //   ,6c,6c,20,6b,6e,6f,77,6e,20,6c,61,77,73,20,6f,66,20,61,76,69,61
  //   ,74,69,6f,6e,2c,20,74,68,65,72,65,20,69,73,20,6e,6f,20,77,61,79
  //   ,20,61,20,62,65,65,20,73,68,6f,75,6c,64,20,62,65,20,61,62,6c,65
  //   ,20,ba,48*0,ba,74,6f,20,66,6c,79,2e,20,49,74,73,20,77,69,6e,67
  //   ,73,20,61,72,65,20,74,6f,6f,20,73,6d,61,6c,6c,20,74,6f,20,67,65
  //   ,74,20,69,74,73,20,66,61,74,20,6c,69,74,74,6c,65,20,62,6f,64,79
  //   ,20,6f,66,66,20,74,68,65,20,67,72,6f,75,6e,64,2e,20,54,68,65,ba
  //   ,48*0,ba,20,62,65,65,2c,20,6f,66,20,63,6f,75,72,73,65,2c,20,66
  //   ,6c,69,65,73,20,61,6e,79,77,61,79,20,62,65,63,61,75,73,65,20,62
  //   ,65,65,73,20,64,6f,6e,27,74,20,63,61,72,65,20,77,68,61,74,20,68
  //   ,75,6d,61,6e,73,20,74,68,69,6e,6b,20,69,73,20,69,6d,70,ba,48*0
  //   ,ba,6f,73,73,69,62,6c,65,2e,20,59,65,6c,6c,6f,77,2c,20,62,6c,61
  //   ,63,6b,2e,20,59,65,6c,6c,6f,77,2c,20,62,6c,61,63,6b,2e,20,59,65
  //   ,6c,6c,6f,77,2c,20,62,6c,61,63,6b,2e,20,59,65,6c,6c,6f,77,2c,20
  //   ,62,6c,61,63,6b,2e,20,4f,6f,68,2c,20,62,6c,61,63,ba,48*0,ba,6b
  //   ,20,61,6e,64,20,79,65,6c,6c,6f,77,21,20,4c,65,74,27,73,20,73,68
  //   ,61,6b,65,20,69,74,20,75,70,20,61,20,6c,69,74,74,6c,65,2e,20,42
  //   ,61,72,72,79,21,20,42,72,65,61,6b,66,61,73,74,20,69,73,20,72,65
  //   ,61,64,79,21,20,4f,6f,6d,69,6e,67,21,20,48,ba,48*0,ba,61,6e,67
  //   ,20,6f,6e,20,61,20,73,65,63,6f,6e,64,2e,20,48,65,6c,6c,6f,3f,20
  //   ,2d,20,42,61,72,72,79,3f,20,2d,20,41,64,61,6d,3f,20,2d,20,4f,61
  //   ,6e,20,79,6f,75,20,62,65,6c,69,65,76,65,20,74,68,69,73,20,69,73
  //   ,20,68,61,70,70,65,6e,69,6e,67,3f,20,ba,48*0,ba,2d,20,49,20,63
  //   ,61,6e,27,74,2e,20,49,27,6c,6c,20,70,69,63,6b,20,79,6f,75,20,75
  //   ,70,2e,20,4c,6f,6f,6b,69,6e,67,20,73,68,61,72,70,2e,20,55,73,65
  //   ,20,74,68,65,20,73,74,61,69,72,73,2e,20,59,6f,75,72,20,66,61,74
  //   ,68,65,72,20,70,61,69,64,20,67,ba,48*0,ba,6f,6f,64,20,6d,6f,6e
  //   ,65,79,20,66,6f,72,20,74,68,6f,73,65,2e,20,53,6f,72,72,79,2e,20
  //   ,49,27,6d,20,65,78,63,69,74,65,64,2e,20,48,65,72,65,27,73,20,74
  //   ,68,65,20,67,72,61,64,75,61,74,65,2e,20,57,65,27,72,65,20,76,65
  //   ,72,79,20,70,72,6f,75,64,ba,48*0,ba,20,6f,66,20,79,6f,75,2c,20
  //   ,73,6f,6e,2e,20,41,20,70,65,72,66,65,63,74,20,72,65,70,6f,72,74
  //   ,20,63,61,72,64,2c,20,61,6c,6c,20,42,27,73,2e,20,56,65,72,79,20
  //   ,70,72,6f,75,64,2e,20,4d,61,21,20,49,20,67,6f,74,20,61,20,74,68
  //   ,69,6e,67,20,67,6f,ba,48*0,ba,69,6e,67,20,68,65,72,65,2e,20,2d
  //   ,20,59,6f,75,20,67,6f,74,20,6c,69,6e,74,20,6f,6e,20,79,6f,75,72
  //   ,20,66,75,7a,7a,2e,20,2d,20,4f,77,21,20,54,68,61,74,27,73,20,6d
  //   ,65,21,20,2d,20,57,61,76,65,20,74,6f,20,75,73,21,20,57,65,27,6c,6c
  //   ,20,62,65,ba,48*0,ba,20,69,6e,20,72,6f,77,20,31,31,38,2c,30,30,30
  //   ,2e,20,2d,20,42,79,65,21,20,42,61,72,72,79,2c,20,49,20,74,6f,6c
  //   ,64,20,79,6f,75,2c,20,73,74,6f,70,20,66,6c,79,69,6e,67,20,69,6e
  //   ,20,74,68,65,20,68,6f,75,73,65,21,20,2d,20,48,65,79,2c,20,41,64
  //   ,ba,48*0,ba,61,6d,2e,20,2d,20,48,65,79,2c,20,42,61,72,72,79,2e
  //   ,20,2d,20,49,73,20,74,68,61,74,20,66,75,7a,7a,20,67,65,6c,3f,20
  //   ,2d,20,41,20,6c,69,74,74,6c,65,2e,20,53,70,65,63,69,61,6c,20,64
  //   ,61,79,2c,20,67,72,61,64,75,61,74,69,6f,6e,2e,20,4e,65,76,ba,48*0
  //   ,ba,65,72,20,74,68,6f,75,67,68,74,20,49,27,64,20,6d,61,6b,65,20
  //   ,69,74,2e,20,54,68,72,65,65,20,64,61,79,73,20,67,72,61,64,65,20
  //   ,73,63,68,6f,6f,6c,2c,20,74,68,72,65,65,20,64,61,79,73,20,68,69
  //   ,67,68,20,73,63,68,6f,6f,6c,2e,20,54,68,6f,73,65,ba,48*0,ba,20
  //   ,77,65,72,65,20,61,77,6b,77,61,72,64,2e,20,54,68,72,65,65,20,64
  //   ,61,79,73,20,63,6f,6c,6c,65,67,65,2e,20,49,27,6d,20,67,6c,61,64
  //   ,20,49,20,74,6f,6f,6b,20,61,20,64,61,79,20,61,6e,64,20,68,69,74
  //   ,63,68,68,69,6b,65,64,20,61,72,6f,75,6e,64,ba,48*0,ba,0,1,2,3
  //   ,4,5,6,7,8,9,a,b,c,d,e,f,10,11,12,13,14,15,16,17,18,19,1a,1b,1c
  //   ,1d,1e,1f,20,21,22,23,24,25,26,27,28,29,2a,2b,2c,2d,2e,2f,30,31
  //   ,32,33,34,35,36,37,38,39,3a,3b,3c,3d,3e,3f,40,41,42,43,44,45,46
  //   ,47,48,49,4a,4b,4c,4d,ba,48*0,ba,4e,4f,50,51,52,53,54,55,56,57
  //   ,58,59,5a,5b,5c,5d,5e,5f,60,61,62,63,64,65,66,67,68,69,6a,6b,6c
  //   ,6d,6e,6f,70,71,72,73,74,75,76,77,78,79,7a,7b,7c,7d,7e,7f,80,81
  //   ,82,83,84,85,86,87,88,89,8a,8b,8c,8d,8e,8f,90,91,92,93,94,95,96
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endmodule

/* Code of horizontal:
module horizontal(
	input [7:0] char,
	output sync_n,
	output clr_n
);
	assign clr_n = ~(char == 8'd199);
	assign sync_n = ~(char >= 8'd164 && char < 8'd188);
endmodule
*/

/* Code of vertical:
module vertical(
	input [11:0] line,
	output sync_n,
	output clr_n
);
	assign clr_n = ~(line == 524);
	assign sync_n = ~(line >= 490 && line < 492);
endmodule
*/
