// Digital circuit state_char.dig as structural Verilog
module state_char (
  input  [7:0] D,
  input  drawing,
  input  clk,
  input  reset,
  output next,
  output done,
  output send,
  output fill
);

  wire and_1_out, and_4_out, jk_ff_1_nq, not_1_out, not_2_out;

  not not_1 (not_1_out, D[0]);
  and and_1 (and_1_out, not_1_out, jk_ff_1_nq);
  and and_2 (next, and_1_out, D[3], D[1]);
  and and_3 (done, and_1_out, D[3], D[2], drawing);
  and and_4 (and_4_out, and_1_out, D[3], D[4], drawing);
  not not_2 (not_2_out, D[3]);
  and and_5 (fill, and_1_out, not_2_out);
  JK_FF jk_ff_1 (.J(and_4_out), .C(clk), .K(reset), .Q(send), .nQ(jk_ff_1_nq));
endmodule
