// Digital circuit textgen.dig as structural Verilog
module textgen (
  input  clk,
  output video_out,
  output [7:0] reg1,
  output [7:0] reg0_debug,
  output hsync,
  output [11:0] line,
  output vsync,
  output [6:0] char
);

  wire counter_1_ovf, counter_3_ovf, counter_4_ovf, nclk, nor_1_out, not_2_out, u_horizontal_clr,
       u_vertical_clr;
  wire [0:0] counter_6_out_2;
  wire [3:0] counter_6_out;
  wire [3:3] counter_2_out;
  wire [7:0] char_rom_d, register_2_q, text_rom_d;

  Counter #(.Bits(4)) counter_1 (
    .en(1'b1), .C(counter_6_out_2[0]), .clr(u_horizontal_clr), .out(char[3:0]), .ovf(counter_1_ovf));
  Counter #(.Bits(4)) counter_2 (
    .en(counter_1_ovf), .C(counter_6_out_2[0]), .clr(u_horizontal_clr), .out({counter_2_out[3], char[6:4]}));  // open: ovf
  Counter #(.Bits(4)) counter_3 (
    .en(u_horizontal_clr), .C(counter_6_out_2[0]), .clr(1'b0), .out(line[3:0]), .ovf(counter_3_ovf));
  Counter #(.Bits(4)) counter_4 (
    .en(counter_3_ovf), .C(counter_6_out_2[0]), .clr(u_vertical_clr), .out(line[7:4]), .ovf(counter_4_ovf));
  Counter #(.Bits(4)) counter_5 (
    .en(counter_4_ovf), .C(counter_6_out_2[0]), .clr(u_vertical_clr), .out(line[11:8]));  // open: ovf
  not not_1 (nclk, clk);
  Counter #(.Bits(4)) counter_6 (
    .en(1'b1), .C(clk), .clr(1'b0), .out({counter_6_out[3], counter_6_out_2[0], counter_6_out[1:0]}));  // open: ovf
  nor nor_1 (nor_1_out, counter_6_out[0], counter_6_out[1], counter_6_out_2[0]);
  horizontal #(.applicationType("IVERILOG")) u_horizontal (.char(char), .sync(hsync), .clr(u_horizontal_clr));
  not not_2 (not_2_out, nor_1_out);
  ROM #(.AddrBits(12), .Bits(8)) text_rom (.A({char_rom_d, line[3:0]}), .sel(1'b1), .D(text_rom_d));
  vertical #(.applicationType("IVERILOG")) u_vertical (.line(line), .sync(vsync), .clr(u_vertical_clr));
  Register #(.Bits(8)) register_1 (.D(text_rom_d), .C(nclk), .en(nor_1_out), .Q(reg0_debug));
  shift_reg shift_reg_1 (.sh_nld(not_2_out), .clk(nclk), .in(text_rom_d), .out(video_out));
  Register #(.Bits(8)) register_2 (.D(char_rom_d), .C(counter_6_out[1]), .en(counter_6_out_2[0]), .Q(register_2_q));
  ROM #(.AddrBits(13), .Bits(8)) char_rom (.A({line[8:4], char, counter_6_out_2[0]}), .sel(1'b1), .D(char_rom_d));
  Register #(.Bits(8)) register_3 (.D(register_2_q), .C(nclk), .en(nor_1_out), .Q(reg1));

  // Notes on the sheet:
  //   clk: Hz: 100
  //   contents of text_rom (hex, n*v repeats v):
  //   18*0,7e,81,a5,81,81,bd,99,81,81,7e,6*0,7e,ff,db,ff,ff,c3,e7,ff,ff
  //   ,7e,8*0,6c,4*fe,7c,38,10,8*0,10,38,7c,fe,7c,38,10,8*0,18,3c,3c
  //   ,e7,e7,e7,18,18,3c,7*0,18,3c,7e,ff,ff,7e,18,18,3c,10*0,18,3c,3c
  //   ,18,6*0,6*ff,e7,c3,c3,e7,6*ff,5*0,3c,66,42,42,66,3c,5*0,5*ff,c3
  //   ,99,bd,bd,99,c3,5*ff,0,0,1e,e,1a,32,78,4*cc,78,6*0,3c,4*66,3c
  //   ,18,7e,18,18,6*0,3f,33,3f,4*30,70,f0,e0,6*0,7f,63,7f,4*63,67,e7
  //   ,e6,c0,6*0,18,18,db,3c,e7,3c,db,18,18,5*0,80,c0,e0,f0,f8,fe,f8
  //   ,f0,e0,c0,80,5*0,2,6,e,1e,3e,fe,3e,1e,e,6,2,6*0,18,3c,7e,18,18,18
  //   ,7e,3c,18,7*0,7*66,0,66,66,6*0,7f,db,db,db,7b,5*1b,5*0,7c,c6,60
  //   ,38,6c,c6,c6,6c,38,c,c6,7c,11*0,4*fe,6*0,18,3c,7e,18,18,18,7e
  //   ,3c,18,7e,6*0,18,3c,7e,7*18,6*0,7*18,7e,3c,18,9*0,18,c,fe,c,18
  //   ,11*0,30,60,fe,60,30,12*0,c0,c0,c0,fe,11*0,24,66,ff,66,24,10*0
  //   ,10,38,38,7c,7c,fe,fe,9*0,fe,fe,7c,7c,38,38,10,23*0,18,3c,3c,3c
  //   ,18,18,18,0,18,18,5*0,66,66,66,24,14*0,6c,6c,fe,6c,6c,6c,fe,6c,6c
  //   ,4*0,18,18,7c,c6,c2,c0,7c,6,6,86,c6,7c,18,18,6*0,c2,c6,c,18,30
  //   ,60,c6,86,6*0,38,6c,6c,38,76,dc,cc,cc,cc,76,5*0,30,30,30,60,13*0
  //   ,c,18,6*30,18,c,6*0,30,18,6*c,18,30,9*0,66,3c,ff,3c,66,11*0,18,18
  //   ,7e,18,18,15*0,18,18,18,30,10*0,fe,18*0,18,18,8*0,2,6,c,18,30
  //   ,60,c0,80,6*0,3c,66,c3,c3,db,db,c3,c3,66,3c,6*0,18,38,78,6*18
  //   ,7e,6*0,7c,c6,6,c,18,30,60,c0,c6,fe,6*0,7c,c6,6,6,3c,6,6,6,c6
  //   ,7c,6*0,c,1c,3c,6c,cc,fe,c,c,c,1e,6*0,fe,c0,c0,c0,fc,6,6,6,c6
  //   ,7c,6*0,38,60,c0,c0,fc,4*c6,7c,6*0,fe,c6,6,6,c,18,4*30,6*0,7c
  //   ,c6,c6,c6,7c,4*c6,7c,6*0,7c,c6,c6,c6,7e,6,6,6,c,78,8*0,18,18,0,0,0
  //   ,18,18,9*0,18,18,0,0,0,18,18,30,7*0,6,c,18,30,60,30,18,c,6,9*0
  //   ,7e,0,0,7e,10*0,60,30,18,c,6,c,18,30,60,6*0,7c,c6,c6,c,18,18,18
  //   ,0,18,18,7*0,7c,c6,c6,de,de,de,dc,c0,7c,6*0,10,38,6c,c6,c6,fe
  //   ,4*c6,6*0,fc,66,66,66,7c,4*66,fc,6*0,3c,66,c2,4*c0,c2,66,3c,6*0
  //   ,f8,6c,6*66,6c,f8,6*0,fe,66,62,68,78,68,60,62,66,fe,6*0,fe,66
  //   ,62,68,78,68,60,60,60,f0,6*0,3c,66,c2,c0,c0,de,c6,c6,66,3a,6*0
  //   ,4*c6,fe,5*c6,6*0,3c,8*18,3c,6*0,1e,5*c,cc,cc,cc,78,6*0,e6,66,66
  //   ,6c,78,78,6c,66,66,e6,6*0,f0,6*60,62,66,fe,6*0,c3,e7,ff,ff,db
  //   ,5*c3,6*0,c6,e6,f6,fe,de,ce,4*c6,6*0,7c,8*c6,7c,6*0,fc,66,66,66
  //   ,7c,4*60,f0,6*0,7c,6*c6,d6,de,7c,c,e,4*0,fc,66,66,66,7c,6c,66,66,66
  //   ,e6,6*0,7c,c6,c6,60,38,c,6,c6,c6,7c,6*0,ff,db,99,6*18,3c,6*0,9*c6
  //   ,7c,6*0,7*c3,66,3c,18,6*0,5*c3,db,db,ff,66,66,6*0,c3,c3,66,3c
  //   ,18,18,3c,66,c3,c3,6*0,c3,c3,c3,66,3c,4*18,3c,6*0,ff,c3,86,c,18
  //   ,30,60,c1,c3,ff,6*0,3c,8*30,3c,7*0,80,c0,e0,70,38,1c,e,6,2,6*0
  //   ,3c,8*c,3c,4*0,10,38,6c,c6,25*0,ff,0,0,30,30,18,18*0,78,c,7c,cc,cc,cc
  //   ,76,6*0,e0,60,60,78,6c,4*66,7c,9*0,7c,c6,c0,c0,c0,c6,7c,6*0,1c
  //   ,c,c,3c,6c,4*cc,76,9*0,7c,c6,fe,c0,c0,c6,7c,6*0,38,6c,64,60,f0
  //   ,4*60,f0,9*0,76,5*cc,7c,c,cc,78,0,0,0,e0,60,60,6c,76,4*66,e6,6*0
  //   ,18,18,0,38,5*18,3c,6*0,6,6,0,e,6*6,66,66,3c,0,0,0,e0,60,60,66
  //   ,6c,78,78,6c,66,e6,6*0,38,8*18,3c,9*0,e6,ff,5*db,9*0,dc,6*66,9*0
  //   ,7c,5*c6,7c,9*0,dc,5*66,7c,60,60,f0,6*0,76,5*cc,7c,c,c,1e,6*0
  //   ,dc,76,66,60,60,60,f0,9*0,7c,c6,60,38,c,c6,7c,6*0,10,30,30,fc
  //   ,4*30,36,1c,9*0,6*cc,76,9*0,4*c3,66,3c,18,9*0,c3,c3,c3,db,db,ff
  //   ,66,9*0,c3,66,3c,18,3c,66,c3,9*0,6*c6,7e,6,c,f8,6*0,fe,cc,18,30
  //   ,60,c6,fe,6*0,e,18,18,18,70,4*18,e,6*0,4*18,0,5*18,6*0,70,18,18,18
  //   ,e,4*18,70,6*0,76,dc,16*0,10,38,6c,c6,c6,c6,fe,7*0,3c,66,c2,c0,c0,c0
  //   ,c2,66,3c,c,6,7c,4*0,cc,0,0,6*cc,76,5*0,c,18,30,0,7c,c6,fe,c0,c0
  //   ,c6,7c,5*0,10,38,6c,0,78,c,7c,cc,cc,cc,76,6*0,cc,0,0,78,c,7c,cc,cc,cc
  //   ,76,5*0,60,30,18,0,78,c,7c,cc,cc,cc,76,5*0,38,6c,38,0,78,c,7c
  //   ,cc,cc,cc,76,8*0,3c,66,60,60,66,3c,c,6,3c,4*0,10,38,6c,0,7c,c6
  //   ,fe,c0,c0,c6,7c,6*0,c6,0,0,7c,c6,fe,c0,c0,c6,7c,5*0,60,30,18,0
  //   ,7c,c6,fe,c0,c0,c6,7c,6*0,66,0,0,38,5*18,3c,5*0,18,3c,66,0,38
  //   ,5*18,3c,5*0,60,30,18,0,38,5*18,3c,5*0,c6,0,10,38,6c,c6,c6,fe
  //   ,c6,c6,c6,4*0,38,6c,38,0,38,6c,c6,c6,fe,c6,c6,c6,4*0,18,30,60
  //   ,0,fe,66,60,7c,60,60,66,fe,9*0,6e,3b,1b,7e,d8,dc,77,6*0,3e,6c
  //   ,cc,cc,fe,4*cc,ce,5*0,10,38,6c,0,7c,5*c6,7c,6*0,c6,0,0,7c,5*c6
  //   ,7c,5*0,60,30,18,0,7c,5*c6,7c,5*0,30,78,cc,0,6*cc,76,5*0,60,30
  //   ,18,0,6*cc,76,6*0,c6,0,0,6*c6,7e,6,c,78,0,0,c6,0,7c,7*c6,7c,5*0
  //   ,c6,0,8*c6,7c,5*0,18,18,7e,c3,c0,c0,c0,c3,7e,18,18,5*0,38,6c,64
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  //   contents of char_rom (hex, n*v repeats v):
  //   4f,0,77,1,6e,0,20,1,61,0,20,1,6d,0,75,1,73,0,6b,1,65,0,74,1,20
  //   ,0,66,1,6f,0,72,1,20,0,68,1,6f,0,6d,1,65,0,20,1,64,0,65,1,66,0
  //   ,65,1,6e,0,73,1,65,0,2c,1,20,0,73,1,69,0,6e,1,63,0,65,1,20,0,74
  //   ,1,68,0,61,1,74,0,27,1,73,0,20,1,77,0,68,1,61,0,74,1,20,0,74,1
  //   ,68,0,65,1,20,0,66,1,6f,0,75,1,6e,0,64,1,69,0,6e,1,67,0,20,1,66
  //   ,0,61,1,74,0,68,1,65,0,72,1,73,0,20,1,69,0,6e,1,74,0,65,1,6e,0
  //   ,64,1,65,0,64,1,2e,0,20,1,96*0,46,1,6f,0,75,1,72,0,20,1,72,0,75
  //   ,1,66,0,66,1,69,0,61,1,6e,0,73,1,20,0,62,1,72,0,65,1,61,0,6b,1
  //   ,20,0,69,1,6e,0,74,1,6f,0,20,1,6d,0,79,1,20,0,68,1,6f,0,75,1,73
  //   ,0,65,1,2e,0,20,1,22,0,57,1,68,0,61,1,74,0,20,1,74,0,68,1,65,0
  //   ,20,1,64,0,65,1,76,0,69,1,6c,0,3f,1,22,0,20,1,41,0,73,1,20,0,49
  //   ,1,20,0,67,1,72,0,61,1,62,0,20,1,6d,0,79,1,20,0,70,1,6f,0,77,1
  //   ,64,0,65,1,72,0,65,1,64,0,20,1,77,0,69,1,67,0,20,1,61,97*0,6e
  //   ,0,64,1,20,0,4b,1,65,0,6e,1,74,0,75,1,63,0,6b,1,79,0,20,1,72,0
  //   ,69,1,66,0,6c,1,65,0,2e,1,20,0,42,1,6c,0,6f,1,77,0,20,1,61,0,20
  //   ,1,67,0,6f,1,6c,0,66,1,20,0,62,1,61,0,6c,1,6c,0,20,1,73,0,69,1
  //   ,7a,0,65,1,64,0,20,1,68,0,6f,1,6c,0,65,1,20,0,74,1,68,0,72,1,6f
  //   ,0,75,1,67,0,68,1,20,0,74,1,68,0,65,1,20,0,66,1,69,0,72,1,73,0
  //   ,74,1,20,0,6d,1,61,0,6e,1,2c,0,20,1,68,0,65,1,27,0,73,1,20,0,64
  //   ,1,65,0,61,1,64,0,20,1,96*0,6f,1,6e,0,20,1,74,0,68,1,65,0,20,1
  //   ,73,0,70,1,6f,0,74,1,2e,0,20,1,44,0,72,1,61,0,77,1,20,0,6d,1,79
  //   ,0,20,1,70,0,69,1,73,0,74,1,6f,0,6c,1,20,0,6f,1,6e,0,20,1,74,0
  //   ,68,1,65,0,20,1,73,0,65,1,63,0,6f,1,6e,0,64,1,20,0,6d,1,61,0,6e
  //   ,1,2c,0,20,1,6d,0,69,1,73,0,73,1,20,0,68,1,69,0,6d,1,20,0,65,1
  //   ,6e,0,74,1,69,0,72,1,65,0,6c,1,79,0,20,1,62,0,65,1,63,0,61,1,75
  //   ,0,73,1,65,0,20,1,69,0,74,1,27,0,73,1,20,0,73,1,6d,97*0,6f,0,6f
  //   ,1,74,0,68,1,62,0,6f,1,72,0,65,1,20,0,61,1,6e,0,64,1,20,0,6e,1
  //   ,61,0,69,1,6c,0,73,1,20,0,74,1,68,0,65,1,20,0,6e,1,65,0,69,1,67
  //   ,0,68,1,62,0,6f,1,72,0,73,1,20,0,64,1,6f,0,67,1,2e,0,20,1,49,0
  //   ,20,1,68,0,61,1,76,0,65,1,20,0,74,1,6f,0,20,1,72,0,65,1,73,0,6f
  //   ,1,72,0,74,1,20,0,74,1,6f,0,20,1,74,0,68,1,65,0,20,1,63,0,61,1
  //   ,6e,0,6e,1,6f,0,6e,1,20,0,6d,1,6f,0,75,1,6e,0,74,1,65,0,64,1,20
  //   ,0,61,1,74,0,20,1,96*0,74,1,68,0,65,1,20,0,74,1,6f,0,70,1,20,0
  //   ,6f,1,66,0,20,1,74,0,68,1,65,0,20,1,73,0,74,1,61,0,69,1,72,0,73
  //   ,1,20,0,6c,1,6f,0,61,1,64,0,65,1,64,0,20,1,77,0,69,1,74,0,68,1
  //   ,20,0,67,1,72,0,61,1,70,0,65,1,20,0,73,1,68,0,6f,1,74,0,2c,1,20
  //   ,0,22,1,54,0,61,1,6c,0,6c,1,79,0,20,1,68,0,6f,1,20,0,6c,1,61,0
  //   ,64,1,73,0,22,1,20,0,74,1,68,0,65,1,20,0,67,1,72,0,61,1,70,0,65
  //   ,1,20,0,73,1,68,0,6f,1,74,0,20,1,73,0,68,1,72,97*0,65,0,64,1,73
  //   ,0,20,1,74,0,77,1,6f,0,20,1,6d,0,65,1,6e,0,20,1,69,0,6e,1,20,0
  //   ,74,1,68,0,65,1,20,0,62,1,6c,0,61,1,73,0,74,1,2c,0,20,1,74,0,68
  //   ,1,65,0,20,1,73,0,6f,1,75,0,6e,1,64,0,20,1,61,0,6e,1,64,0,20,1
  //   ,65,0,78,1,74,0,72,1,61,0,20,1,73,0,68,1,72,0,61,1,70,0,6e,1,65
  //   ,0,6c,1,20,0,73,1,65,0,74,1,20,0,6f,1,66,0,66,1,20,0,63,1,61,0
  //   ,72,1,20,0,61,1,6c,0,61,1,72,0,6d,1,73,0,2e,1,20,0,46,1,69,0,78
  //   ,1,20,0,62,1,96*0,61,1,79,0,6f,1,6e,0,65,1,74,0,20,1,61,0,6e,1
  //   ,64,0,20,1,63,0,68,1,61,0,72,1,67,0,65,1,20,0,74,1,68,0,65,1,20
  //   ,0,6c,1,61,0,73,1,74,0,20,1,74,0,65,1,72,0,72,1,69,0,66,1,69,0
  //   ,65,1,64,0,20,1,72,0,61,1,70,0,73,1,63,0,61,1,6c,0,6c,1,69,0,6f
  //   ,1,6e,0,2e,1,20,0,48,1,65,0,20,1,42,0,6c,1,65,0,65,1,64,0,73,1
  //   ,20,0,6f,1,75,0,74,1,20,0,77,1,61,0,69,1,74,0,69,1,6e,0,67,1,20
  //   ,0,6f,1,6e,0,20,1,74,0,68,1,65,0,20,1,70,97*0,6f,0,6c,1,69,0,63
  //   ,1,65,0,20,1,74,0,6f,1,20,0,61,1,72,0,72,1,69,0,76,1,65,0,20,1
  //   ,73,0,69,1,6e,0,63,1,65,0,20,1,74,0,72,1,69,0,61,1,6e,0,67,1,75
  //   ,0,6c,1,61,0,72,1,20,0,62,1,61,0,79,1,6f,0,6e,1,65,0,74,1,20,0
  //   ,77,1,6f,0,75,1,6e,0,64,1,73,0,20,1,61,0,72,1,65,0,20,1,69,0,6d
  //   ,1,70,0,6f,1,73,0,73,1,69,0,62,1,6c,0,65,1,20,0,74,1,6f,0,20,1
  //   ,73,0,74,1,69,0,74,1,63,0,68,1,20,0,75,1,70,0,2e,1,20,0,4a,1,75
  //   ,0,73,1,96*0,74,1,20,0,61,1,73,0,20,1,74,0,68,1,65,0,20,1,66,0
  //   ,6f,1,75,0,6e,1,64,0,69,1,6e,0,67,1,20,0,66,1,61,0,74,1,68,0,65
  //   ,1,72,0,73,1,20,0,69,1,6e,0,74,1,65,0,6e,1,64,0,65,1,64,0,2e,1
endmodule

/* Code of horizontal:
module horizontal(
	input [6:0] char,
	output sync,
	output clr
);
	assign clr = char == 8'd99;
	assign sync = !(char >= 8'd82 && char < 8'd94);
endmodule
*/

/* Code of vertical:
module vertical(
	input [11:0] line,
	output sync,
	output clr
);
	assign clr = line == 524;
	assign sync = !(line >= 490 && line < 492);
endmodule
*/
