// Digital circuit vga_real.dig as structural Verilog
module vga_real (
  input  clk,
  input  reset,
  output [11:0] line,
  output hsync,
  output vsync,
  output [7:0] video,
  output [7:0] pixel,
  output [7:0] data,
  output [11:0] pos
);

  wire _4bit_counter_2_ovf, _4bit_counter_3_ovf, _4bit_counter_sync_1_ovf, _4bit_counter_sync_2_ovf,
       and_1_out, and_3_out, nor_1_out, not_1_out, not_2_out, not_3_out, not_4_out, u_hsync_blank,
       u_hsync_pad, u_hsync_reset, u_vsync_blank, u_vsync_reset;
  wire [3:0] _4bit_counter_1_out;
  wire [7:0] d_ff_1_q;
  wire [7:7] and_2_out;

  _4bit_counter _4bit_counter_1 (
    .in(4'b0000), .clk(clk), .nclr(1'b1), .en(1'b1), .nld(1'b1), .cin(1'b1), .out(_4bit_counter_1_out));  // open: ovf
  _4bit_counter _4bit_counter_2 (
    .in(4'b0000), .clk(_4bit_counter_1_out[0]), .nclr(u_hsync_reset), .en(1'b1), .nld(1'b1), .cin(1'b1),
    .out(pixel[3:0]), .ovf(_4bit_counter_2_ovf));
  _4bit_counter _4bit_counter_3 (
    .in(4'b0000), .clk(_4bit_counter_1_out[0]), .nclr(u_hsync_reset), .en(1'b1), .nld(1'b1),
    .cin(_4bit_counter_2_ovf), .out(pixel[7:4]), .ovf(_4bit_counter_3_ovf));
  _4bit_counter _4bit_counter_4 (
    .in(4'b0000), .clk(_4bit_counter_1_out[0]), .nclr(u_hsync_reset), .en(1'b1), .nld(1'b1),
    .cin(_4bit_counter_3_ovf), .out(pos[11:8]));  // open: ovf
  _4bit_counter_sync _4bit_counter_sync_1 (
    .in(4'b0000), .clk(u_hsync_reset), .nclr(and_1_out), .en(1'b1), .nld(1'b1), .cin(1'b1), .out(line[3:0]),
    .ovf(_4bit_counter_sync_1_ovf));
  _4bit_counter_sync _4bit_counter_sync_2 (
    .in(4'b0000), .clk(u_hsync_reset), .nclr(and_1_out), .en(1'b1), .nld(1'b1),
    .cin(_4bit_counter_sync_1_ovf), .out(line[7:4]), .ovf(_4bit_counter_sync_2_ovf));
  _4bit_counter_sync _4bit_counter_sync_3 (
    .in(4'b0000), .clk(u_hsync_reset), .nclr(and_1_out), .en(1'b1), .nld(1'b1),
    .cin(_4bit_counter_sync_2_ovf), .out(line[11:8]));  // open: ovf
  hsync #(.applicationType("IVERILOG")) u_hsync (
    .pos({pos[11:8], pixel}), .sync(hsync), .blank(u_hsync_blank), .pad(u_hsync_pad), .reset(u_hsync_reset));
  vsync #(.applicationType("IVERILOG")) u_vsync (
    .pos(line), .sync(vsync), .blank(u_vsync_blank), .reset(u_vsync_reset));
  and and_1 (and_1_out, u_vsync_reset, not_1_out);
  not not_1 (not_1_out, reset);
  nor nor_1 (nor_1_out, u_hsync_blank, u_vsync_blank);
  and and_2 (and_2_out[7], u_hsync_pad, ~u_vsync_blank);  // And
  not not_2 (not_2_out, clk);
  ROM #(.AddrBits(16), .Bits(8)) buffer (.A({line[8:1], pixel}), .sel(_4bit_counter_1_out[0]), .D(data));
  not not_3 (not_3_out, _4bit_counter_1_out[0]);
  RAMSinglePort #(.AddrBits(16), .Bits(8)) ramsingleport_1 (
    .A({line[8:1], pixel}), .str(_4bit_counter_1_out[0]), .C(not_2_out), .ld(not_3_out), .D(data));
  and and_3 (and_3_out, not_2_out, not_3_out);
  D_FF #(.Bits(8)) d_ff_1 (.D(data), .C(and_3_out), .Q(d_ff_1_q));  // open: nQ
  Multiplexer #(.Bits(8)) multiplexer_1 (.sel(not_4_out), .in_0(d_ff_1_q), .in_1({8{and_2_out[7]}}), .out(video));
  not not_4 (not_4_out, nor_1_out);

  assign pos[7:0] = pixel;

  // Notes on the sheet:
  //   clk: Hz: 100
  //   contents of buffer (hex, n*v repeats v):
  //   28*97,9b,9b,97,9b,9b,9b,bb,4*9b,bb,bb,9b,9b,bb,9b,9b,30*bb,b7
  //   ,10*bb,97,4*bb,b7,b7,67*bb,db,bb,bb,13*db,bb,bb,77*db,27*97,9b,9b
  //   ,97,9b,9b,9b,97,9b,9b,bb,9b,9b,97,bb,5*9b,28*bb,b7,9*bb,b7,5*bb
  //   ,b7,70*bb,db,bb,db,db,db,bb,9*db,bb,79*db,26*97,9b,97,9b,9b,9b
  //   ,bb,9b,9b,9b,bb,bb,9b,bb,bb,bb,9b,9b,bb,bb,bb,9b,bb,bb,9b,6*bb
  //   ,9b,14*bb,9b,bb,97,bb,b7,5*bb,97,8*bb,97,65*bb,db,bb,bb,db,db
  //   ,bb,db,db,db,bb,4*db,bb,85*db,27*97,9b,97,97,4*9b,bb,9b,97,7*9b
  //   ,bb,bb,9b,9b,97,16*bb,97,8*bb,b7,82*bb,16*db,bb,71*db,df,10*db
  //   ,27*97,9b,9b,97,97,10*9b,4*bb,9b,bb,9b,bb,9b,9*bb,9b,bb,9b,99*bb
  //   ,db,db,db,bb,7*db,bb,83*db,28*97,4*9b,97,9b,9b,97,9b,bb,9b,9b,9b
  //   ,bb,9b,bb,9b,9b,9b,97,97,4*bb,9b,4*bb,9b,5*bb,97,bb,bb,9b,88*bb
  //   ,db,bb,bb,14*db,bb,bb,81*db,26*97,9b,97,12*9b,97,4*9b,97,9b,9b
  //   ,5*bb,b7,bb,b7,bb,b7,4*bb,9b,4*bb,9b,97,b7,bb,97,bb,bb,bb,97,80*bb
  //   ,db,bb,db,db,bb,83*db,df,db,db,df,6*db,df,db,26*97,9b,9b,9b,97
  //   ,11*9b,bb,9b,9b,97,97,97,bb,97,bb,97,4*bb,9b,bb,9b,97,9b,5*bb
  //   ,9b,91*bb,db,bb,bb,bb,db,db,db,bb,70*db,df,7*db,df,df,db,db,db
  //   ,df,db,df,db,db,df,df,db,26*97,4*9b,97,11*9b,bb,4*9b,97,9b,bb
  //   ,97,6*bb,97,bb,bb,bb,9b,9b,bb,bb,9b,9b,bb,9b,9b,85*bb,4*db,bb
  //   ,db,bb,77*db,df,8*db,df,db,db,5*df,25*97,9b,9b,97,9b,97,16*9b
  //   ,6*bb,9b,bb,97,bb,bb,97,bb,bb,bb,9b,97,4*bb,9b,85*bb,db,bb,db
  //   ,bb,db,bb,db,bb,6*db,bb,69*db,df,db,db,df,5*db,df,db,4*df,db,df,df,df
  //   ,27*97,9b,97,97,97,bb,9b,9b,97,97,9b,9b,9b,97,bb,97,9b,bb,9b,9b
  //   ,bb,9b,bb,bb,bb,9b,bb,9b,bb,bb,bb,97,97,4*bb,9b,9b,4*bb,97,86*bb
  //   ,db,bb,db,db,bb,72*db,df,6*db,df,db,df,df,db,11*df,17*97,9b,6*97
  //   ,4*9b,97,97,97,10*9b,97,7*9b,bb,97,8*bb,97,bb,bb,9b,bb,bb,bb,9b
  //   ,85*bb,db,bb,bb,76*db,df,db,df,db,df,df,df,db,db,16*df,19*97,9b
  //   ,6*97,9b,97,9b,9b,97,9b,97,9b,9b,97,5*9b,97,9b,9b,9b,bb,9b,9b
  //   ,4*bb,97,9b,bb,bb,bb,9b,bb,9b,bb,bb,bb,9b,97,9b,bb,9b,84*bb,db
  //   ,bb,9*db,bb,66*db,df,df,db,df,df,df,db,19*df,11*97,9b,97,97,9b
  //   ,10*97,9b,97,5*9b,97,5*9b,bb,7*9b,bb,9b,4*bb,6*9b,97,4*bb,9b,87*bb
  //   ,78*db,df,db,df,df,db,db,df,df,df,db,db,14*df,ff,df,9*97,9b,5*97
  //   ,9b,9b,97,97,9b,9b,4*97,11*9b,bb,4*9b,bb,6*9b,4*bb,9b,bb,bb,9b
  //   ,bb,9b,9b,9b,97,91*bb,db,bb,db,db,db,bb,67*db,df,db,db,df,df,db
  //   ,df,df,db,df,db,18*df,ff,ff,9b,9b,97,97,9b,97,97,97,9b,97,97,97
  //   ,9b,97,4*9b,97,12*9b,97,9b,9b,9b,bb,9b,9b,9b,bb,9b,9b,9b,bb,9b
  //   ,bb,9b,9b,7*bb,9b,9b,bb,9b,bb,bb,9b,4*bb,9b,bb,bb,97,79*bb,db
  //   ,bb,bb,72*db,df,db,df,df,df,db,df,df,db,df,df,db,20*df,97,97,9b
  //   ,5*97,9b,9b,97,9b,9b,9b,97,9b,9b,97,17*9b,bb,9b,17*bb,9b,bb,bb,bb
  //   ,9b,4*bb,9b,bb,9b,9b,81*bb,db,bb,bb,bb,69*db,df,db,df,df,db,db,db
  //   ,df,db,df,df,db,df,db,18*df,ff,ff,ff,9b,97,97,9b,9b,97,32*9b,bb,bb,bb
  //   ,9b,bb,9b,11*bb,9b,9b,4*bb,9b,9b,bb,9b,83*bb,db,bb,bb,72*db,df
  //   ,db,db,6*df,db,17*df,ff,df,ff,ff,df,ff,5*9b,97,18*9b,bb,7*9b,5*bb
  //   ,9b,bb,bb,bb,9b,104*bb,db,bb,bb,bb,70*db,5*df,db,df,db,df,df,db
  //   ,16*df,ff,df,7*ff,21*9b,bb,9b,bb,9b,9b,bb,9b,bb,bb,9b,117*bb,71*db
  //   ,df,db,db,db,df,df,df,db,db,df,df,db,15*df,ff,df,df,ff,ff,df,4*ff
  //   ,9b,9b,9b,97,9b,9b,9b,bb,12*9b,5*bb,9b,4*bb,9b,bb,bb,9b,30*bb
  //   ,9b,77*bb,db,4*bb,72*db,df,df,db,db,df,db,db,db,df,db,18*df,ff,ff
  //   ,df,4*ff,df,ff,bb,6*9b,bb,8*9b,bb,9b,bb,bb,9b,bb,bb,bb,9b,117*bb
  //   ,db,bb,bb,db,bb,73*db,df,db,df,df,db,df,db,db,df,db,db,15*df,ff
  //   ,4*df,5*ff,5*9b,bb,bb,9b,bb,9b,bb,bb,9b,bb,9b,9b,9b,bb,9b,9b,9b
  //   ,121*bb,db,bb,75*db,df,df,10*db,18*df,ff,ff,df,4*ff,9b,9b,4*bb
  //   ,9b,bb,4*9b,7*bb,9b,121*bb,db,bb,bb,db,db,bb,bb,73*db,df,db,db
  //   ,df,6*db,6*df,db,14*df,4*ff,9b,9b,9b,bb,bb,9b,9b,8*bb,9b,9b,bb,bb
  //   ,9b,122*bb,db,bb,89*db,df,df,4*db,11*df,ff,df,df,ff,ff,ff,5*bb
  //   ,9b,4*bb,9b,129*bb,4*db,bb,77*db,df,16*db,13*df,ff,ff,ff,df,bb
  //   ,9b,9b,5*bb,9b,9b,131*bb,80*db,df,db,db,df,13*db,df,db,12*df,4*ff
  //   ,142*bb,97*db,df,db,10*df,5*ff,10*bb,9b,130*bb,96*db,15*df,4*ff
  //   ,141*bb,91*db,df,db,db,db,12*df,ff,df,6*ff,9b,140*bb,96*db,df
  //   ,db,12*df,5*ff,139*bb,48*db,b7,bb,db,bb,bb,45*db,df,db,12*df,ff
  //   ,df,ff,ff,ff,137*bb,db,bb,bb,46*db,b7,96,96,bb,4*b7,b6,44*db,10*df
  //   ,ff,df,5*ff,135*bb,db,bb,db,bb,47*db,92,92,b6,b7,96,96,db,b7,bb
  //   ,b7,bb,40*db,13*df,6*ff,132*bb,db,db,bb,bb,db,db,bb,bb,45*db,b7
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endmodule

/* Code of hsync:
module hsync(
	input [11:0] pos,
	output sync,
	output blank,
	output pad,
	output reset
);

/*assign blank = pos >= 64;
assign pad = blank && (pos < 72 || pos > 92);
assign reset = !(pos == 100);
assign sync = !(pos >= 74 && pos < 86);
endmodule* /

/*assign blank = pos >= 512;
assign pad = blank && (pos < 576 || pos > 736);
assign reset = !(pos == 800);
assign sync = !(pos >= 592 && pos < 688);
endmodule* /

assign blank = pos >= 256;
assign pad = blank && (pos < 288 || pos > 368);
assign reset = !(pos == 400);
assign sync = !(pos >= 296 && pos < 344);
endmodule
*/

/* Code of vsync:
module vsync(
	input [11:0] pos,
	output sync,
	output blank,
	output reset
);

assign blank = pos >= 480;
assign reset = !(pos == 524);
assign sync = !(pos >= 490 && pos < 492);
endmodule
*/
