// Digital circuit whole_gpu.dig as structural Verilog
module whole_gpu (
  input  _2clk,
  input  reset,
  input  in_13,
  output [11:0] line,
  output hsync,
  output vsync,
  output [7:0] video,
  output [7:0] pixel,
  output [7:0] data,
  output [15:0] sprite_addr,
  output [15:0] addr_out,
  output [7:0] data_out,
  output [11:0] POS,
  output [15:0] addr_out_2
);

  wire _4bit_counter_sync_1_ovf, _4bit_counter_sync_2_ovf, _4bit_counter_sync_3_ovf,
       _4bit_counter_sync_5_ovf, _4bit_counter_sync_7_ovf, _4bit_counter_sync_10_ovf,
       _4bit_counter_sync_11_ovf, _4bit_counter_sync_13_ovf, _4bit_counter_sync_14_ovf, and_2_out, and_3_out,
       and_4_out, and_6_out, and_9_out, and_11_out, and_12_out, and_14_out, and_15_out, and_16_out, clk,
       comparator_1_eq, demultiplexer_1_out_0, demultiplexer_1_out_1, demultiplexer_1_out_2,
       demultiplexer_1_out_3, demultiplexer_1_out_4, demultiplexer_1_out_6, done, drawing, idle, ld, ld_h,
       multiplexer_1_out, next, nidle, nor_1_out, not_1_out, not_2_out, not_3_out, not_4_out, not_5_out,
       not_6_out, not_7_out, or_1_out, or_2_out, or_3_out, or_4_out, or_5_out, or_6_out, reload_nq, reload_q,
       store, transfer, u_hsync_blank, u_hsync_pad, u_hsync_reset, u_vsync_blank, u_vsync_reset;
  wire [3:0] _4bit_counter_sync_4_out, d_ff_2_q;
  wire [3:1] _4bit_counter_sync_9_out;
  wire [7:0] d_ff_1_q, d_ff_3_q, data_t;
  wire [7:4] d_ff_2_q_2;
  wire [7:7] and_13_out;

  D_FF #(.Bits(8)) d_ff_1 (.D(sprite_addr[11:4]), .C(demultiplexer_1_out_4), .Q(d_ff_1_q));  // open: nQ
  assign data_t = not_1_out ? d_ff_1_q : 8'bz;  // Driver driver_1
  or or_1 (or_1_out, _4bit_counter_sync_1_ovf, ~demultiplexer_1_out_3);  // Or
  _4bit_counter_sync _4bit_counter_sync_1 (
    .in(4'b0000), .clk(clk), .nclr(1'b1), .en(1'b1), .nld(ld), .cin(1'b1), .out(sprite_addr[3:0]),
    .ovf(_4bit_counter_sync_1_ovf));
  _4bit_counter_sync _4bit_counter_sync_2 (
    .in(data_t[3:0]), .clk(clk), .nclr(1'b1), .en(1'b1), .nld(ld), .cin(or_1_out), .out(sprite_addr[7:4]),
    .ovf(_4bit_counter_sync_2_ovf));
  _4bit_counter_sync _4bit_counter_sync_3 (
    .in(data_t[7:4]), .clk(clk), .nclr(1'b1), .en(1'b1), .nld(ld), .cin(_4bit_counter_sync_2_ovf),
    .out(sprite_addr[11:8]), .ovf(_4bit_counter_sync_3_ovf));
  _4bit_counter_sync _4bit_counter_sync_4 (
    .in(data_t[3:0]), .clk(clk), .nclr(1'b1), .en(1'b1), .nld(ld_h), .cin(_4bit_counter_sync_3_ovf),
    .out(_4bit_counter_sync_4_out));  // open: ovf
  assign sprite_addr[15:12] = _4bit_counter_sync_4_out & {4{drawing}};  // And and_1, 4 bits wide
  and and_2 (and_2_out, nidle, reload_nq);
  EEPROMDualPort #(.AddrBits(16), .Bits(8)) eepromdualport_1 (
    .A(sprite_addr), .Din({8{1'b0}}), .str(1'b0), .C(1'b0), .ld(and_2_out), .D(data_t));
  Demultiplexer #(.Selector_Bits(3), .Default(1)) demultiplexer_1 (
    .sel(sprite_addr[2:0]), .in(drawing), .out_0(demultiplexer_1_out_0), .out_1(demultiplexer_1_out_1),
    .out_2(demultiplexer_1_out_2), .out_3(demultiplexer_1_out_3), .out_4(demultiplexer_1_out_4),
    .out_5(ld_h), .out_6(demultiplexer_1_out_6));  // open: out_7
  not not_1 (not_1_out, reload_nq);
  JK_FF u_drawing (.J(~demultiplexer_1_out_6), .C(clk), .K(reload_q), .Q(drawing));  // open: nQ
  JK_FF reload (.J(done), .C(clk), .K(reload_q), .Q(reload_q), .nQ(reload_nq));
  not not_2 (not_2_out, demultiplexer_1_out_2);
  Comparator #(.Bits(6)) comparator_1 (.a(data_t[5:0]), .b({6{1'b1}}), .eq(comparator_1_eq));  // open: gt, lt
  and and_3 (and_3_out, data_t[0], not_2_out);
  and and_4 (and_4_out, ~demultiplexer_1_out_0, ~clk);  // And
  and and_5 (ld, demultiplexer_1_out_6, reload_nq);
  JK_FF idling (.J(and_3_out), .C(clk), .K(in_13), .Q(idle), .nQ(nidle));
  D_FF #(.Bits(8)) d_ff_2 (.D(data_t), .C(and_4_out), .Q({d_ff_2_q_2, d_ff_2_q}));  // open: nQ
  Multiplexer multiplexer_1 (.sel(idle), .in_0(clk), .in_1(u_hsync_reset), .out(multiplexer_1_out));
  or or_2 (or_2_out, drawing, idle);
  and and_6 (and_6_out, demultiplexer_1_out_1, ~next);  // And
  or or_3 (or_3_out, next, line[0]);
  and and_7 (done, comparator_1_eq, ~data_t[6], data_t[7]);  // And
  and and_8 (next, comparator_1_eq, ~data_t[7], data_t[6]);  // And
  and and_9 (and_9_out, data_t[7], data_t[6]);
  or or_4 (or_4_out, and_9_out, ~comparator_1_eq);  // Or
  _4bit_counter_sync _4bit_counter_sync_5 (
    .in(d_ff_2_q), .clk(clk), .nclr(or_5_out), .en(or_2_out), .nld(and_6_out), .cin(1'b1),
    .out(addr_out[3:0]), .ovf(_4bit_counter_sync_5_ovf));
  _4bit_counter_sync _4bit_counter_sync_6 (
    .in(d_ff_2_q_2), .clk(clk), .nclr(or_5_out), .en(or_2_out), .nld(and_6_out),
    .cin(_4bit_counter_sync_5_ovf), .out(addr_out[7:4]));  // open: ovf
  _4bit_counter_sync _4bit_counter_sync_7 (
    .in(data_t[3:0]), .clk(multiplexer_1_out), .nclr(or_6_out), .en(or_3_out), .nld(demultiplexer_1_out_1),
    .cin(1'b1), .out(addr_out[11:8]), .ovf(_4bit_counter_sync_7_ovf));
  _4bit_counter_sync _4bit_counter_sync_8 (
    .in(data_t[7:4]), .clk(multiplexer_1_out), .nclr(or_6_out), .en(or_3_out), .nld(demultiplexer_1_out_1),
    .cin(_4bit_counter_sync_7_ovf), .out(addr_out[15:12]));  // open: ovf
  and and_10 (store, or_4_out, reload_nq, drawing, nidle);
  assign data_out = nidle ? data_t : 8'bz;  // Driver driver_2
  and and_11 (and_11_out, not_3_out, idle);
  not not_3 (not_3_out, and_12_out);
  RAMSinglePort #(.AddrBits(16), .Bits(8)) ramsingleport_1 (
    .A(addr_out), .str(store), .C(clk), .ld(idle), .D(data_out));
  JK_FF reload_2 (.J(and_11_out), .C(clk), .K(nidle), .Q(transfer));  // open: nQ
  or or_5 (or_5_out, nidle, u_hsync_reset);
  or or_6 (or_6_out, nidle, and_12_out);
  _4bit_counter_sync _4bit_counter_sync_9 (
    .in(4'b0000), .clk(_2clk), .nclr(1'b1), .en(1'b1), .nld(1'b1), .cin(1'b1),
    .out({_4bit_counter_sync_9_out, clk}));  // open: ovf
  _4bit_counter_sync _4bit_counter_sync_10 (
    .in(4'b0000), .clk(clk), .nclr(u_hsync_reset), .en(1'b1), .nld(1'b1), .cin(1'b1), .out(addr_out_2[3:0]),
    .ovf(_4bit_counter_sync_10_ovf));
  _4bit_counter_sync _4bit_counter_sync_11 (
    .in(4'b0000), .clk(clk), .nclr(u_hsync_reset), .en(1'b1), .nld(1'b1), .cin(_4bit_counter_sync_10_ovf),
    .out(addr_out_2[7:4]), .ovf(_4bit_counter_sync_11_ovf));
  _4bit_counter_sync _4bit_counter_sync_12 (
    .in(4'b0000), .clk(clk), .nclr(u_hsync_reset), .en(1'b1), .nld(1'b1), .cin(_4bit_counter_sync_11_ovf),
    .out(POS[11:8]));  // open: ovf
  _4bit_counter_sync _4bit_counter_sync_13 (
    .in(4'b0000), .clk(u_hsync_reset), .nclr(and_12_out), .en(1'b1), .nld(1'b1), .cin(1'b1),
    .out({addr_out_2[10:8], line[0]}), .ovf(_4bit_counter_sync_13_ovf));
  _4bit_counter_sync _4bit_counter_sync_14 (
    .in(4'b0000), .clk(u_hsync_reset), .nclr(and_12_out), .en(1'b1), .nld(1'b1),
    .cin(_4bit_counter_sync_13_ovf), .out(addr_out_2[14:11]), .ovf(_4bit_counter_sync_14_ovf));
  _4bit_counter_sync _4bit_counter_sync_15 (
    .in(4'b0000), .clk(u_hsync_reset), .nclr(and_12_out), .en(1'b1), .nld(1'b1),
    .cin(_4bit_counter_sync_14_ovf), .out({line[11:9], addr_out_2[15]}));  // open: ovf
  hsync #(.applicationType("IVERILOG")) u_hsync (
    .pos({POS[11:8], addr_out_2[7:0]}), .sync(hsync), .blank(u_hsync_blank), .pad(u_hsync_pad),
    .reset(u_hsync_reset));
  vsync #(.applicationType("IVERILOG")) u_vsync (
    .pos({line[11:9], addr_out_2[15:8], line[0]}), .sync(vsync), .blank(u_vsync_blank), .reset(u_vsync_reset));
  and and_12 (and_12_out, u_vsync_reset, not_4_out);
  not not_4 (not_4_out, reset);
  nor nor_1 (nor_1_out, u_hsync_blank, u_vsync_blank);
  and and_13 (and_13_out[7], u_hsync_pad, ~u_vsync_blank);  // And
  and and_14 (and_14_out, transfer, clk);
  not not_5 (not_5_out, _2clk);
  not not_6 (not_6_out, clk);
  assign data = and_15_out ? data_out : 8'bz;  // Driver driver_3
  and and_15 (and_15_out, idle, clk);
  RAMSinglePort #(.AddrBits(16), .Bits(8)) ramsingleport_2 (
    .A(addr_out_2), .str(and_14_out), .C(not_5_out), .ld(not_6_out), .D(data));
  and and_16 (and_16_out, not_5_out, not_6_out);
  D_FF #(.Bits(8)) d_ff_3 (.D(data), .C(and_16_out), .Q(d_ff_3_q));  // open: nQ
  Multiplexer #(.Bits(8)) multiplexer_2 (.sel(not_7_out), .in_0(d_ff_3_q), .in_1({8{and_13_out[7]}}), .out(video));
  not not_7 (not_7_out, nor_1_out);

  assign line[8:1] = addr_out_2[15:8];
  assign pixel = addr_out_2[7:0];
  assign POS[7:0] = addr_out_2[7:0];

  // Other names for the same wires on the sheet: line_t = line[0]

  // Notes on the sheet:
  //   _2clk: Hz: 50000
  //   contents of eepromdualport_1 (hex, n*v repeats v):
  //   1,2,14*0,3,4,1,0,0,1,23,14*0,1,23,4619*0,7f,0,3f,0,ff,0,bf
endmodule

/* Code of hsync:
module hsync(
	input [11:0] pos,
	output sync,
	output blank,
	output pad,
	output reset
);

assign blank = pos >= 512/2;
assign pad = blank && (pos < 576/2 || pos > 736/2);
assign reset = !(pos == 800/2);
assign sync = !(pos >= 592/2 && pos < 688/2);
endmodule
*/

/* Code of vsync:
module vsync(
	input [11:0] pos,
	output sync,
	output blank,
	output reset
);

assign blank = pos >= 480;
assign reset = !(pos == 524);
assign sync = !(pos >= 490 && pos < 492);
endmodule
*/
